// Logisim project MIPS.circ as structural Verilog
// D Latch
module Gated_D_Latch (
  input  D,
  input  E,
  output Q,
  output nQ
);

  wire nand_1_out, nand_2_out;

  nand nand_1 (nand_1_out, D, E);
  nand nand_2 (nand_2_out, nand_1_out, E);
  nand nand_3 (Q, nand_1_out, nQ);
  nand nand_4 (nQ, Q, nand_2_out);
endmodule

module _32_Bit_General_Register (
  input  E,
  input  D0,
  input  D1,
  input  D2,
  input  D3,
  input  D4,
  input  D5,
  input  D6,
  input  D7,
  input  D8,
  input  D9,
  input  D10,
  input  D11,
  input  D12,
  input  D13,
  input  D14,
  input  D15,
  input  D16,
  input  D17,
  input  D18,
  input  D19,
  input  D20,
  input  D21,
  input  D22,
  input  D23,
  input  D24,
  input  D25,
  input  D26,
  input  D27,
  input  D28,
  input  D29,
  input  D30,
  input  D31,
  output Q0,
  output Q1,
  output Q2,
  output Q3,
  output Q4,
  output Q5,
  output Q6,
  output Q7,
  output Q8,
  output Q9,
  output Q10,
  output Q11,
  output Q12,
  output Q13,
  output Q14,
  output Q15,
  output Q16,
  output Q17,
  output Q18,
  output D19_2,
  output D20_2,
  output D21_2,
  output D22_2,
  output D23_2,
  output D24_2,
  output D25_2,
  output D26_2,
  output D27_2,
  output D28_2,
  output D29_2,
  output D30_2,
  output D31_2
);

  Gated_D_Latch gated_d_latch_1 (.E(E), .D(D0), .Q(Q0));  // open: nQ
  Gated_D_Latch gated_d_latch_2 (.E(E), .D(D1), .Q(Q1));  // open: nQ
  Gated_D_Latch gated_d_latch_3 (.E(E), .D(D2), .Q(Q2));  // open: nQ
  Gated_D_Latch gated_d_latch_4 (.E(E), .D(D3), .Q(Q3));  // open: nQ
  Gated_D_Latch gated_d_latch_5 (.E(E), .D(D4), .Q(Q4));  // open: nQ
  Gated_D_Latch gated_d_latch_6 (.E(E), .D(D5), .Q(Q5));  // open: nQ
  Gated_D_Latch gated_d_latch_7 (.E(E), .D(D6), .Q(Q6));  // open: nQ
  Gated_D_Latch gated_d_latch_8 (.E(E), .D(D7), .Q(Q7));  // open: nQ
  Gated_D_Latch gated_d_latch_9 (.E(E), .D(D8), .Q(Q8));  // open: nQ
  Gated_D_Latch gated_d_latch_10 (.E(E), .D(D9), .Q(Q9));  // open: nQ
  Gated_D_Latch gated_d_latch_11 (.E(E), .D(D10), .Q(Q10));  // open: nQ
  Gated_D_Latch gated_d_latch_12 (.E(E), .D(D11), .Q(Q11));  // open: nQ
  Gated_D_Latch gated_d_latch_13 (.E(E), .D(D12), .Q(Q12));  // open: nQ
  Gated_D_Latch gated_d_latch_14 (.E(E), .D(D13), .Q(Q13));  // open: nQ
  Gated_D_Latch gated_d_latch_15 (.E(E), .D(D14), .Q(Q14));  // open: nQ
  Gated_D_Latch gated_d_latch_16 (.E(E), .D(D15), .Q(Q15));  // open: nQ
  Gated_D_Latch gated_d_latch_17 (.E(E), .D(D16), .Q(Q16));  // open: nQ
  Gated_D_Latch gated_d_latch_18 (.E(E), .D(D17), .Q(Q17));  // open: nQ
  Gated_D_Latch gated_d_latch_19 (.E(E), .D(D18), .Q(Q18));  // open: nQ
  Gated_D_Latch gated_d_latch_20 (.E(E), .D(D19), .Q(D19_2));  // open: nQ
  Gated_D_Latch gated_d_latch_21 (.E(E), .D(D20), .Q(D20_2));  // open: nQ
  Gated_D_Latch gated_d_latch_22 (.E(E), .D(D21), .Q(D21_2));  // open: nQ
  Gated_D_Latch gated_d_latch_23 (.E(E), .D(D22), .Q(D22_2));  // open: nQ
  Gated_D_Latch gated_d_latch_24 (.E(E), .D(D23), .Q(D23_2));  // open: nQ
  Gated_D_Latch gated_d_latch_25 (.E(E), .D(D24), .Q(D24_2));  // open: nQ
  Gated_D_Latch gated_d_latch_26 (.E(E), .D(D25), .Q(D25_2));  // open: nQ
  Gated_D_Latch gated_d_latch_27 (.E(E), .D(D26), .Q(D26_2));  // open: nQ
  Gated_D_Latch gated_d_latch_28 (.E(E), .D(D27), .Q(D27_2));  // open: nQ
  Gated_D_Latch gated_d_latch_29 (.E(E), .D(D28), .Q(D28_2));  // open: nQ
  Gated_D_Latch gated_d_latch_30 (.E(E), .D(D29), .Q(D29_2));  // open: nQ
  Gated_D_Latch gated_d_latch_31 (.E(E), .D(D30), .Q(D30_2));  // open: nQ
  Gated_D_Latch gated_d_latch_32 (.E(E), .D(D31), .Q(D31_2));  // open: nQ
endmodule

module _16_Bit_General_Register (
  input  E,
  input  D0,
  input  D1,
  input  D2,
  input  D3,
  input  D4,
  input  D5,
  input  D6,
  input  D7,
  input  D8,
  input  D9,
  input  D10,
  input  D11,
  input  D12,
  input  D13,
  input  D14,
  input  D15,
  output Q0,
  output Q1,
  output Q2,
  output Q3,
  output Q4,
  output Q5,
  output Q6,
  output Q7,
  output Q8,
  output Q9,
  output Q10,
  output Q11,
  output Q12,
  output Q13,
  output Q14,
  output Q15
);

  Gated_D_Latch gated_d_latch_1 (.E(E), .D(D0), .Q(Q0));  // open: nQ
  Gated_D_Latch gated_d_latch_2 (.E(E), .D(D1), .Q(Q1));  // open: nQ
  Gated_D_Latch gated_d_latch_3 (.E(E), .D(D2), .Q(Q2));  // open: nQ
  Gated_D_Latch gated_d_latch_4 (.E(E), .D(D3), .Q(Q3));  // open: nQ
  Gated_D_Latch gated_d_latch_5 (.E(E), .D(D4), .Q(Q4));  // open: nQ
  Gated_D_Latch gated_d_latch_6 (.E(E), .D(D5), .Q(Q5));  // open: nQ
  Gated_D_Latch gated_d_latch_7 (.E(E), .D(D6), .Q(Q6));  // open: nQ
  Gated_D_Latch gated_d_latch_8 (.E(E), .D(D7), .Q(Q7));  // open: nQ
  Gated_D_Latch gated_d_latch_9 (.E(E), .D(D8), .Q(Q8));  // open: nQ
  Gated_D_Latch gated_d_latch_10 (.E(E), .D(D9), .Q(Q9));  // open: nQ
  Gated_D_Latch gated_d_latch_11 (.E(E), .D(D10), .Q(Q10));  // open: nQ
  Gated_D_Latch gated_d_latch_12 (.E(E), .D(D11), .Q(Q11));  // open: nQ
  Gated_D_Latch gated_d_latch_13 (.E(E), .D(D12), .Q(Q12));  // open: nQ
  Gated_D_Latch gated_d_latch_14 (.E(E), .D(D13), .Q(Q13));  // open: nQ
  Gated_D_Latch gated_d_latch_15 (.E(E), .D(D14), .Q(Q14));  // open: nQ
  Gated_D_Latch gated_d_latch_16 (.E(E), .D(D15), .Q(Q15));  // open: nQ
endmodule

module Operations_Conditional_8_Bit_Register (
  input  E,
  input  _2_0,
  input  _2_1,
  input  _2_2,
  input  _2_3,
  input  _2_4,
  input  _2_5,
  input  _2_6,
  input  _2_7,
  output out_10,
  output out_11,
  output out_12,
  output out_13,
  output out_14,
  output out_15,
  output out_16,
  output out_17,
  output out_18,
  output out_19,
  output out_20,
  output out_21,
  output out_22,
  output out_23,
  output out_24,
  output out_25,
  output out_26,
  output out_27,
  output out_28,
  output out_29,
  output out_30,
  output out_31,
  output out_32,
  output out_33,
  output out_34,
  output out_35,
  output out_36,
  output out_37,
  output out_38,
  output out_39,
  output out_40,
  output out_41,
  output out_42,
  output out_43,
  output out_44,
  output out_45,
  output out_46,
  output out_47,
  output out_48,
  output out_49,
  output out_50,
  output out_51,
  output out_52,
  output out_53,
  output out_54,
  output out_55,
  output out_56,
  output out_57,
  output out_58,
  output out_59,
  output out_60,
  output out_61,
  output out_62
);

  wire and_1_out, and_2_out, and_3_out, and_4_out, and_5_out, and_6_out, and_7_out, and_8_out, and_9_out,
       and_10_out, and_11_out, and_12_out, and_13_out, and_14_out, and_21_out, and_22_out, and_28_out,
       and_29_out, and_35_out, and_36_out, and_42_out, and_43_out, and_44_out, and_49_out, and_50_out,
       and_51_out, and_56_out, and_57_out, and_58_out, and_63_out, and_64_out, and_69_out, and_70_out,
       and_71_out, and_76_out, and_77_out, and_78_out, and_83_out, and_84_out, and_85_out, and_89_out,
       and_90_out, and_94_out, and_95_out, and_96_out, and_98_out, and_99_out, and_100_out,
       gated_d_latch_1_q, gated_d_latch_2_q, gated_d_latch_3_q, gated_d_latch_4_q, gated_d_latch_5_q,
       gated_d_latch_6_q, gated_d_latch_7_q, gated_d_latch_8_q, nand_1_out, nand_2_out, nand_3_out,
       nand_4_out, nand_5_out, nand_6_out, nand_7_out, nand_8_out, nand_9_out, nand_10_out, nand_11_out,
       nand_12_out, not_1_out, not_2_out, not_3_out, not_4_out, not_5_out, not_6_out, not_7_out, not_8_out,
       not_9_out, not_10_out, not_11_out, not_12_out, not_13_out, not_14_out, not_15_out, not_16_out,
       not_17_out, not_18_out, not_19_out, not_20_out, not_21_out;

  Gated_D_Latch gated_d_latch_1 (.E(E), .D(_2_0), .Q(gated_d_latch_1_q));  // open: nQ
  Gated_D_Latch gated_d_latch_2 (.E(E), .D(_2_1), .Q(gated_d_latch_2_q));  // open: nQ
  Gated_D_Latch gated_d_latch_3 (.E(E), .D(_2_2), .Q(gated_d_latch_3_q));  // open: nQ
  Gated_D_Latch gated_d_latch_4 (.E(E), .D(_2_3), .Q(gated_d_latch_4_q));  // open: nQ
  Gated_D_Latch gated_d_latch_5 (.E(E), .D(_2_4), .Q(gated_d_latch_5_q));  // open: nQ
  Gated_D_Latch gated_d_latch_6 (.E(E), .D(_2_5), .Q(gated_d_latch_6_q));  // open: nQ
  Gated_D_Latch gated_d_latch_7 (.E(E), .D(_2_6), .Q(gated_d_latch_7_q));  // open: nQ
  Gated_D_Latch gated_d_latch_8 (.E(E), .D(_2_7), .Q(gated_d_latch_8_q));  // open: nQ
  not not_1 (not_1_out, gated_d_latch_2_q);
  not not_2 (not_2_out, gated_d_latch_6_q);
  not not_3 (not_3_out, gated_d_latch_5_q);
  not not_4 (not_4_out, gated_d_latch_8_q);
  not not_5 (not_5_out, gated_d_latch_6_q);
  not not_6 (not_6_out, gated_d_latch_8_q);
  and and_1 (and_1_out, gated_d_latch_1_q, not_1_out);
  and and_2 (and_2_out, and_1_out, nand_1_out);
  nand nand_1 (nand_1_out, gated_d_latch_3_q, gated_d_latch_4_q);
  nand nand_2 (nand_2_out, gated_d_latch_5_q, gated_d_latch_6_q);
  and and_3 (and_3_out, nand_2_out, nand_3_out);
  nand nand_3 (nand_3_out, gated_d_latch_7_q, gated_d_latch_8_q);
  and and_4 (and_4_out, gated_d_latch_5_q, not_2_out);
  and and_5 (and_5_out, and_4_out, nand_4_out);
  nand nand_4 (nand_4_out, gated_d_latch_7_q, gated_d_latch_8_q);
  and and_6 (and_6_out, not_3_out, gated_d_latch_6_q);
  and and_7 (and_7_out, and_6_out, nand_5_out);
  nand nand_5 (nand_5_out, gated_d_latch_7_q, gated_d_latch_8_q);
  and and_8 (and_8_out, gated_d_latch_5_q, gated_d_latch_6_q);
  and and_9 (and_9_out, and_8_out, nand_6_out);
  nand nand_6 (nand_6_out, gated_d_latch_7_q, gated_d_latch_8_q);
  nand nand_7 (nand_7_out, gated_d_latch_5_q, gated_d_latch_6_q);
  and and_10 (and_10_out, nand_7_out, and_11_out);
  and and_11 (and_11_out, gated_d_latch_7_q, not_4_out);
  and and_12 (and_12_out, gated_d_latch_5_q, not_5_out);
  and and_13 (and_13_out, and_12_out, and_14_out);
  and and_14 (and_14_out, gated_d_latch_7_q, not_6_out);
  and and_15 (out_10, and_3_out, and_2_out);
  and and_16 (out_20, and_5_out, and_2_out);
  and and_17 (out_34, and_7_out, and_2_out);
  and and_18 (out_35, and_9_out, and_2_out);
  and and_19 (out_39, and_10_out, and_2_out);
  and and_20 (out_51, and_13_out, and_2_out);
  not not_7 (not_7_out, gated_d_latch_1_q);
  and and_21 (and_21_out, not_7_out, gated_d_latch_2_q);
  nand nand_8 (nand_8_out, gated_d_latch_3_q, gated_d_latch_4_q);
  and and_22 (and_22_out, and_21_out, nand_8_out);
  and and_23 (out_11, and_3_out, and_22_out);
  and and_24 (out_21, and_5_out, and_22_out);
  and and_25 (out_36, and_9_out, and_22_out);
  and and_26 (out_40, and_10_out, and_22_out);
  and and_27 (out_52, and_13_out, and_22_out);
  and and_28 (and_28_out, gated_d_latch_1_q, gated_d_latch_2_q);
  nand nand_9 (nand_9_out, gated_d_latch_3_q, gated_d_latch_4_q);
  and and_29 (and_29_out, and_28_out, nand_9_out);
  and and_30 (out_12, and_3_out, and_29_out);
  and and_31 (out_22, and_5_out, and_29_out);
  and and_32 (out_37, and_9_out, and_29_out);
  and and_33 (out_41, and_10_out, and_29_out);
  and and_34 (out_53, and_13_out, and_29_out);
  not not_8 (not_8_out, gated_d_latch_4_q);
  nand nand_10 (nand_10_out, gated_d_latch_1_q, gated_d_latch_2_q);
  and and_35 (and_35_out, gated_d_latch_3_q, not_8_out);
  and and_36 (and_36_out, nand_10_out, and_35_out);
  and and_37 (out_13, and_3_out, and_36_out);
  and and_38 (out_23, and_5_out, and_36_out);
  and and_39 (out_38, and_9_out, and_36_out);
  and and_40 (out_42, and_10_out, and_36_out);
  and and_41 (out_54, and_13_out, and_36_out);
  not not_9 (not_9_out, gated_d_latch_2_q);
  not not_10 (not_10_out, gated_d_latch_4_q);
  and and_42 (and_42_out, gated_d_latch_1_q, not_9_out);
  and and_43 (and_43_out, gated_d_latch_3_q, not_10_out);
  and and_44 (and_44_out, and_42_out, and_43_out);
  and and_45 (out_14, and_3_out, and_44_out);
  and and_46 (out_24, and_5_out, and_44_out);
  and and_47 (out_43, and_10_out, and_44_out);
  and and_48 (out_55, and_13_out, and_44_out);
  not not_11 (not_11_out, gated_d_latch_1_q);
  and and_49 (and_49_out, not_11_out, gated_d_latch_2_q);
  and and_50 (and_50_out, gated_d_latch_3_q, not_12_out);
  not not_12 (not_12_out, gated_d_latch_4_q);
  and and_51 (and_51_out, and_49_out, and_50_out);
  and and_52 (out_15, and_3_out, and_51_out);
  and and_53 (out_25, and_5_out, and_51_out);
  and and_54 (out_44, and_10_out, and_51_out);
  and and_55 (out_56, and_13_out, and_51_out);
  and and_56 (and_56_out, gated_d_latch_1_q, gated_d_latch_2_q);
  and and_57 (and_57_out, gated_d_latch_3_q, not_13_out);
  not not_13 (not_13_out, gated_d_latch_4_q);
  and and_58 (and_58_out, and_56_out, and_57_out);
  and and_59 (out_16, and_3_out, and_58_out);
  and and_60 (out_26, and_5_out, and_58_out);
  and and_61 (out_45, and_10_out, and_58_out);
  and and_62 (out_57, and_13_out, and_58_out);
  not not_14 (not_14_out, gated_d_latch_3_q);
  and and_63 (and_63_out, not_14_out, gated_d_latch_4_q);
  nand nand_11 (nand_11_out, gated_d_latch_1_q, gated_d_latch_2_q);
  and and_64 (and_64_out, nand_11_out, and_63_out);
  and and_65 (out_17, and_3_out, and_64_out);
  and and_66 (out_27, and_5_out, and_64_out);
  and and_67 (out_46, and_10_out, and_64_out);
  and and_68 (out_58, and_13_out, and_64_out);
  and and_69 (and_69_out, gated_d_latch_1_q, not_15_out);
  not not_15 (not_15_out, gated_d_latch_2_q);
  not not_16 (not_16_out, gated_d_latch_3_q);
  and and_70 (and_70_out, not_16_out, gated_d_latch_4_q);
  and and_71 (and_71_out, and_69_out, and_70_out);
  and and_72 (out_18, and_3_out, and_71_out);
  and and_73 (out_28, and_5_out, and_71_out);
  and and_74 (out_47, and_10_out, and_71_out);
  and and_75 (out_59, and_13_out, and_71_out);
  not not_17 (not_17_out, gated_d_latch_1_q);
  and and_76 (and_76_out, not_17_out, gated_d_latch_2_q);
  not not_18 (not_18_out, gated_d_latch_3_q);
  and and_77 (and_77_out, not_18_out, gated_d_latch_4_q);
  and and_78 (and_78_out, and_76_out, and_77_out);
  and and_79 (out_19, and_3_out, and_78_out);
  and and_80 (out_29, and_5_out, and_78_out);
  and and_81 (out_48, and_10_out, and_78_out);
  and and_82 (out_60, and_13_out, and_78_out);
  and and_83 (and_83_out, gated_d_latch_1_q, gated_d_latch_2_q);
  not not_19 (not_19_out, gated_d_latch_3_q);
  and and_84 (and_84_out, not_19_out, gated_d_latch_4_q);
  and and_85 (and_85_out, and_83_out, and_84_out);
  and and_86 (out_30, and_5_out, and_85_out);
  and and_87 (out_49, and_10_out, and_85_out);
  and and_88 (out_61, and_13_out, and_85_out);
  and and_89 (and_89_out, gated_d_latch_3_q, gated_d_latch_4_q);
  nand nand_12 (nand_12_out, gated_d_latch_1_q, gated_d_latch_2_q);
  and and_90 (and_90_out, nand_12_out, and_89_out);
  and and_91 (out_31, and_5_out, and_90_out);
  and and_92 (out_50, and_10_out, and_90_out);
  and and_93 (out_62, and_13_out, and_90_out);
  and and_94 (and_94_out, gated_d_latch_1_q, not_20_out);
  not not_20 (not_20_out, gated_d_latch_2_q);
  and and_95 (and_95_out, gated_d_latch_3_q, gated_d_latch_4_q);
  and and_96 (and_96_out, and_94_out, and_95_out);
  and and_97 (out_32, and_5_out, and_96_out);
  not not_21 (not_21_out, gated_d_latch_1_q);
  and and_98 (and_98_out, not_21_out, gated_d_latch_2_q);
  and and_99 (and_99_out, gated_d_latch_3_q, gated_d_latch_4_q);
  and and_100 (and_100_out, and_98_out, and_99_out);
  and and_101 (out_33, and_5_out, and_100_out);

  // Notes on the sheet:
  //   add
  //   and
  //   lui
  //   slt
  //   beq
  //   lb
  //   Arithmatic
  //   Logical
  //   Constant
  //   Manipulation
  //   Comparitors
  //   Branch/Jump
  //   Load/Store
  //   add
  //   and
  //   lui
  //   slt
  //   beq
  //   lb
  //   slti
  //   lbu
  //   addi
  //   andi
  //   bgez
  //   addi
  //   andi
  //   slti
  //   bgez
  //   lbu
  //   addu
  //   nand
  //   sltu
  //   bgezal
  //   lh
  //   addu
  //   nand
  //   sltu
  //   bgezal
  //   lh
  //   addiu
  //   nandi
  //   sltiu
  //   bgtz
  //   lhu
  //   addiu
  //   nandi
  //   sltiu
  //   bgtz
  //   lhu
  //   div
  //   or
  //   blez
  //   lw
  //   div
  //   or
  //   blez
  //   lw
  //   divu
  //   ori
  //   bltzal
  //   lwl
  //   divu
  //   ori
  //   bltzal
  //   lwl
  //   mult
  //   nor
  //   bltz
  //   lwr
  //   mult
  //   nor
  //   bltz
  //   lwr
  //   multu
  //   nori
  //   bne
  //   sb
  //   multu
  //   nori
  //   bne
  //   sb
  //   sub
  //   xor
  //   j
  //   sh
  //   sub
  //   xor
  //   j
  //   sh
  //   subu
  //   xori
  //   jal
  //   sw
  //   subu
  //   xori
  //   jal
  //   sw
  //   xnor
  //   jalr
  //   swl
  //   xnor
  //   jalr
  //   swl
  //   xnori
  //   jr
  //   swr
  //   xnori
  //   jr
  //   swr
  //   sll
  //   sll
  //   slr
  //   slr
endmodule

module Register_Array (
  input  RDest,
  input  RSrc1,
  input  RSrc2,
  input  Imm,
  input  Hi,
  input  Lo,
  input  D0,
  input  D1,
  input  D2,
  input  D3,
  input  D4,
  input  D5,
  input  D6,
  input  D7,
  input  D8,
  input  D9,
  input  D10,
  input  D11,
  input  D12,
  input  D13,
  input  D14,
  input  D15,
  input  D16,
  input  D17,
  input  D18,
  input  D19,
  input  D20,
  input  D21,
  input  D22,
  input  D23,
  input  D24,
  input  D25,
  input  D26,
  input  D27,
  input  D28,
  input  D29,
  input  D30,
  input  D31,
  input  RDest_2,
  input  RSrc1_2,
  input  RSrc2_2,
  input  Imm_2,
  input  Hi_2,
  input  Lo_2,
  output Q0,
  output Q1,
  output Q2,
  output Q3,
  output Q4,
  output Q5,
  output Q6,
  output Q7,
  output Q8,
  output Q9,
  output Q10,
  output Q11,
  output Q12,
  output Q13,
  output Q14,
  output Q15,
  output Q16,
  output Q17,
  output Q18,
  output Q19,
  output Q20,
  output Q21,
  output Q22,
  output Q23,
  output Q24,
  output Q25,
  output Q26,
  output Q27,
  output Q28,
  output Q29,
  output Q30,
  output Q31
);

  wire Hi_d19_2, Hi_d20_2, Hi_d21_2, Hi_d22_2, Hi_d23_2, Hi_d24_2, Hi_d25_2, Hi_d26_2, Hi_d27_2, Hi_d28_2,
       Hi_d29_2, Hi_d30_2, Hi_d31_2, Hi_q0, Hi_q1, Hi_q2, Hi_q3, Hi_q4, Hi_q5, Hi_q6, Hi_q7, Hi_q8, Hi_q9,
       Hi_q10, Hi_q11, Hi_q12, Hi_q13, Hi_q14, Hi_q15, Hi_q16, Hi_q17, Hi_q18, Imm_q0, Imm_q1, Imm_q2,
       Imm_q3, Imm_q4, Imm_q5, Imm_q6, Imm_q7, Imm_q8, Imm_q9, Imm_q10, Imm_q11, Imm_q12, Imm_q13, Imm_q14,
       Imm_q15, Lo_d19_2, Lo_d20_2, Lo_d21_2, Lo_d22_2, Lo_d23_2, Lo_d24_2, Lo_d25_2, Lo_d26_2, Lo_d27_2,
       Lo_d28_2, Lo_d29_2, Lo_d30_2, Lo_d31_2, Lo_q0, Lo_q1, Lo_q2, Lo_q3, Lo_q4, Lo_q5, Lo_q6, Lo_q7, Lo_q8,
       Lo_q9, Lo_q10, Lo_q11, Lo_q12, Lo_q13, Lo_q14, Lo_q15, Lo_q16, Lo_q17, Lo_q18, RDest_d19_2,
       RDest_d20_2, RDest_d21_2, RDest_d22_2, RDest_d23_2, RDest_d24_2, RDest_d25_2, RDest_d26_2,
       RDest_d27_2, RDest_d28_2, RDest_d29_2, RDest_d30_2, RDest_d31_2, RDest_q0, RDest_q1, RDest_q2,
       RDest_q3, RDest_q4, RDest_q5, RDest_q6, RDest_q7, RDest_q8, RDest_q9, RDest_q10, RDest_q11, RDest_q12,
       RDest_q13, RDest_q14, RDest_q15, RDest_q16, RDest_q17, RDest_q18, RSrc1_d19_2, RSrc1_d20_2,
       RSrc1_d21_2, RSrc1_d22_2, RSrc1_d23_2, RSrc1_d24_2, RSrc1_d25_2, RSrc1_d26_2, RSrc1_d27_2,
       RSrc1_d28_2, RSrc1_d29_2, RSrc1_d30_2, RSrc1_d31_2, RSrc1_q0, RSrc1_q1, RSrc1_q2, RSrc1_q3, RSrc1_q4,
       RSrc1_q5, RSrc1_q6, RSrc1_q7, RSrc1_q8, RSrc1_q9, RSrc1_q10, RSrc1_q11, RSrc1_q12, RSrc1_q13,
       RSrc1_q14, RSrc1_q15, RSrc1_q16, RSrc1_q17, RSrc1_q18, RSrc2_d19_2, RSrc2_d20_2, RSrc2_d21_2,
       RSrc2_d22_2, RSrc2_d23_2, RSrc2_d24_2, RSrc2_d25_2, RSrc2_d26_2, RSrc2_d27_2, RSrc2_d28_2,
       RSrc2_d29_2, RSrc2_d30_2, RSrc2_d31_2, RSrc2_q0, RSrc2_q1, RSrc2_q2, RSrc2_q3, RSrc2_q4, RSrc2_q5,
       RSrc2_q6, RSrc2_q7, RSrc2_q8, RSrc2_q9, RSrc2_q10, RSrc2_q11, RSrc2_q12, RSrc2_q13, RSrc2_q14,
       RSrc2_q15, RSrc2_q16, RSrc2_q17, RSrc2_q18;

  _32_Bit_General_Register u_RDest (
    .E(RDest), .D0(D0), .Q0(RDest_q0), .D1(D1), .Q1(RDest_q1), .D2(D2), .Q2(RDest_q2), .D3(D3),
    .Q3(RDest_q3), .D4(D4), .Q4(RDest_q4), .D5(D5), .Q5(RDest_q5), .D6(D6), .Q6(RDest_q6), .D7(D7),
    .Q7(RDest_q7), .D8(D8), .Q8(RDest_q8), .D9(D9), .Q9(RDest_q9), .D10(D10), .Q10(RDest_q10), .D11(D11),
    .Q11(RDest_q11), .D12(D12), .Q12(RDest_q12), .D13(D13), .Q13(RDest_q13), .D14(D14), .Q14(RDest_q14),
    .D15(D15), .Q15(RDest_q15), .D16(D16), .Q16(RDest_q16), .D17(D17), .Q17(RDest_q17), .D18(D18),
    .Q18(RDest_q18), .D19(D19), .D19_2(RDest_d19_2), .D20(D20), .D20_2(RDest_d20_2), .D21(D21),
    .D21_2(RDest_d21_2), .D22(D22), .D22_2(RDest_d22_2), .D23(D23), .D23_2(RDest_d23_2), .D24(D24),
    .D24_2(RDest_d24_2), .D25(D25), .D25_2(RDest_d25_2), .D26(D26), .D26_2(RDest_d26_2), .D27(D27),
    .D27_2(RDest_d27_2), .D28(D28), .D28_2(RDest_d28_2), .D29(D29), .D29_2(RDest_d29_2), .D30(D30),
    .D30_2(RDest_d30_2), .D31(D31), .D31_2(RDest_d31_2));
  _32_Bit_General_Register u_RSrc1 (
    .E(RSrc1), .D0(D0), .Q0(RSrc1_q0), .D1(D1), .Q1(RSrc1_q1), .D2(D2), .Q2(RSrc1_q2), .D3(D3),
    .Q3(RSrc1_q3), .D4(D4), .Q4(RSrc1_q4), .D5(D5), .Q5(RSrc1_q5), .D6(D6), .Q6(RSrc1_q6), .D7(D7),
    .Q7(RSrc1_q7), .D8(D8), .Q8(RSrc1_q8), .D9(D9), .Q9(RSrc1_q9), .D10(D10), .Q10(RSrc1_q10), .D11(D11),
    .Q11(RSrc1_q11), .D12(D12), .Q12(RSrc1_q12), .D13(D13), .Q13(RSrc1_q13), .D14(D14), .Q14(RSrc1_q14),
    .D15(D15), .Q15(RSrc1_q15), .D16(D16), .Q16(RSrc1_q16), .D17(D17), .Q17(RSrc1_q17), .D18(D18),
    .Q18(RSrc1_q18), .D19(D19), .D19_2(RSrc1_d19_2), .D20(D20), .D20_2(RSrc1_d20_2), .D21(D21),
    .D21_2(RSrc1_d21_2), .D22(D22), .D22_2(RSrc1_d22_2), .D23(D23), .D23_2(RSrc1_d23_2), .D24(D24),
    .D24_2(RSrc1_d24_2), .D25(D25), .D25_2(RSrc1_d25_2), .D26(D26), .D26_2(RSrc1_d26_2), .D27(D27),
    .D27_2(RSrc1_d27_2), .D28(D28), .D28_2(RSrc1_d28_2), .D29(D29), .D29_2(RSrc1_d29_2), .D30(D30),
    .D30_2(RSrc1_d30_2), .D31(D31), .D31_2(RSrc1_d31_2));
  _32_Bit_General_Register u_RSrc2 (
    .E(RSrc2), .D0(D0), .Q0(RSrc2_q0), .D1(D1), .Q1(RSrc2_q1), .D2(D2), .Q2(RSrc2_q2), .D3(D3),
    .Q3(RSrc2_q3), .D4(D4), .Q4(RSrc2_q4), .D5(D5), .Q5(RSrc2_q5), .D6(D6), .Q6(RSrc2_q6), .D7(D7),
    .Q7(RSrc2_q7), .D8(D8), .Q8(RSrc2_q8), .D9(D9), .Q9(RSrc2_q9), .D10(D10), .Q10(RSrc2_q10), .D11(D11),
    .Q11(RSrc2_q11), .D12(D12), .Q12(RSrc2_q12), .D13(D13), .Q13(RSrc2_q13), .D14(D14), .Q14(RSrc2_q14),
    .D15(D15), .Q15(RSrc2_q15), .D16(D16), .Q16(RSrc2_q16), .D17(D17), .Q17(RSrc2_q17), .D18(D18),
    .Q18(RSrc2_q18), .D19(D19), .D19_2(RSrc2_d19_2), .D20(D20), .D20_2(RSrc2_d20_2), .D21(D21),
    .D21_2(RSrc2_d21_2), .D22(D22), .D22_2(RSrc2_d22_2), .D23(D23), .D23_2(RSrc2_d23_2), .D24(D24),
    .D24_2(RSrc2_d24_2), .D25(D25), .D25_2(RSrc2_d25_2), .D26(D26), .D26_2(RSrc2_d26_2), .D27(D27),
    .D27_2(RSrc2_d27_2), .D28(D28), .D28_2(RSrc2_d28_2), .D29(D29), .D29_2(RSrc2_d29_2), .D30(D30),
    .D30_2(RSrc2_d30_2), .D31(D31), .D31_2(RSrc2_d31_2));
  and and_1 (Q0, RDest_q0, RDest_2);
  and and_2 (Q1, RDest_q1, RDest_2);
  and and_3 (Q2, RDest_q2, RDest_2);
  and and_4 (Q3, RDest_q3, RDest_2);
  and and_5 (Q4, RDest_q4, RDest_2);
  and and_6 (Q5, RDest_q5, RDest_2);
  and and_7 (Q6, RDest_q6, RDest_2);
  and and_8 (Q7, RDest_q7, RDest_2);
  and and_9 (Q8, RDest_q8, RDest_2);
  and and_10 (Q9, RDest_q9, RDest_2);
  and and_11 (Q10, RDest_q10, RDest_2);
  and and_12 (Q11, RDest_q11, RDest_2);
  and and_13 (Q12, RDest_q12, RDest_2);
  and and_14 (Q13, RDest_q13, RDest_2);
  and and_15 (Q14, RDest_q14, RDest_2);
  and and_16 (Q15, RDest_q15, RDest_2);
  and and_17 (Q16, RDest_q16, RDest_2);
  and and_18 (Q17, RDest_q17, RDest_2);
  and and_19 (Q18, RDest_q18, RDest_2);
  and and_20 (Q19, RDest_d19_2, RDest_2);
  and and_21 (Q20, RDest_d20_2, RDest_2);
  and and_22 (Q21, RDest_d21_2, RDest_2);
  and and_23 (Q22, RDest_d22_2, RDest_2);
  and and_24 (Q23, RDest_d23_2, RDest_2);
  and and_25 (Q24, RDest_d24_2, RDest_2);
  and and_26 (Q25, RDest_d25_2, RDest_2);
  and and_27 (Q26, RDest_d26_2, RDest_2);
  and and_28 (Q27, RDest_d27_2, RDest_2);
  and and_29 (Q28, RDest_d28_2, RDest_2);
  and and_30 (Q29, RDest_d29_2, RDest_2);
  and and_31 (Q30, RDest_d30_2, RDest_2);
  and and_32 (Q31, RDest_d31_2, RDest_2);
  and and_33 (Q0, RSrc1_q0, RSrc1_2);
  and and_34 (Q1, RSrc1_q1, RSrc1_2);
  and and_35 (Q2, RSrc1_q2, RSrc1_2);
  and and_36 (Q3, RSrc1_q3, RSrc1_2);
  and and_37 (Q4, RSrc1_q4, RSrc1_2);
  and and_38 (Q5, RSrc1_q5, RSrc1_2);
  and and_39 (Q6, RSrc1_q6, RSrc1_2);
  and and_40 (Q7, RSrc1_q7, RSrc1_2);
  and and_41 (Q8, RSrc1_q8, RSrc1_2);
  and and_42 (Q9, RSrc1_q9, RSrc1_2);
  and and_43 (Q10, RSrc1_q10, RSrc1_2);
  and and_44 (Q11, RSrc1_q11, RSrc1_2);
  and and_45 (Q12, RSrc1_q12, RSrc1_2);
  and and_46 (Q13, RSrc1_q13, RSrc1_2);
  and and_47 (Q14, RSrc1_q14, RSrc1_2);
  and and_48 (Q15, RSrc1_q15, RSrc1_2);
  and and_49 (Q16, RSrc1_q16, RSrc1_2);
  and and_50 (Q17, RSrc1_q17, RSrc1_2);
  and and_51 (Q18, RSrc1_q18, RSrc1_2);
  and and_52 (Q19, RSrc1_d19_2, RSrc1_2);
  and and_53 (Q20, RSrc1_d20_2, RSrc1_2);
  and and_54 (Q21, RSrc1_d21_2, RSrc1_2);
  and and_55 (Q22, RSrc1_d22_2, RSrc1_2);
  and and_56 (Q23, RSrc1_d23_2, RSrc1_2);
  and and_57 (Q24, RSrc1_d24_2, RSrc1_2);
  and and_58 (Q25, RSrc1_d25_2, RSrc1_2);
  and and_59 (Q26, RSrc1_d26_2, RSrc1_2);
  and and_60 (Q27, RSrc1_d27_2, RSrc1_2);
  and and_61 (Q28, RSrc1_d28_2, RSrc1_2);
  and and_62 (Q29, RSrc1_d29_2, RSrc1_2);
  and and_63 (Q30, RSrc1_d30_2, RSrc1_2);
  and and_64 (Q31, RSrc1_d31_2, RSrc1_2);
  and and_65 (Q0, RSrc2_q0, RSrc2_2);
  and and_66 (Q1, RSrc2_q1, RSrc2_2);
  and and_67 (Q2, RSrc2_q2, RSrc2_2);
  and and_68 (Q3, RSrc2_q3, RSrc2_2);
  and and_69 (Q4, RSrc2_q4, RSrc2_2);
  and and_70 (Q5, RSrc2_q5, RSrc2_2);
  and and_71 (Q6, RSrc2_q6, RSrc2_2);
  and and_72 (Q7, RSrc2_q7, RSrc2_2);
  and and_73 (Q8, RSrc2_q8, RSrc2_2);
  and and_74 (Q9, RSrc2_q9, RSrc2_2);
  and and_75 (Q10, RSrc2_q10, RSrc2_2);
  and and_76 (Q11, RSrc2_q11, RSrc2_2);
  and and_77 (Q12, RSrc2_q12, RSrc2_2);
  and and_78 (Q13, RSrc2_q13, RSrc2_2);
  and and_79 (Q14, RSrc2_q14, RSrc2_2);
  and and_80 (Q15, RSrc2_q15, RSrc2_2);
  and and_81 (Q16, RSrc2_q16, RSrc2_2);
  and and_82 (Q17, RSrc2_q17, RSrc2_2);
  and and_83 (Q18, RSrc2_q18, RSrc2_2);
  and and_84 (Q19, RSrc2_d19_2, RSrc2_2);
  and and_85 (Q20, RSrc2_d20_2, RSrc2_2);
  and and_86 (Q21, RSrc2_d21_2, RSrc2_2);
  and and_87 (Q22, RSrc2_d22_2, RSrc2_2);
  and and_88 (Q23, RSrc2_d23_2, RSrc2_2);
  and and_89 (Q24, RSrc2_d24_2, RSrc2_2);
  and and_90 (Q25, RSrc2_d25_2, RSrc2_2);
  and and_91 (Q26, RSrc2_d26_2, RSrc2_2);
  and and_92 (Q27, RSrc2_d27_2, RSrc2_2);
  and and_93 (Q28, RSrc2_d28_2, RSrc2_2);
  and and_94 (Q29, RSrc2_d29_2, RSrc2_2);
  and and_95 (Q30, RSrc2_d30_2, RSrc2_2);
  and and_96 (Q31, RSrc2_d31_2, RSrc2_2);
  _16_Bit_General_Register u_Imm (
    .E(Imm), .D0(D0), .Q0(Imm_q0), .D1(D1), .Q1(Imm_q1), .D2(D2), .Q2(Imm_q2), .D3(D3), .Q3(Imm_q3), .D4(D4),
    .Q4(Imm_q4), .D5(D5), .Q5(Imm_q5), .D6(D6), .Q6(Imm_q6), .D7(D7), .Q7(Imm_q7), .D8(D8), .Q8(Imm_q8),
    .D9(D9), .Q9(Imm_q9), .D10(D10), .Q10(Imm_q10), .D11(D11), .Q11(Imm_q11), .D12(D12), .Q12(Imm_q12),
    .D13(D13), .Q13(Imm_q13), .D14(D14), .Q14(Imm_q14), .D15(D15), .Q15(Imm_q15));
  _32_Bit_General_Register u_Hi (
    .E(Hi), .D0(D0), .Q0(Hi_q0), .D1(D1), .Q1(Hi_q1), .D2(D2), .Q2(Hi_q2), .D3(D3), .Q3(Hi_q3), .D4(D4),
    .Q4(Hi_q4), .D5(D5), .Q5(Hi_q5), .D6(D6), .Q6(Hi_q6), .D7(D7), .Q7(Hi_q7), .D8(D8), .Q8(Hi_q8), .D9(D9),
    .Q9(Hi_q9), .D10(D10), .Q10(Hi_q10), .D11(D11), .Q11(Hi_q11), .D12(D12), .Q12(Hi_q12), .D13(D13),
    .Q13(Hi_q13), .D14(D14), .Q14(Hi_q14), .D15(D15), .Q15(Hi_q15), .D16(D16), .Q16(Hi_q16), .D17(D17),
    .Q17(Hi_q17), .D18(D18), .Q18(Hi_q18), .D19(D19), .D19_2(Hi_d19_2), .D20(D20), .D20_2(Hi_d20_2),
    .D21(D21), .D21_2(Hi_d21_2), .D22(D22), .D22_2(Hi_d22_2), .D23(D23), .D23_2(Hi_d23_2), .D24(D24),
    .D24_2(Hi_d24_2), .D25(D25), .D25_2(Hi_d25_2), .D26(D26), .D26_2(Hi_d26_2), .D27(D27), .D27_2(Hi_d27_2),
    .D28(D28), .D28_2(Hi_d28_2), .D29(D29), .D29_2(Hi_d29_2), .D30(D30), .D30_2(Hi_d30_2), .D31(D31),
    .D31_2(Hi_d31_2));
  _32_Bit_General_Register u_Lo (
    .E(Lo), .D0(D0), .Q0(Lo_q0), .D1(D1), .Q1(Lo_q1), .D2(D2), .Q2(Lo_q2), .D3(D3), .Q3(Lo_q3), .D4(D4),
    .Q4(Lo_q4), .D5(D5), .Q5(Lo_q5), .D6(D6), .Q6(Lo_q6), .D7(D7), .Q7(Lo_q7), .D8(D8), .Q8(Lo_q8), .D9(D9),
    .Q9(Lo_q9), .D10(D10), .Q10(Lo_q10), .D11(D11), .Q11(Lo_q11), .D12(D12), .Q12(Lo_q12), .D13(D13),
    .Q13(Lo_q13), .D14(D14), .Q14(Lo_q14), .D15(D15), .Q15(Lo_q15), .D16(D16), .Q16(Lo_q16), .D17(D17),
    .Q17(Lo_q17), .D18(D18), .Q18(Lo_q18), .D19(D19), .D19_2(Lo_d19_2), .D20(D20), .D20_2(Lo_d20_2),
    .D21(D21), .D21_2(Lo_d21_2), .D22(D22), .D22_2(Lo_d22_2), .D23(D23), .D23_2(Lo_d23_2), .D24(D24),
    .D24_2(Lo_d24_2), .D25(D25), .D25_2(Lo_d25_2), .D26(D26), .D26_2(Lo_d26_2), .D27(D27), .D27_2(Lo_d27_2),
    .D28(D28), .D28_2(Lo_d28_2), .D29(D29), .D29_2(Lo_d29_2), .D30(D30), .D30_2(Lo_d30_2), .D31(D31),
    .D31_2(Lo_d31_2));
  and and_97 (Q0, Imm_q0, Imm_2);
  and and_98 (Q1, Imm_q1, Imm_2);
  and and_99 (Q2, Imm_q2, Imm_2);
  and and_100 (Q3, Imm_q3, Imm_2);
  and and_101 (Q4, Imm_q4, Imm_2);
  and and_102 (Q5, Imm_q5, Imm_2);
  and and_103 (Q6, Imm_q6, Imm_2);
  and and_104 (Q7, Imm_q7, Imm_2);
  and and_105 (Q8, Imm_q8, Imm_2);
  and and_106 (Q9, Imm_q9, Imm_2);
  and and_107 (Q10, Imm_q10, Imm_2);
  and and_108 (Q11, Imm_q11, Imm_2);
  and and_109 (Q12, Imm_q12, Imm_2);
  and and_110 (Q13, Imm_q13, Imm_2);
  and and_111 (Q14, Imm_q14, Imm_2);
  and and_112 (Q15, Imm_q15, Imm_2);
  and and_113 (Q0, Hi_q0, Hi_2);
  and and_114 (Q1, Hi_q1, Hi_2);
  and and_115 (Q2, Hi_q2, Hi_2);
  and and_116 (Q3, Hi_q3, Hi_2);
  and and_117 (Q4, Hi_q4, Hi_2);
  and and_118 (Q5, Hi_q5, Hi_2);
  and and_119 (Q6, Hi_q6, Hi_2);
  and and_120 (Q7, Hi_q7, Hi_2);
  and and_121 (Q8, Hi_q8, Hi_2);
  and and_122 (Q9, Hi_q9, Hi_2);
  and and_123 (Q10, Hi_q10, Hi_2);
  and and_124 (Q11, Hi_q11, Hi_2);
  and and_125 (Q12, Hi_q12, Hi_2);
  and and_126 (Q13, Hi_q13, Hi_2);
  and and_127 (Q14, Hi_q14, Hi_2);
  and and_128 (Q15, Hi_q15, Hi_2);
  and and_129 (Q16, Hi_q16, Hi_2);
  and and_130 (Q17, Hi_q17, Hi_2);
  and and_131 (Q18, Hi_q18, Hi_2);
  and and_132 (Q19, Hi_d19_2, Hi_2);
  and and_133 (Q20, Hi_d20_2, Hi_2);
  and and_134 (Q21, Hi_d21_2, Hi_2);
  and and_135 (Q22, Hi_d22_2, Hi_2);
  and and_136 (Q23, Hi_d23_2, Hi_2);
  and and_137 (Q24, Hi_d24_2, Hi_2);
  and and_138 (Q25, Hi_d25_2, Hi_2);
  and and_139 (Q26, Hi_d26_2, Hi_2);
  and and_140 (Q27, Hi_d27_2, Hi_2);
  and and_141 (Q28, Hi_d28_2, Hi_2);
  and and_142 (Q29, Hi_d29_2, Hi_2);
  and and_143 (Q30, Hi_d30_2, Hi_2);
  and and_144 (Q31, Hi_d31_2, Hi_2);
  and and_145 (Q0, Lo_q0, Lo_2);
  and and_146 (Q1, Lo_q1, Lo_2);
  and and_147 (Q2, Lo_q2, Lo_2);
  and and_148 (Q3, Lo_q3, Lo_2);
  and and_149 (Q4, Lo_q4, Lo_2);
  and and_150 (Q5, Lo_q5, Lo_2);
  and and_151 (Q6, Lo_q6, Lo_2);
  and and_152 (Q7, Lo_q7, Lo_2);
  and and_153 (Q8, Lo_q8, Lo_2);
  and and_154 (Q9, Lo_q9, Lo_2);
  and and_155 (Q10, Lo_q10, Lo_2);
  and and_156 (Q11, Lo_q11, Lo_2);
  and and_157 (Q12, Lo_q12, Lo_2);
  and and_158 (Q13, Lo_q13, Lo_2);
  and and_159 (Q14, Lo_q14, Lo_2);
  and and_160 (Q15, Lo_q15, Lo_2);
  and and_161 (Q16, Lo_q16, Lo_2);
  and and_162 (Q17, Lo_q17, Lo_2);
  and and_163 (Q18, Lo_q18, Lo_2);
  and and_164 (Q19, Lo_d19_2, Lo_2);
  and and_165 (Q20, Lo_d20_2, Lo_2);
  and and_166 (Q21, Lo_d21_2, Lo_2);
  and and_167 (Q22, Lo_d22_2, Lo_2);
  and and_168 (Q23, Lo_d23_2, Lo_2);
  and and_169 (Q24, Lo_d24_2, Lo_2);
  and and_170 (Q25, Lo_d25_2, Lo_2);
  and and_171 (Q26, Lo_d26_2, Lo_2);
  and and_172 (Q27, Lo_d27_2, Lo_2);
  and and_173 (Q28, Lo_d28_2, Lo_2);
  and and_174 (Q29, Lo_d29_2, Lo_2);
  and and_175 (Q30, Lo_d30_2, Lo_2);
  and and_176 (Q31, Lo_d31_2, Lo_2);

  // Notes on the sheet:
  //   Input
  //   Write to Input Register
  //   Read from Output Register
  //   Output
endmodule

module Half_Adder (
  input  A,
  input  B,
  output Sum,
  output Carry
);

  xor xor_1 (Sum, A, B);
  and and_1 (Carry, B, A);
endmodule

module Full_Adder (
  input  A,
  input  B,
  input  C_in,
  output Sum,
  output C_out
);

  wire and_1_out, half_adder_1_carry, xor_1_out;

  Half_Adder half_adder_1 (.A(xor_1_out), .B(C_in), .Sum(Sum), .Carry(half_adder_1_carry));
  xor xor_1 (xor_1_out, A, B);
  and and_1 (and_1_out, A, B);
  or or_1 (C_out, half_adder_1_carry, and_1_out);
endmodule

module add (
  input  A0,
  input  B0,
  input  A1,
  input  B1,
  input  A2,
  input  B2,
  input  A3,
  input  B3,
  input  A4,
  input  B4,
  input  A5,
  input  B5,
  input  A6,
  input  B6,
  input  A7,
  input  B7,
  input  A8,
  input  B8,
  input  A9,
  input  B9,
  input  A10,
  input  B10,
  input  A11,
  input  B11,
  input  A12,
  input  B12,
  input  A13,
  input  B13,
  input  A14,
  input  B14,
  input  A15,
  input  B15,
  input  A16,
  input  B16,
  input  A17,
  input  B17,
  input  A18,
  input  B18,
  input  A19,
  input  B19,
  input  A20,
  input  B20,
  input  A21,
  input  B21,
  input  A22,
  input  B22,
  input  A23,
  input  B23,
  input  A24,
  input  B24,
  input  A25,
  input  B25,
  input  A26,
  input  B26,
  input  A27,
  input  B27,
  input  A28,
  input  B28,
  input  A29,
  input  B29,
  input  A30,
  input  B30,
  input  A31,
  input  B31,
  output _0,
  output _1,
  output _2,
  output _3,
  output _4,
  output _5,
  output _6,
  output _7,
  output _8,
  output _9,
  output _10,
  output _11,
  output _12,
  output _13,
  output _14,
  output _15,
  output _16,
  output _17,
  output _18,
  output _19,
  output _20,
  output _21,
  output _22,
  output _23,
  output _24,
  output _25,
  output _26,
  output _27,
  output _28,
  output _29,
  output _30,
  output _31,
  output Carry,
  output Overflow
);

  wire full_adder_1_c_out, full_adder_2_c_out, full_adder_3_c_out, full_adder_4_c_out, full_adder_5_c_out,
       full_adder_6_c_out, full_adder_7_c_out, full_adder_8_c_out, full_adder_9_c_out, full_adder_10_c_out,
       full_adder_11_c_out, full_adder_12_c_out, full_adder_13_c_out, full_adder_14_c_out,
       full_adder_15_c_out, full_adder_16_c_out, full_adder_17_c_out, full_adder_18_c_out,
       full_adder_19_c_out, full_adder_20_c_out, full_adder_21_c_out, full_adder_22_c_out,
       full_adder_23_c_out, full_adder_24_c_out, full_adder_25_c_out, full_adder_26_c_out,
       full_adder_27_c_out, full_adder_28_c_out, full_adder_29_c_out, full_adder_30_c_out, half_adder_1_carry;

  Half_Adder half_adder_1 (.A(A0), .B(B0), .Sum(_0), .Carry(half_adder_1_carry));
  Full_Adder full_adder_1 (.A(A1), .B(B1), .C_in(half_adder_1_carry), .Sum(_1), .C_out(full_adder_1_c_out));
  Full_Adder full_adder_2 (.A(A2), .B(B2), .C_in(full_adder_1_c_out), .Sum(_2), .C_out(full_adder_2_c_out));
  Full_Adder full_adder_3 (.A(A3), .B(B3), .C_in(full_adder_2_c_out), .Sum(_3), .C_out(full_adder_3_c_out));
  Full_Adder full_adder_4 (.A(A4), .B(B4), .C_in(full_adder_3_c_out), .Sum(_4), .C_out(full_adder_4_c_out));
  Full_Adder full_adder_5 (.A(A5), .B(B5), .C_in(full_adder_4_c_out), .Sum(_5), .C_out(full_adder_5_c_out));
  Full_Adder full_adder_6 (.A(A6), .B(B6), .C_in(full_adder_5_c_out), .Sum(_6), .C_out(full_adder_6_c_out));
  Full_Adder full_adder_7 (.A(A7), .B(B7), .C_in(full_adder_6_c_out), .Sum(_7), .C_out(full_adder_7_c_out));
  Full_Adder full_adder_8 (.A(A8), .B(B8), .C_in(full_adder_7_c_out), .Sum(_8), .C_out(full_adder_8_c_out));
  Full_Adder full_adder_9 (.A(A9), .B(B9), .C_in(full_adder_8_c_out), .Sum(_9), .C_out(full_adder_9_c_out));
  Full_Adder full_adder_10 (.A(A10), .B(B10), .C_in(full_adder_9_c_out), .Sum(_10), .C_out(full_adder_10_c_out));
  Full_Adder full_adder_11 (.A(A11), .B(B11), .C_in(full_adder_10_c_out), .Sum(_11), .C_out(full_adder_11_c_out));
  Full_Adder full_adder_12 (.A(A12), .B(B12), .C_in(full_adder_11_c_out), .Sum(_12), .C_out(full_adder_12_c_out));
  Full_Adder full_adder_13 (.A(A13), .B(B13), .C_in(full_adder_12_c_out), .Sum(_13), .C_out(full_adder_13_c_out));
  Full_Adder full_adder_14 (.A(A14), .B(B14), .C_in(full_adder_13_c_out), .Sum(_14), .C_out(full_adder_14_c_out));
  Full_Adder full_adder_15 (.A(A15), .B(B15), .C_in(full_adder_14_c_out), .Sum(_15), .C_out(full_adder_15_c_out));
  Full_Adder full_adder_16 (.A(A16), .B(B16), .C_in(full_adder_15_c_out), .Sum(_16), .C_out(full_adder_16_c_out));
  Full_Adder full_adder_17 (.A(A17), .B(B17), .C_in(full_adder_16_c_out), .Sum(_17), .C_out(full_adder_17_c_out));
  Full_Adder full_adder_18 (.A(A18), .B(B18), .C_in(full_adder_17_c_out), .Sum(_18), .C_out(full_adder_18_c_out));
  Full_Adder full_adder_19 (.A(A19), .B(B19), .C_in(full_adder_18_c_out), .Sum(_19), .C_out(full_adder_19_c_out));
  Full_Adder full_adder_20 (.A(A20), .B(B20), .C_in(full_adder_19_c_out), .Sum(_20), .C_out(full_adder_20_c_out));
  Full_Adder full_adder_21 (.A(A21), .B(B21), .C_in(full_adder_20_c_out), .Sum(_21), .C_out(full_adder_21_c_out));
  Full_Adder full_adder_22 (.A(A22), .B(B22), .C_in(full_adder_21_c_out), .Sum(_22), .C_out(full_adder_22_c_out));
  Full_Adder full_adder_23 (.A(A23), .B(B23), .C_in(full_adder_22_c_out), .Sum(_23), .C_out(full_adder_23_c_out));
  Full_Adder full_adder_24 (.A(A24), .B(B24), .C_in(full_adder_23_c_out), .Sum(_24), .C_out(full_adder_24_c_out));
  Full_Adder full_adder_25 (.A(A25), .B(B25), .C_in(full_adder_24_c_out), .Sum(_25), .C_out(full_adder_25_c_out));
  Full_Adder full_adder_26 (.A(A26), .B(B26), .C_in(full_adder_25_c_out), .Sum(_26), .C_out(full_adder_26_c_out));
  Full_Adder full_adder_27 (.A(A27), .B(B27), .C_in(full_adder_26_c_out), .Sum(_27), .C_out(full_adder_27_c_out));
  Full_Adder full_adder_28 (.A(A28), .B(B28), .C_in(full_adder_27_c_out), .Sum(_28), .C_out(full_adder_28_c_out));
  Full_Adder full_adder_29 (.A(A29), .B(B29), .C_in(full_adder_28_c_out), .Sum(_29), .C_out(full_adder_29_c_out));
  Full_Adder full_adder_30 (.A(A30), .B(B30), .C_in(full_adder_29_c_out), .Sum(_30), .C_out(full_adder_30_c_out));
  Full_Adder full_adder_31 (.A(A31), .B(B31), .C_in(full_adder_30_c_out), .Sum(_31), .C_out(Carry));
  xor xor_1 (Overflow, Carry, full_adder_30_c_out);
endmodule

module addi (
  input  A0,
  input  B0,
  input  A1,
  input  B1,
  input  A2,
  input  B2,
  input  A3,
  input  B3,
  input  A4,
  input  B4,
  input  A5,
  input  B5,
  input  A6,
  input  B6,
  input  A7,
  input  B7,
  input  A8,
  input  B8,
  input  A9,
  input  B9,
  input  A10,
  input  B10,
  input  A11,
  input  B11,
  input  A12,
  input  B12,
  input  A13,
  input  B13,
  input  A14,
  input  B14,
  input  A15,
  input  B15,
  input  A16,
  input  A17,
  input  A18,
  input  A19,
  input  A20,
  input  A21,
  input  A22,
  input  A23,
  input  A24,
  input  A25,
  input  A26,
  input  A27,
  input  A28,
  input  A29,
  input  A30,
  input  A31,
  output _0,
  output _1,
  output _2,
  output _3,
  output _4,
  output _5,
  output _6,
  output _7,
  output _8,
  output _9,
  output _10,
  output _11,
  output _12,
  output _13,
  output _14,
  output _15,
  output _16,
  output _17,
  output _18,
  output _19,
  output _20,
  output _21,
  output _22,
  output _23,
  output _24,
  output _25,
  output _26,
  output _27,
  output _28,
  output _29,
  output _30,
  output _31,
  output Carry,
  output Overflow
);

  wire full_adder_1_c_out, full_adder_2_c_out, full_adder_3_c_out, full_adder_4_c_out, full_adder_5_c_out,
       full_adder_6_c_out, full_adder_7_c_out, full_adder_8_c_out, full_adder_9_c_out, full_adder_10_c_out,
       full_adder_11_c_out, full_adder_12_c_out, full_adder_13_c_out, full_adder_14_c_out,
       full_adder_15_c_out, full_adder_16_c_out, full_adder_17_c_out, full_adder_18_c_out,
       full_adder_19_c_out, full_adder_20_c_out, full_adder_21_c_out, full_adder_22_c_out,
       full_adder_23_c_out, full_adder_24_c_out, full_adder_25_c_out, full_adder_26_c_out,
       full_adder_27_c_out, full_adder_28_c_out, full_adder_29_c_out, full_adder_30_c_out, half_adder_1_carry;

  Half_Adder half_adder_1 (.A(A0), .B(B0), .Sum(_0), .Carry(half_adder_1_carry));
  Full_Adder full_adder_1 (.A(A1), .B(B1), .C_in(half_adder_1_carry), .Sum(_1), .C_out(full_adder_1_c_out));
  Full_Adder full_adder_2 (.A(A2), .B(B2), .C_in(full_adder_1_c_out), .Sum(_2), .C_out(full_adder_2_c_out));
  Full_Adder full_adder_3 (.A(A3), .B(B3), .C_in(full_adder_2_c_out), .Sum(_3), .C_out(full_adder_3_c_out));
  Full_Adder full_adder_4 (.A(A4), .B(B4), .C_in(full_adder_3_c_out), .Sum(_4), .C_out(full_adder_4_c_out));
  Full_Adder full_adder_5 (.A(A5), .B(B5), .C_in(full_adder_4_c_out), .Sum(_5), .C_out(full_adder_5_c_out));
  Full_Adder full_adder_6 (.A(A6), .B(B6), .C_in(full_adder_5_c_out), .Sum(_6), .C_out(full_adder_6_c_out));
  Full_Adder full_adder_7 (.A(A7), .B(B7), .C_in(full_adder_6_c_out), .Sum(_7), .C_out(full_adder_7_c_out));
  Full_Adder full_adder_8 (.A(A8), .B(B8), .C_in(full_adder_7_c_out), .Sum(_8), .C_out(full_adder_8_c_out));
  Full_Adder full_adder_9 (.A(A9), .B(B9), .C_in(full_adder_8_c_out), .Sum(_9), .C_out(full_adder_9_c_out));
  Full_Adder full_adder_10 (.A(A10), .B(B10), .C_in(full_adder_9_c_out), .Sum(_10), .C_out(full_adder_10_c_out));
  Full_Adder full_adder_11 (.A(A11), .B(B11), .C_in(full_adder_10_c_out), .Sum(_11), .C_out(full_adder_11_c_out));
  Full_Adder full_adder_12 (.A(A12), .B(B12), .C_in(full_adder_11_c_out), .Sum(_12), .C_out(full_adder_12_c_out));
  Full_Adder full_adder_13 (.A(A13), .B(B13), .C_in(full_adder_12_c_out), .Sum(_13), .C_out(full_adder_13_c_out));
  Full_Adder full_adder_14 (.A(A14), .B(B14), .C_in(full_adder_13_c_out), .Sum(_14), .C_out(full_adder_14_c_out));
  Full_Adder full_adder_15 (.A(A15), .B(B15), .C_in(full_adder_14_c_out), .Sum(_15), .C_out(full_adder_15_c_out));
  Full_Adder full_adder_16 (.A(A16), .B(1'b0), .C_in(full_adder_15_c_out), .Sum(_16), .C_out(full_adder_16_c_out));
  Full_Adder full_adder_17 (.A(A17), .B(1'b0), .C_in(full_adder_16_c_out), .Sum(_17), .C_out(full_adder_17_c_out));
  Full_Adder full_adder_18 (.A(A18), .B(1'b0), .C_in(full_adder_17_c_out), .Sum(_18), .C_out(full_adder_18_c_out));
  Full_Adder full_adder_19 (.A(A19), .B(1'b0), .C_in(full_adder_18_c_out), .Sum(_19), .C_out(full_adder_19_c_out));
  Full_Adder full_adder_20 (.A(A20), .B(1'b0), .C_in(full_adder_19_c_out), .Sum(_20), .C_out(full_adder_20_c_out));
  Full_Adder full_adder_21 (.A(A21), .B(1'b0), .C_in(full_adder_20_c_out), .Sum(_21), .C_out(full_adder_21_c_out));
  Full_Adder full_adder_22 (.A(A22), .B(1'b0), .C_in(full_adder_21_c_out), .Sum(_22), .C_out(full_adder_22_c_out));
  Full_Adder full_adder_23 (.A(A23), .B(1'b0), .C_in(full_adder_22_c_out), .Sum(_23), .C_out(full_adder_23_c_out));
  Full_Adder full_adder_24 (.A(A24), .B(1'b0), .C_in(full_adder_23_c_out), .Sum(_24), .C_out(full_adder_24_c_out));
  Full_Adder full_adder_25 (.A(A25), .B(1'b0), .C_in(full_adder_24_c_out), .Sum(_25), .C_out(full_adder_25_c_out));
  Full_Adder full_adder_26 (.A(A26), .B(1'b0), .C_in(full_adder_25_c_out), .Sum(_26), .C_out(full_adder_26_c_out));
  Full_Adder full_adder_27 (.A(A27), .B(1'b0), .C_in(full_adder_26_c_out), .Sum(_27), .C_out(full_adder_27_c_out));
  Full_Adder full_adder_28 (.A(A28), .B(1'b0), .C_in(full_adder_27_c_out), .Sum(_28), .C_out(full_adder_28_c_out));
  Full_Adder full_adder_29 (.A(A29), .B(1'b0), .C_in(full_adder_28_c_out), .Sum(_29), .C_out(full_adder_29_c_out));
  Full_Adder full_adder_30 (.A(A30), .B(1'b0), .C_in(full_adder_29_c_out), .Sum(_30), .C_out(full_adder_30_c_out));
  Full_Adder full_adder_31 (.A(A31), .B(1'b0), .C_in(full_adder_30_c_out), .Sum(_31), .C_out(Carry));
  xor xor_1 (Overflow, Carry, full_adder_30_c_out);
endmodule

module addu (
  input  A0,
  input  B0,
  input  A1,
  input  B1,
  input  A2,
  input  B2,
  input  A3,
  input  B3,
  input  A4,
  input  B4,
  input  A5,
  input  B5,
  input  A6,
  input  B6,
  input  A7,
  input  B7,
  input  A8,
  input  B8,
  input  A9,
  input  B9,
  input  A10,
  input  B10,
  input  A11,
  input  B11,
  input  A12,
  input  B12,
  input  A13,
  input  B13,
  input  A14,
  input  B14,
  input  A15,
  input  B15,
  input  A16,
  input  B16,
  input  A17,
  input  B17,
  input  A18,
  input  B18,
  input  A19,
  input  B19,
  input  A20,
  input  B20,
  input  A21,
  input  B21,
  input  A22,
  input  B22,
  input  A23,
  input  B23,
  input  A24,
  input  B24,
  input  A25,
  input  B25,
  input  A26,
  input  B26,
  input  A27,
  input  B27,
  input  A28,
  input  B28,
  input  A29,
  input  B29,
  input  A30,
  input  B30,
  input  A31,
  input  B31,
  output _0,
  output _1,
  output _2,
  output _3,
  output _4,
  output _5,
  output _6,
  output _7,
  output _8,
  output _9,
  output _10,
  output _11,
  output _12,
  output _13,
  output _14,
  output _15,
  output _16,
  output _17,
  output _18,
  output _19,
  output _20,
  output _21,
  output _22,
  output _23,
  output _24,
  output _25,
  output _26,
  output _27,
  output _28,
  output _29,
  output _30,
  output _31,
  output Carry
);

  wire full_adder_1_c_out, full_adder_2_c_out, full_adder_3_c_out, full_adder_4_c_out, full_adder_5_c_out,
       full_adder_6_c_out, full_adder_7_c_out, full_adder_8_c_out, full_adder_9_c_out, full_adder_10_c_out,
       full_adder_11_c_out, full_adder_12_c_out, full_adder_13_c_out, full_adder_14_c_out,
       full_adder_15_c_out, full_adder_16_c_out, full_adder_17_c_out, full_adder_18_c_out,
       full_adder_19_c_out, full_adder_20_c_out, full_adder_21_c_out, full_adder_22_c_out,
       full_adder_23_c_out, full_adder_24_c_out, full_adder_25_c_out, full_adder_26_c_out,
       full_adder_27_c_out, full_adder_28_c_out, full_adder_29_c_out, full_adder_30_c_out, half_adder_1_carry;

  Half_Adder half_adder_1 (.A(A0), .B(B0), .Sum(_0), .Carry(half_adder_1_carry));
  Full_Adder full_adder_1 (.A(A1), .B(B1), .C_in(half_adder_1_carry), .Sum(_1), .C_out(full_adder_1_c_out));
  Full_Adder full_adder_2 (.A(A2), .B(B2), .C_in(full_adder_1_c_out), .Sum(_2), .C_out(full_adder_2_c_out));
  Full_Adder full_adder_3 (.A(A3), .B(B3), .C_in(full_adder_2_c_out), .Sum(_3), .C_out(full_adder_3_c_out));
  Full_Adder full_adder_4 (.A(A4), .B(B4), .C_in(full_adder_3_c_out), .Sum(_4), .C_out(full_adder_4_c_out));
  Full_Adder full_adder_5 (.A(A5), .B(B5), .C_in(full_adder_4_c_out), .Sum(_5), .C_out(full_adder_5_c_out));
  Full_Adder full_adder_6 (.A(A6), .B(B6), .C_in(full_adder_5_c_out), .Sum(_6), .C_out(full_adder_6_c_out));
  Full_Adder full_adder_7 (.A(A7), .B(B7), .C_in(full_adder_6_c_out), .Sum(_7), .C_out(full_adder_7_c_out));
  Full_Adder full_adder_8 (.A(A8), .B(B8), .C_in(full_adder_7_c_out), .Sum(_8), .C_out(full_adder_8_c_out));
  Full_Adder full_adder_9 (.A(A9), .B(B9), .C_in(full_adder_8_c_out), .Sum(_9), .C_out(full_adder_9_c_out));
  Full_Adder full_adder_10 (.A(A10), .B(B10), .C_in(full_adder_9_c_out), .Sum(_10), .C_out(full_adder_10_c_out));
  Full_Adder full_adder_11 (.A(A11), .B(B11), .C_in(full_adder_10_c_out), .Sum(_11), .C_out(full_adder_11_c_out));
  Full_Adder full_adder_12 (.A(A12), .B(B12), .C_in(full_adder_11_c_out), .Sum(_12), .C_out(full_adder_12_c_out));
  Full_Adder full_adder_13 (.A(A13), .B(B13), .C_in(full_adder_12_c_out), .Sum(_13), .C_out(full_adder_13_c_out));
  Full_Adder full_adder_14 (.A(A14), .B(B14), .C_in(full_adder_13_c_out), .Sum(_14), .C_out(full_adder_14_c_out));
  Full_Adder full_adder_15 (.A(A15), .B(B15), .C_in(full_adder_14_c_out), .Sum(_15), .C_out(full_adder_15_c_out));
  Full_Adder full_adder_16 (.A(A16), .B(B16), .C_in(full_adder_15_c_out), .Sum(_16), .C_out(full_adder_16_c_out));
  Full_Adder full_adder_17 (.A(A17), .B(B17), .C_in(full_adder_16_c_out), .Sum(_17), .C_out(full_adder_17_c_out));
  Full_Adder full_adder_18 (.A(A18), .B(B18), .C_in(full_adder_17_c_out), .Sum(_18), .C_out(full_adder_18_c_out));
  Full_Adder full_adder_19 (.A(A19), .B(B19), .C_in(full_adder_18_c_out), .Sum(_19), .C_out(full_adder_19_c_out));
  Full_Adder full_adder_20 (.A(A20), .B(B20), .C_in(full_adder_19_c_out), .Sum(_20), .C_out(full_adder_20_c_out));
  Full_Adder full_adder_21 (.A(A21), .B(B21), .C_in(full_adder_20_c_out), .Sum(_21), .C_out(full_adder_21_c_out));
  Full_Adder full_adder_22 (.A(A22), .B(B22), .C_in(full_adder_21_c_out), .Sum(_22), .C_out(full_adder_22_c_out));
  Full_Adder full_adder_23 (.A(A23), .B(B23), .C_in(full_adder_22_c_out), .Sum(_23), .C_out(full_adder_23_c_out));
  Full_Adder full_adder_24 (.A(A24), .B(B24), .C_in(full_adder_23_c_out), .Sum(_24), .C_out(full_adder_24_c_out));
  Full_Adder full_adder_25 (.A(A25), .B(B25), .C_in(full_adder_24_c_out), .Sum(_25), .C_out(full_adder_25_c_out));
  Full_Adder full_adder_26 (.A(A26), .B(B26), .C_in(full_adder_25_c_out), .Sum(_26), .C_out(full_adder_26_c_out));
  Full_Adder full_adder_27 (.A(A27), .B(B27), .C_in(full_adder_26_c_out), .Sum(_27), .C_out(full_adder_27_c_out));
  Full_Adder full_adder_28 (.A(A28), .B(B28), .C_in(full_adder_27_c_out), .Sum(_28), .C_out(full_adder_28_c_out));
  Full_Adder full_adder_29 (.A(A29), .B(B29), .C_in(full_adder_28_c_out), .Sum(_29), .C_out(full_adder_29_c_out));
  Full_Adder full_adder_30 (.A(A30), .B(B30), .C_in(full_adder_29_c_out), .Sum(_30), .C_out(full_adder_30_c_out));
  Full_Adder full_adder_31 (.A(A31), .B(B31), .C_in(full_adder_30_c_out), .Sum(_31), .C_out(Carry));
endmodule

module addiu (
  input  A0,
  input  B0,
  input  A1,
  input  B1,
  input  A2,
  input  B2,
  input  A3,
  input  B3,
  input  A4,
  input  B4,
  input  A5,
  input  B5,
  input  A6,
  input  B6,
  input  A7,
  input  B7,
  input  A8,
  input  B8,
  input  A9,
  input  B9,
  input  A10,
  input  B10,
  input  A11,
  input  B11,
  input  A12,
  input  B12,
  input  A13,
  input  B13,
  input  A14,
  input  B14,
  input  A15,
  input  B15,
  input  A16,
  input  A17,
  input  A18,
  input  A19,
  input  A20,
  input  A21,
  input  A22,
  input  A23,
  input  A24,
  input  A25,
  input  A26,
  input  A27,
  input  A28,
  input  A29,
  input  A30,
  input  A31,
  output _0,
  output _1,
  output _2,
  output _3,
  output _4,
  output _5,
  output _6,
  output _7,
  output _8,
  output _9,
  output _10,
  output _11,
  output _12,
  output _13,
  output _14,
  output _15,
  output _16,
  output _17,
  output _18,
  output _19,
  output _20,
  output _21,
  output _22,
  output _23,
  output _24,
  output _25,
  output _26,
  output _27,
  output _28,
  output _29,
  output _30,
  output _31,
  output Carry
);

  wire full_adder_1_c_out, full_adder_2_c_out, full_adder_3_c_out, full_adder_4_c_out, full_adder_5_c_out,
       full_adder_6_c_out, full_adder_7_c_out, full_adder_8_c_out, full_adder_9_c_out, full_adder_10_c_out,
       full_adder_11_c_out, full_adder_12_c_out, full_adder_13_c_out, full_adder_14_c_out,
       full_adder_15_c_out, full_adder_16_c_out, full_adder_17_c_out, full_adder_18_c_out,
       full_adder_19_c_out, full_adder_20_c_out, full_adder_21_c_out, full_adder_22_c_out,
       full_adder_23_c_out, full_adder_24_c_out, full_adder_25_c_out, full_adder_26_c_out,
       full_adder_27_c_out, full_adder_28_c_out, full_adder_29_c_out, full_adder_30_c_out, half_adder_1_carry;

  Half_Adder half_adder_1 (.A(A0), .B(B0), .Sum(_0), .Carry(half_adder_1_carry));
  Full_Adder full_adder_1 (.A(A1), .B(B1), .C_in(half_adder_1_carry), .Sum(_1), .C_out(full_adder_1_c_out));
  Full_Adder full_adder_2 (.A(A2), .B(B2), .C_in(full_adder_1_c_out), .Sum(_2), .C_out(full_adder_2_c_out));
  Full_Adder full_adder_3 (.A(A3), .B(B3), .C_in(full_adder_2_c_out), .Sum(_3), .C_out(full_adder_3_c_out));
  Full_Adder full_adder_4 (.A(A4), .B(B4), .C_in(full_adder_3_c_out), .Sum(_4), .C_out(full_adder_4_c_out));
  Full_Adder full_adder_5 (.A(A5), .B(B5), .C_in(full_adder_4_c_out), .Sum(_5), .C_out(full_adder_5_c_out));
  Full_Adder full_adder_6 (.A(A6), .B(B6), .C_in(full_adder_5_c_out), .Sum(_6), .C_out(full_adder_6_c_out));
  Full_Adder full_adder_7 (.A(A7), .B(B7), .C_in(full_adder_6_c_out), .Sum(_7), .C_out(full_adder_7_c_out));
  Full_Adder full_adder_8 (.A(A8), .B(B8), .C_in(full_adder_7_c_out), .Sum(_8), .C_out(full_adder_8_c_out));
  Full_Adder full_adder_9 (.A(A9), .B(B9), .C_in(full_adder_8_c_out), .Sum(_9), .C_out(full_adder_9_c_out));
  Full_Adder full_adder_10 (.A(A10), .B(B10), .C_in(full_adder_9_c_out), .Sum(_10), .C_out(full_adder_10_c_out));
  Full_Adder full_adder_11 (.A(A11), .B(B11), .C_in(full_adder_10_c_out), .Sum(_11), .C_out(full_adder_11_c_out));
  Full_Adder full_adder_12 (.A(A12), .B(B12), .C_in(full_adder_11_c_out), .Sum(_12), .C_out(full_adder_12_c_out));
  Full_Adder full_adder_13 (.A(A13), .B(B13), .C_in(full_adder_12_c_out), .Sum(_13), .C_out(full_adder_13_c_out));
  Full_Adder full_adder_14 (.A(A14), .B(B14), .C_in(full_adder_13_c_out), .Sum(_14), .C_out(full_adder_14_c_out));
  Full_Adder full_adder_15 (.A(A15), .B(B15), .C_in(full_adder_14_c_out), .Sum(_15), .C_out(full_adder_15_c_out));
  Full_Adder full_adder_16 (.A(A16), .B(1'b0), .C_in(full_adder_15_c_out), .Sum(_16), .C_out(full_adder_16_c_out));
  Full_Adder full_adder_17 (.A(A17), .B(1'b0), .C_in(full_adder_16_c_out), .Sum(_17), .C_out(full_adder_17_c_out));
  Full_Adder full_adder_18 (.A(A18), .B(1'b0), .C_in(full_adder_17_c_out), .Sum(_18), .C_out(full_adder_18_c_out));
  Full_Adder full_adder_19 (.A(A19), .B(1'b0), .C_in(full_adder_18_c_out), .Sum(_19), .C_out(full_adder_19_c_out));
  Full_Adder full_adder_20 (.A(A20), .B(1'b0), .C_in(full_adder_19_c_out), .Sum(_20), .C_out(full_adder_20_c_out));
  Full_Adder full_adder_21 (.A(A21), .B(1'b0), .C_in(full_adder_20_c_out), .Sum(_21), .C_out(full_adder_21_c_out));
  Full_Adder full_adder_22 (.A(A22), .B(1'b0), .C_in(full_adder_21_c_out), .Sum(_22), .C_out(full_adder_22_c_out));
  Full_Adder full_adder_23 (.A(A23), .B(1'b0), .C_in(full_adder_22_c_out), .Sum(_23), .C_out(full_adder_23_c_out));
  Full_Adder full_adder_24 (.A(A24), .B(1'b0), .C_in(full_adder_23_c_out), .Sum(_24), .C_out(full_adder_24_c_out));
  Full_Adder full_adder_25 (.A(A25), .B(1'b0), .C_in(full_adder_24_c_out), .Sum(_25), .C_out(full_adder_25_c_out));
  Full_Adder full_adder_26 (.A(A26), .B(1'b0), .C_in(full_adder_25_c_out), .Sum(_26), .C_out(full_adder_26_c_out));
  Full_Adder full_adder_27 (.A(A27), .B(1'b0), .C_in(full_adder_26_c_out), .Sum(_27), .C_out(full_adder_27_c_out));
  Full_Adder full_adder_28 (.A(A28), .B(1'b0), .C_in(full_adder_27_c_out), .Sum(_28), .C_out(full_adder_28_c_out));
  Full_Adder full_adder_29 (.A(A29), .B(1'b0), .C_in(full_adder_28_c_out), .Sum(_29), .C_out(full_adder_29_c_out));
  Full_Adder full_adder_30 (.A(A30), .B(1'b0), .C_in(full_adder_29_c_out), .Sum(_30), .C_out(full_adder_30_c_out));
  Full_Adder full_adder_31 (.A(A31), .B(1'b0), .C_in(full_adder_30_c_out), .Sum(_31), .C_out(Carry));
endmodule

module sub (
  input  A0,
  input  B0,
  input  A1,
  input  B1,
  input  A2,
  input  B2,
  input  A3,
  input  B3,
  input  A4,
  input  B4,
  input  A5,
  input  B5,
  input  A6,
  input  B6,
  input  A7,
  input  B7,
  input  A8,
  input  B8,
  input  A9,
  input  B9,
  input  A10,
  input  B10,
  input  A11,
  input  B11,
  input  A12,
  input  B12,
  input  A13,
  input  B13,
  input  A14,
  input  B14,
  input  A15,
  input  B15,
  input  A16,
  input  B16,
  input  A17,
  input  B17,
  input  A18,
  input  B18,
  input  A19,
  input  B19,
  input  A20,
  input  B20,
  input  A21,
  input  B21,
  input  A22,
  input  B22,
  input  A23,
  input  B23,
  input  A24,
  input  B24,
  input  A25,
  input  B25,
  input  A26,
  input  B26,
  input  A27,
  input  B27,
  input  A28,
  input  B28,
  input  A29,
  input  B29,
  input  A30,
  input  B30,
  input  A31,
  input  B31,
  output _0,
  output _1,
  output _2,
  output _3,
  output _4,
  output _5,
  output _6,
  output _7,
  output _8,
  output _9,
  output _10,
  output _11,
  output _12,
  output _13,
  output _14,
  output _15,
  output _16,
  output _17,
  output _18,
  output _19,
  output _20,
  output _21,
  output _22,
  output _23,
  output _24,
  output _25,
  output _26,
  output _27,
  output _28,
  output _29,
  output _30,
  output _31,
  output Overflow
);

  wire full_adder_1_c_out, full_adder_2_c_out, full_adder_3_c_out, full_adder_4_c_out, full_adder_5_c_out,
       full_adder_6_c_out, full_adder_7_c_out, full_adder_8_c_out, full_adder_9_c_out, full_adder_10_c_out,
       full_adder_11_c_out, full_adder_12_c_out, full_adder_13_c_out, full_adder_14_c_out,
       full_adder_15_c_out, full_adder_16_c_out, full_adder_17_c_out, full_adder_18_c_out,
       full_adder_19_c_out, full_adder_20_c_out, full_adder_21_c_out, full_adder_22_c_out,
       full_adder_23_c_out, full_adder_24_c_out, full_adder_25_c_out, full_adder_26_c_out,
       full_adder_27_c_out, full_adder_28_c_out, full_adder_29_c_out, full_adder_30_c_out,
       full_adder_31_c_out, full_adder_32_c_out, not_1_out, not_2_out, not_3_out, not_4_out, not_5_out,
       not_6_out, not_7_out, not_8_out, not_9_out, not_10_out, not_11_out, not_12_out, not_13_out,
       not_14_out, not_15_out, not_16_out, not_17_out, not_18_out, not_19_out, not_20_out, not_21_out,
       not_22_out, not_23_out, not_24_out, not_25_out, not_26_out, not_27_out, not_28_out, not_29_out,
       not_30_out, not_31_out, not_32_out;

  Full_Adder full_adder_1 (.A(A0), .B(not_1_out), .C_in(1'b1), .Sum(_0), .C_out(full_adder_1_c_out));
  not not_1 (not_1_out, B0);
  not not_2 (not_2_out, B1);
  Full_Adder full_adder_2 (.A(A1), .B(not_2_out), .C_in(full_adder_1_c_out), .Sum(_1), .C_out(full_adder_2_c_out));
  Full_Adder full_adder_3 (.A(A2), .B(not_3_out), .C_in(full_adder_2_c_out), .Sum(_2), .C_out(full_adder_3_c_out));
  not not_3 (not_3_out, B2);
  Full_Adder full_adder_4 (.A(A3), .B(not_4_out), .C_in(full_adder_3_c_out), .Sum(_3), .C_out(full_adder_4_c_out));
  not not_4 (not_4_out, B3);
  Full_Adder full_adder_5 (.A(A4), .B(not_5_out), .C_in(full_adder_4_c_out), .Sum(_4), .C_out(full_adder_5_c_out));
  not not_5 (not_5_out, B4);
  Full_Adder full_adder_6 (.A(A5), .B(not_6_out), .C_in(full_adder_5_c_out), .Sum(_5), .C_out(full_adder_6_c_out));
  not not_6 (not_6_out, B5);
  Full_Adder full_adder_7 (.A(A6), .B(not_7_out), .C_in(full_adder_6_c_out), .Sum(_6), .C_out(full_adder_7_c_out));
  not not_7 (not_7_out, B6);
  Full_Adder full_adder_8 (.A(A7), .B(not_8_out), .C_in(full_adder_7_c_out), .Sum(_7), .C_out(full_adder_8_c_out));
  not not_8 (not_8_out, B7);
  Full_Adder full_adder_9 (.A(A8), .B(not_9_out), .C_in(full_adder_8_c_out), .Sum(_8), .C_out(full_adder_9_c_out));
  not not_9 (not_9_out, B8);
  not not_10 (not_10_out, B9);
  Full_Adder full_adder_10 (.A(A9), .B(not_10_out), .C_in(full_adder_9_c_out), .Sum(_9), .C_out(full_adder_10_c_out));
  Full_Adder full_adder_11 (
    .A(A10), .B(not_11_out), .C_in(full_adder_10_c_out), .Sum(_10), .C_out(full_adder_11_c_out));
  not not_11 (not_11_out, B10);
  Full_Adder full_adder_12 (
    .A(A11), .B(not_12_out), .C_in(full_adder_11_c_out), .Sum(_11), .C_out(full_adder_12_c_out));
  not not_12 (not_12_out, B11);
  Full_Adder full_adder_13 (
    .A(A12), .B(not_13_out), .C_in(full_adder_12_c_out), .Sum(_12), .C_out(full_adder_13_c_out));
  not not_13 (not_13_out, B12);
  Full_Adder full_adder_14 (
    .A(A13), .B(not_14_out), .C_in(full_adder_13_c_out), .Sum(_13), .C_out(full_adder_14_c_out));
  not not_14 (not_14_out, B13);
  Full_Adder full_adder_15 (
    .A(A14), .B(not_15_out), .C_in(full_adder_14_c_out), .Sum(_14), .C_out(full_adder_15_c_out));
  not not_15 (not_15_out, B14);
  Full_Adder full_adder_16 (
    .A(A15), .B(not_16_out), .C_in(full_adder_15_c_out), .Sum(_15), .C_out(full_adder_16_c_out));
  not not_16 (not_16_out, B15);
  Full_Adder full_adder_17 (
    .A(A16), .B(not_17_out), .C_in(full_adder_16_c_out), .Sum(_16), .C_out(full_adder_17_c_out));
  not not_17 (not_17_out, B16);
  not not_18 (not_18_out, B17);
  Full_Adder full_adder_18 (
    .A(A17), .B(not_18_out), .C_in(full_adder_17_c_out), .Sum(_17), .C_out(full_adder_18_c_out));
  Full_Adder full_adder_19 (
    .A(A18), .B(not_19_out), .C_in(full_adder_18_c_out), .Sum(_18), .C_out(full_adder_19_c_out));
  not not_19 (not_19_out, B18);
  Full_Adder full_adder_20 (
    .A(A19), .B(not_20_out), .C_in(full_adder_19_c_out), .Sum(_19), .C_out(full_adder_20_c_out));
  not not_20 (not_20_out, B19);
  Full_Adder full_adder_21 (
    .A(A20), .B(not_21_out), .C_in(full_adder_20_c_out), .Sum(_20), .C_out(full_adder_21_c_out));
  not not_21 (not_21_out, B20);
  Full_Adder full_adder_22 (
    .A(A21), .B(not_22_out), .C_in(full_adder_21_c_out), .Sum(_21), .C_out(full_adder_22_c_out));
  not not_22 (not_22_out, B21);
  Full_Adder full_adder_23 (
    .A(A22), .B(not_23_out), .C_in(full_adder_22_c_out), .Sum(_22), .C_out(full_adder_23_c_out));
  not not_23 (not_23_out, B22);
  Full_Adder full_adder_24 (
    .A(A23), .B(not_24_out), .C_in(full_adder_23_c_out), .Sum(_23), .C_out(full_adder_24_c_out));
  not not_24 (not_24_out, B23);
  Full_Adder full_adder_25 (
    .A(A24), .B(not_25_out), .C_in(full_adder_24_c_out), .Sum(_24), .C_out(full_adder_25_c_out));
  not not_25 (not_25_out, B24);
  not not_26 (not_26_out, B25);
  Full_Adder full_adder_26 (
    .A(A25), .B(not_26_out), .C_in(full_adder_25_c_out), .Sum(_25), .C_out(full_adder_26_c_out));
  Full_Adder full_adder_27 (
    .A(A26), .B(not_27_out), .C_in(full_adder_26_c_out), .Sum(_26), .C_out(full_adder_27_c_out));
  not not_27 (not_27_out, B26);
  Full_Adder full_adder_28 (
    .A(A27), .B(not_28_out), .C_in(full_adder_27_c_out), .Sum(_27), .C_out(full_adder_28_c_out));
  not not_28 (not_28_out, B27);
  Full_Adder full_adder_29 (
    .A(A28), .B(not_29_out), .C_in(full_adder_28_c_out), .Sum(_28), .C_out(full_adder_29_c_out));
  not not_29 (not_29_out, B28);
  Full_Adder full_adder_30 (
    .A(A29), .B(not_30_out), .C_in(full_adder_29_c_out), .Sum(_29), .C_out(full_adder_30_c_out));
  not not_30 (not_30_out, B29);
  Full_Adder full_adder_31 (
    .A(A30), .B(not_31_out), .C_in(full_adder_30_c_out), .Sum(_30), .C_out(full_adder_31_c_out));
  not not_31 (not_31_out, B30);
  Full_Adder full_adder_32 (
    .A(A31), .B(not_32_out), .C_in(full_adder_31_c_out), .Sum(_31), .C_out(full_adder_32_c_out));
  not not_32 (not_32_out, B31);
  xor xor_1 (Overflow, full_adder_32_c_out, full_adder_31_c_out);
endmodule

module subu (
  input  A0,
  input  B0,
  input  A1,
  input  B1,
  input  A2,
  input  B2,
  input  A3,
  input  B3,
  input  A4,
  input  B4,
  input  A5,
  input  B5,
  input  A6,
  input  B6,
  input  A7,
  input  B7,
  input  A8,
  input  B8,
  input  A9,
  input  B9,
  input  A10,
  input  B10,
  input  A11,
  input  B11,
  input  A12,
  input  B12,
  input  A13,
  input  B13,
  input  A14,
  input  B14,
  input  A15,
  input  B15,
  input  A16,
  input  B16,
  input  A17,
  input  B17,
  input  A18,
  input  B18,
  input  A19,
  input  B19,
  input  A20,
  input  B20,
  input  A21,
  input  B21,
  input  A22,
  input  B22,
  input  A23,
  input  B23,
  input  A24,
  input  B24,
  input  A25,
  input  B25,
  input  A26,
  input  B26,
  input  A27,
  input  B27,
  input  A28,
  input  B28,
  input  A29,
  input  B29,
  input  A30,
  input  B30,
  input  A31,
  input  B31,
  output _0,
  output _1,
  output _2,
  output _3,
  output _4,
  output _5,
  output _6,
  output _7,
  output _8,
  output _9,
  output _10,
  output _11,
  output _12,
  output _13,
  output _14,
  output _15,
  output _16,
  output _17,
  output _18,
  output _19,
  output _20,
  output _21,
  output _22,
  output _23,
  output _24,
  output _25,
  output _26,
  output _27,
  output _28,
  output _29,
  output _30,
  output _31
);

  wire full_adder_1_c_out, full_adder_2_c_out, full_adder_3_c_out, full_adder_4_c_out, full_adder_5_c_out,
       full_adder_6_c_out, full_adder_7_c_out, full_adder_8_c_out, full_adder_9_c_out, full_adder_10_c_out,
       full_adder_11_c_out, full_adder_12_c_out, full_adder_13_c_out, full_adder_14_c_out,
       full_adder_15_c_out, full_adder_16_c_out, full_adder_17_c_out, full_adder_18_c_out,
       full_adder_19_c_out, full_adder_20_c_out, full_adder_21_c_out, full_adder_22_c_out,
       full_adder_23_c_out, full_adder_24_c_out, full_adder_25_c_out, full_adder_26_c_out,
       full_adder_27_c_out, full_adder_28_c_out, full_adder_29_c_out, full_adder_30_c_out,
       full_adder_31_c_out, not_1_out, not_2_out, not_3_out, not_4_out, not_5_out, not_6_out, not_7_out,
       not_8_out, not_9_out, not_10_out, not_11_out, not_12_out, not_13_out, not_14_out, not_15_out,
       not_16_out, not_17_out, not_18_out, not_19_out, not_20_out, not_21_out, not_22_out, not_23_out,
       not_24_out, not_25_out, not_26_out, not_27_out, not_28_out, not_29_out, not_30_out, not_31_out,
       not_32_out;

  Full_Adder full_adder_1 (.A(A0), .B(not_1_out), .C_in(1'b1), .Sum(_0), .C_out(full_adder_1_c_out));
  not not_1 (not_1_out, B0);
  not not_2 (not_2_out, B1);
  Full_Adder full_adder_2 (.A(A1), .B(not_2_out), .C_in(full_adder_1_c_out), .Sum(_1), .C_out(full_adder_2_c_out));
  Full_Adder full_adder_3 (.A(A2), .B(not_3_out), .C_in(full_adder_2_c_out), .Sum(_2), .C_out(full_adder_3_c_out));
  not not_3 (not_3_out, B2);
  Full_Adder full_adder_4 (.A(A3), .B(not_4_out), .C_in(full_adder_3_c_out), .Sum(_3), .C_out(full_adder_4_c_out));
  not not_4 (not_4_out, B3);
  Full_Adder full_adder_5 (.A(A4), .B(not_5_out), .C_in(full_adder_4_c_out), .Sum(_4), .C_out(full_adder_5_c_out));
  not not_5 (not_5_out, B4);
  Full_Adder full_adder_6 (.A(A5), .B(not_6_out), .C_in(full_adder_5_c_out), .Sum(_5), .C_out(full_adder_6_c_out));
  not not_6 (not_6_out, B5);
  Full_Adder full_adder_7 (.A(A6), .B(not_7_out), .C_in(full_adder_6_c_out), .Sum(_6), .C_out(full_adder_7_c_out));
  not not_7 (not_7_out, B6);
  Full_Adder full_adder_8 (.A(A7), .B(not_8_out), .C_in(full_adder_7_c_out), .Sum(_7), .C_out(full_adder_8_c_out));
  not not_8 (not_8_out, B7);
  Full_Adder full_adder_9 (.A(A8), .B(not_9_out), .C_in(full_adder_8_c_out), .Sum(_8), .C_out(full_adder_9_c_out));
  not not_9 (not_9_out, B8);
  not not_10 (not_10_out, B9);
  Full_Adder full_adder_10 (.A(A9), .B(not_10_out), .C_in(full_adder_9_c_out), .Sum(_9), .C_out(full_adder_10_c_out));
  Full_Adder full_adder_11 (
    .A(A10), .B(not_11_out), .C_in(full_adder_10_c_out), .Sum(_10), .C_out(full_adder_11_c_out));
  not not_11 (not_11_out, B10);
  Full_Adder full_adder_12 (
    .A(A11), .B(not_12_out), .C_in(full_adder_11_c_out), .Sum(_11), .C_out(full_adder_12_c_out));
  not not_12 (not_12_out, B11);
  Full_Adder full_adder_13 (
    .A(A12), .B(not_13_out), .C_in(full_adder_12_c_out), .Sum(_12), .C_out(full_adder_13_c_out));
  not not_13 (not_13_out, B12);
  Full_Adder full_adder_14 (
    .A(A13), .B(not_14_out), .C_in(full_adder_13_c_out), .Sum(_13), .C_out(full_adder_14_c_out));
  not not_14 (not_14_out, B13);
  Full_Adder full_adder_15 (
    .A(A14), .B(not_15_out), .C_in(full_adder_14_c_out), .Sum(_14), .C_out(full_adder_15_c_out));
  not not_15 (not_15_out, B14);
  Full_Adder full_adder_16 (
    .A(A15), .B(not_16_out), .C_in(full_adder_15_c_out), .Sum(_15), .C_out(full_adder_16_c_out));
  not not_16 (not_16_out, B15);
  Full_Adder full_adder_17 (
    .A(A16), .B(not_17_out), .C_in(full_adder_16_c_out), .Sum(_16), .C_out(full_adder_17_c_out));
  not not_17 (not_17_out, B16);
  not not_18 (not_18_out, B17);
  Full_Adder full_adder_18 (
    .A(A17), .B(not_18_out), .C_in(full_adder_17_c_out), .Sum(_17), .C_out(full_adder_18_c_out));
  Full_Adder full_adder_19 (
    .A(A18), .B(not_19_out), .C_in(full_adder_18_c_out), .Sum(_18), .C_out(full_adder_19_c_out));
  not not_19 (not_19_out, B18);
  Full_Adder full_adder_20 (
    .A(A19), .B(not_20_out), .C_in(full_adder_19_c_out), .Sum(_19), .C_out(full_adder_20_c_out));
  not not_20 (not_20_out, B19);
  Full_Adder full_adder_21 (
    .A(A20), .B(not_21_out), .C_in(full_adder_20_c_out), .Sum(_20), .C_out(full_adder_21_c_out));
  not not_21 (not_21_out, B20);
  Full_Adder full_adder_22 (
    .A(A21), .B(not_22_out), .C_in(full_adder_21_c_out), .Sum(_21), .C_out(full_adder_22_c_out));
  not not_22 (not_22_out, B21);
  Full_Adder full_adder_23 (
    .A(A22), .B(not_23_out), .C_in(full_adder_22_c_out), .Sum(_22), .C_out(full_adder_23_c_out));
  not not_23 (not_23_out, B22);
  Full_Adder full_adder_24 (
    .A(A23), .B(not_24_out), .C_in(full_adder_23_c_out), .Sum(_23), .C_out(full_adder_24_c_out));
  not not_24 (not_24_out, B23);
  Full_Adder full_adder_25 (
    .A(A24), .B(not_25_out), .C_in(full_adder_24_c_out), .Sum(_24), .C_out(full_adder_25_c_out));
  not not_25 (not_25_out, B24);
  not not_26 (not_26_out, B25);
  Full_Adder full_adder_26 (
    .A(A25), .B(not_26_out), .C_in(full_adder_25_c_out), .Sum(_25), .C_out(full_adder_26_c_out));
  Full_Adder full_adder_27 (
    .A(A26), .B(not_27_out), .C_in(full_adder_26_c_out), .Sum(_26), .C_out(full_adder_27_c_out));
  not not_27 (not_27_out, B26);
  Full_Adder full_adder_28 (
    .A(A27), .B(not_28_out), .C_in(full_adder_27_c_out), .Sum(_27), .C_out(full_adder_28_c_out));
  not not_28 (not_28_out, B27);
  Full_Adder full_adder_29 (
    .A(A28), .B(not_29_out), .C_in(full_adder_28_c_out), .Sum(_28), .C_out(full_adder_29_c_out));
  not not_29 (not_29_out, B28);
  Full_Adder full_adder_30 (
    .A(A29), .B(not_30_out), .C_in(full_adder_29_c_out), .Sum(_29), .C_out(full_adder_30_c_out));
  not not_30 (not_30_out, B29);
  Full_Adder full_adder_31 (
    .A(A30), .B(not_31_out), .C_in(full_adder_30_c_out), .Sum(_30), .C_out(full_adder_31_c_out));
  not not_31 (not_31_out, B30);
  Full_Adder full_adder_32 (.A(A31), .B(not_32_out), .C_in(full_adder_31_c_out), .Sum(_31));  // open: C_out
  not not_32 (not_32_out, B31);
endmodule

module \and  (
  input  A0,
  input  B0,
  input  A1,
  input  B1,
  input  A2,
  input  B2,
  input  A3,
  input  B3,
  input  A4,
  input  B4,
  input  A5,
  input  B5,
  input  A6,
  input  B6,
  input  A7,
  input  B7,
  input  A8,
  input  B8,
  input  A9,
  input  B9,
  input  A10,
  input  B10,
  input  A11,
  input  B11,
  input  A12,
  input  B12,
  input  A13,
  input  B13,
  input  A14,
  input  B14,
  input  A15,
  input  B15,
  input  A16,
  input  B16,
  input  A17,
  input  B17,
  input  A18,
  input  B18,
  input  A19,
  input  B19,
  input  A20,
  input  B20,
  input  A21,
  input  B21,
  input  A22,
  input  B22,
  input  A23,
  input  B23,
  input  A24,
  input  B24,
  input  A25,
  input  B25,
  input  A26,
  input  B26,
  input  A27,
  input  B27,
  input  A28,
  input  B28,
  input  A29,
  input  B29,
  input  A30,
  input  B30,
  input  A31,
  input  B31,
  output _0,
  output _1,
  output _2,
  output _3,
  output _4,
  output _5,
  output _6,
  output _7,
  output _8,
  output _9,
  output _10,
  output _11,
  output _12,
  output _13,
  output _14,
  output _15,
  output _16,
  output _17,
  output _18,
  output _19,
  output _20,
  output _21,
  output _22,
  output _23,
  output _24,
  output _25,
  output _26,
  output _27,
  output _28,
  output _29,
  output _30,
  output _31
);

  and and_1 (_0, A0, B0);
  and and_2 (_1, A1, B1);
  and and_3 (_2, A2, B2);
  and and_4 (_3, A3, B3);
  and and_5 (_4, A4, B4);
  and and_6 (_5, A5, B5);
  and and_7 (_6, A6, B6);
  and and_8 (_7, A7, B7);
  and and_9 (_8, A8, B8);
  and and_10 (_9, A9, B9);
  and and_11 (_10, A10, B10);
  and and_12 (_11, A11, B11);
  and and_13 (_12, A12, B12);
  and and_14 (_13, A13, B13);
  and and_15 (_14, A14, B14);
  and and_16 (_15, A15, B15);
  and and_17 (_16, A16, B16);
  and and_18 (_17, A17, B17);
  and and_19 (_18, A18, B18);
  and and_20 (_19, A19, B19);
  and and_21 (_20, A20, B20);
  and and_22 (_21, A21, B21);
  and and_23 (_22, A22, B22);
  and and_24 (_23, A23, B23);
  and and_25 (_24, A24, B24);
  and and_26 (_25, A25, B25);
  and and_27 (_26, A26, B26);
  and and_28 (_27, A27, B27);
  and and_29 (_28, A28, B28);
  and and_30 (_29, A29, B29);
  and and_31 (_30, A30, B30);
  and and_32 (_31, A31, B31);
endmodule

module andi (
  input  A0,
  input  B0,
  input  A1,
  input  B1,
  input  A2,
  input  B2,
  input  A3,
  input  B3,
  input  A4,
  input  B4,
  input  A5,
  input  B5,
  input  A6,
  input  B6,
  input  A7,
  input  B7,
  input  A8,
  input  B8,
  input  A9,
  input  B9,
  input  A10,
  input  B10,
  input  A11,
  input  B11,
  input  A12,
  input  B12,
  input  A13,
  input  B13,
  input  A14,
  input  B14,
  input  A15,
  input  B15,
  output _0,
  output _1,
  output _2,
  output _3,
  output _4,
  output _5,
  output _6,
  output _7,
  output _8,
  output _9,
  output _10,
  output _11,
  output _12,
  output _13,
  output _14,
  output _15
);

  and and_1 (_0, A0, B0);
  and and_2 (_1, A1, B1);
  and and_3 (_2, A2, B2);
  and and_4 (_3, A3, B3);
  and and_5 (_4, A4, B4);
  and and_6 (_5, A5, B5);
  and and_7 (_6, A6, B6);
  and and_8 (_7, A7, B7);
  and and_9 (_8, A8, B8);
  and and_10 (_9, A9, B9);
  and and_11 (_10, A10, B10);
  and and_12 (_11, A11, B11);
  and and_13 (_12, A12, B12);
  and and_14 (_13, A13, B13);
  and and_15 (_14, A14, B14);
  and and_16 (_15, A15, B15);
endmodule

module \nand  (
  input  A0,
  input  B0,
  input  A1,
  input  B1,
  input  A2,
  input  B2,
  input  A3,
  input  B3,
  input  A4,
  input  B4,
  input  A5,
  input  B5,
  input  A6,
  input  B6,
  input  A7,
  input  B7,
  input  A8,
  input  B8,
  input  A9,
  input  B9,
  input  A10,
  input  B10,
  input  A11,
  input  B11,
  input  A12,
  input  B12,
  input  A13,
  input  B13,
  input  A14,
  input  B14,
  input  A15,
  input  B15,
  input  A16,
  input  B16,
  input  A17,
  input  B17,
  input  A18,
  input  B18,
  input  A19,
  input  B19,
  input  A20,
  input  B20,
  input  A21,
  input  B21,
  input  A22,
  input  B22,
  input  A23,
  input  B23,
  input  A24,
  input  B24,
  input  A25,
  input  B25,
  input  A26,
  input  B26,
  input  A27,
  input  B27,
  input  A28,
  input  B28,
  input  A29,
  input  B29,
  input  A30,
  input  B30,
  input  A31,
  input  B31,
  output _0,
  output _1,
  output _2,
  output _3,
  output _4,
  output _5,
  output _6,
  output _7,
  output _8,
  output _9,
  output _10,
  output _11,
  output _12,
  output _13,
  output _14,
  output _15,
  output _16,
  output _17,
  output _18,
  output _19,
  output _20,
  output _21,
  output _22,
  output _23,
  output _24,
  output _25,
  output _26,
  output _27,
  output _28,
  output _29,
  output _30,
  output _31
);

  nand nand_1 (_0, A0, B0);
  nand nand_2 (_1, A1, B1);
  nand nand_3 (_2, A2, B2);
  nand nand_4 (_3, A3, B3);
  nand nand_5 (_4, A4, B4);
  nand nand_6 (_5, A5, B5);
  nand nand_7 (_6, A6, B6);
  nand nand_8 (_7, A7, B7);
  nand nand_9 (_8, A8, B8);
  nand nand_10 (_9, A9, B9);
  nand nand_11 (_10, A10, B10);
  nand nand_12 (_11, A11, B11);
  nand nand_13 (_12, A12, B12);
  nand nand_14 (_13, A13, B13);
  nand nand_15 (_14, A14, B14);
  nand nand_16 (_15, A15, B15);
  nand nand_17 (_16, A16, B16);
  nand nand_18 (_17, A17, B17);
  nand nand_19 (_18, A18, B18);
  nand nand_20 (_19, A19, B19);
  nand nand_21 (_20, A20, B20);
  nand nand_22 (_21, A21, B21);
  nand nand_23 (_22, A22, B22);
  nand nand_24 (_23, A23, B23);
  nand nand_25 (_24, A24, B24);
  nand nand_26 (_25, A25, B25);
  nand nand_27 (_26, A26, B26);
  nand nand_28 (_27, A27, B27);
  nand nand_29 (_28, A28, B28);
  nand nand_30 (_29, A29, B29);
  nand nand_31 (_30, A30, B30);
  nand nand_32 (_31, A31, B31);
endmodule

module nandi (
  input  A0,
  input  B0,
  input  A1,
  input  B1,
  input  A2,
  input  B2,
  input  A3,
  input  B3,
  input  A4,
  input  B4,
  input  A5,
  input  B5,
  input  A6,
  input  B6,
  input  A7,
  input  B7,
  input  A8,
  input  B8,
  input  A9,
  input  B9,
  input  A10,
  input  B10,
  input  A11,
  input  B11,
  input  A12,
  input  B12,
  input  A13,
  input  B13,
  input  A14,
  input  B14,
  input  A15,
  input  B15,
  output _0,
  output _1,
  output _2,
  output _3,
  output _4,
  output _5,
  output _6,
  output _7,
  output _8,
  output _9,
  output _10,
  output _11,
  output _12,
  output _13,
  output _14,
  output _15,
  output _16,
  output _17,
  output _18,
  output _19,
  output _20,
  output _21,
  output _22,
  output _23,
  output _24,
  output _25,
  output _26,
  output _27,
  output _28,
  output _29,
  output _30,
  output _31
);

  nand nand_1 (_0, A0, B0);
  nand nand_2 (_1, A1, B1);
  nand nand_3 (_2, A2, B2);
  nand nand_4 (_3, A3, B3);
  nand nand_5 (_4, A4, B4);
  nand nand_6 (_5, A5, B5);
  nand nand_7 (_6, A6, B6);
  nand nand_8 (_7, A7, B7);
  nand nand_9 (_8, A8, B8);
  nand nand_10 (_9, A9, B9);
  nand nand_11 (_10, A10, B10);
  nand nand_12 (_11, A11, B11);
  nand nand_13 (_12, A12, B12);
  nand nand_14 (_13, A13, B13);
  nand nand_15 (_14, A14, B14);
  nand nand_16 (_15, A15, B15);

  assign _16 = 1'b1;
  assign _17 = 1'b1;
  assign _18 = 1'b1;
  assign _19 = 1'b1;
  assign _20 = 1'b1;
  assign _21 = 1'b1;
  assign _22 = 1'b1;
  assign _23 = 1'b1;
  assign _24 = 1'b1;
  assign _25 = 1'b1;
  assign _26 = 1'b1;
  assign _27 = 1'b1;
  assign _28 = 1'b1;
  assign _29 = 1'b1;
  assign _30 = 1'b1;
  assign _31 = 1'b1;
endmodule

module \or  (
  input  A0,
  input  B0,
  input  A1,
  input  B1,
  input  A2,
  input  B2,
  input  A3,
  input  B3,
  input  A4,
  input  B4,
  input  A5,
  input  B5,
  input  A6,
  input  B6,
  input  A7,
  input  B7,
  input  A8,
  input  B8,
  input  A9,
  input  B9,
  input  A10,
  input  B10,
  input  A11,
  input  B11,
  input  A12,
  input  B12,
  input  A13,
  input  B13,
  input  A14,
  input  B14,
  input  A15,
  input  B15,
  input  A16,
  input  B16,
  input  A17,
  input  B17,
  input  A18,
  input  B18,
  input  A19,
  input  B19,
  input  A20,
  input  B20,
  input  A21,
  input  B21,
  input  A22,
  input  B22,
  input  A23,
  input  B23,
  input  A24,
  input  B24,
  input  A25,
  input  B25,
  input  A26,
  input  B26,
  input  A27,
  input  B27,
  input  A28,
  input  B28,
  input  A29,
  input  B29,
  input  A30,
  input  B30,
  input  A31,
  input  B31,
  output _0,
  output _1,
  output _2,
  output _3,
  output _4,
  output _5,
  output _6,
  output _7,
  output _8,
  output _9,
  output _10,
  output _11,
  output _12,
  output _13,
  output _14,
  output _15,
  output _16,
  output _17,
  output _18,
  output _19,
  output _20,
  output _21,
  output _22,
  output _23,
  output _24,
  output _25,
  output _26,
  output _27,
  output _28,
  output _29,
  output _30,
  output _31
);

  or or_1 (_0, A0, B0);
  or or_2 (_1, A1, B1);
  or or_3 (_2, A2, B2);
  or or_4 (_3, A3, B3);
  or or_5 (_4, A4, B4);
  or or_6 (_5, A5, B5);
  or or_7 (_6, A6, B6);
  or or_8 (_7, A7, B7);
  or or_9 (_8, A8, B8);
  or or_10 (_9, A9, B9);
  or or_11 (_10, A10, B10);
  or or_12 (_11, A11, B11);
  or or_13 (_12, A12, B12);
  or or_14 (_13, A13, B13);
  or or_15 (_14, A14, B14);
  or or_16 (_15, A15, B15);
  or or_17 (_16, A16, B16);
  or or_18 (_17, A17, B17);
  or or_19 (_18, A18, B18);
  or or_20 (_19, A19, B19);
  or or_21 (_20, A20, B20);
  or or_22 (_21, A21, B21);
  or or_23 (_22, A22, B22);
  or or_24 (_23, A23, B23);
  or or_25 (_24, A24, B24);
  or or_26 (_25, A25, B25);
  or or_27 (_26, A26, B26);
  or or_28 (_27, A27, B27);
  or or_29 (_28, A28, B28);
  or or_30 (_29, A29, B29);
  or or_31 (_30, A30, B30);
  or or_32 (_31, A31, B31);
endmodule

module ori (
  input  A0,
  input  B0,
  input  A1,
  input  B1,
  input  A2,
  input  B2,
  input  A3,
  input  B3,
  input  A4,
  input  B4,
  input  A5,
  input  B5,
  input  A6,
  input  B6,
  input  A7,
  input  B7,
  input  A8,
  input  B8,
  input  A9,
  input  B9,
  input  A10,
  input  B10,
  input  A11,
  input  B11,
  input  A12,
  input  B12,
  input  A13,
  input  B13,
  input  A14,
  input  B14,
  input  A15,
  input  B15,
  input  A16,
  input  A17,
  input  A18,
  input  A19,
  input  A20,
  input  A21,
  input  A22,
  input  A23,
  input  A24,
  input  A25,
  input  A26,
  input  A27,
  input  A28,
  input  A29,
  input  A30,
  input  A31,
  output _0,
  output _1,
  output _2,
  output _3,
  output _4,
  output _5,
  output _6,
  output _7,
  output _8,
  output _9,
  output _10,
  output _11,
  output _12,
  output _13,
  output _14,
  output _15,
  output _16,
  output _17,
  output _18,
  output _19,
  output _20,
  output _21,
  output _22,
  output _23,
  output _24,
  output _25,
  output _26,
  output _27,
  output _28,
  output _29,
  output _30,
  output _31
);

  or or_1 (_0, A0, B0);
  or or_2 (_1, A1, B1);
  or or_3 (_2, A2, B2);
  or or_4 (_3, A3, B3);
  or or_5 (_4, A4, B4);
  or or_6 (_5, A5, B5);
  or or_7 (_6, A6, B6);
  or or_8 (_7, A7, B7);
  or or_9 (_8, A8, B8);
  or or_10 (_9, A9, B9);
  or or_11 (_10, A10, B10);
  or or_12 (_11, A11, B11);
  or or_13 (_12, A12, B12);
  or or_14 (_13, A13, B13);
  or or_15 (_14, A14, B14);
  or or_16 (_15, A15, B15);

  assign _16 = A16;
  assign _17 = A17;
  assign _18 = A18;
  assign _19 = A19;
  assign _20 = A20;
  assign _21 = A21;
  assign _22 = A22;
  assign _23 = A23;
  assign _24 = A24;
  assign _25 = A25;
  assign _26 = A26;
  assign _27 = A27;
  assign _28 = A28;
  assign _29 = A29;
  assign _30 = A30;
  assign _31 = A31;
endmodule

module \nor  (
  input  A0,
  input  B0,
  input  A1,
  input  B1,
  input  A2,
  input  B2,
  input  A3,
  input  B3,
  input  A4,
  input  B4,
  input  A5,
  input  B5,
  input  A6,
  input  B6,
  input  A7,
  input  B7,
  input  A8,
  input  B8,
  input  A9,
  input  B9,
  input  A10,
  input  B10,
  input  A11,
  input  B11,
  input  A12,
  input  B12,
  input  A13,
  input  B13,
  input  A14,
  input  B14,
  input  A15,
  input  B15,
  input  A16,
  input  B16,
  input  A17,
  input  B17,
  input  A18,
  input  B18,
  input  A19,
  input  B19,
  input  A20,
  input  B20,
  input  A21,
  input  B21,
  input  A22,
  input  B22,
  input  A23,
  input  B23,
  input  A24,
  input  B24,
  input  A25,
  input  B25,
  input  A26,
  input  B26,
  input  A27,
  input  B27,
  input  A28,
  input  B28,
  input  A29,
  input  B29,
  input  A30,
  input  B30,
  input  A31,
  input  B31,
  output _0,
  output _1,
  output _2,
  output _3,
  output _4,
  output _5,
  output _6,
  output _7,
  output _8,
  output _9,
  output _10,
  output _11,
  output _12,
  output _13,
  output _14,
  output _15,
  output _16,
  output _17,
  output _18,
  output _19,
  output _20,
  output _21,
  output _22,
  output _23,
  output _24,
  output _25,
  output _26,
  output _27,
  output _28,
  output _29,
  output _30,
  output _31
);

  nor nor_1 (_0, A0, B0);
  nor nor_2 (_1, A1, B1);
  nor nor_3 (_2, A2, B2);
  nor nor_4 (_3, A3, B3);
  nor nor_5 (_4, A4, B4);
  nor nor_6 (_5, A5, B5);
  nor nor_7 (_6, A6, B6);
  nor nor_8 (_7, A7, B7);
  nor nor_9 (_8, A8, B8);
  nor nor_10 (_9, A9, B9);
  nor nor_11 (_10, A10, B10);
  nor nor_12 (_11, A11, B11);
  nor nor_13 (_12, A12, B12);
  nor nor_14 (_13, A13, B13);
  nor nor_15 (_14, A14, B14);
  nor nor_16 (_15, A15, B15);
  nor nor_17 (_16, A16, B16);
  nor nor_18 (_17, A17, B17);
  nor nor_19 (_18, A18, B18);
  nor nor_20 (_19, A19, B19);
  nor nor_21 (_20, A20, B20);
  nor nor_22 (_21, A21, B21);
  nor nor_23 (_22, A22, B22);
  nor nor_24 (_23, A23, B23);
  nor nor_25 (_24, A24, B24);
  nor nor_26 (_25, A25, B25);
  nor nor_27 (_26, A26, B26);
  nor nor_28 (_27, A27, B27);
  nor nor_29 (_28, A28, B28);
  nor nor_30 (_29, A29, B29);
  nor nor_31 (_30, A30, B30);
  nor nor_32 (_31, A31, B31);
endmodule

module nori (
  input  A0,
  input  B0,
  input  A1,
  input  B1,
  input  A2,
  input  B2,
  input  A3,
  input  B3,
  input  A4,
  input  B4,
  input  A5,
  input  B5,
  input  A6,
  input  B6,
  input  A7,
  input  B7,
  input  A8,
  input  B8,
  input  A9,
  input  B9,
  input  A10,
  input  B10,
  input  A11,
  input  B11,
  input  A12,
  input  B12,
  input  A13,
  input  B13,
  input  A14,
  input  B14,
  input  A15,
  input  B15,
  input  A16,
  input  A17,
  input  A18,
  input  A19,
  input  A20,
  input  A21,
  input  A22,
  input  A23,
  input  A24,
  input  A25,
  input  A26,
  input  A27,
  input  A28,
  input  A29,
  input  A30,
  input  A31,
  output _0,
  output _1,
  output _2,
  output _3,
  output _4,
  output _5,
  output _6,
  output _7,
  output _8,
  output _9,
  output _10,
  output _11,
  output _12,
  output _13,
  output _14,
  output _15,
  output _16,
  output _17,
  output _18,
  output _19,
  output _20,
  output _21,
  output _22,
  output _23,
  output _24,
  output _25,
  output _26,
  output _27,
  output _28,
  output _29,
  output _30,
  output _31
);

  nor nor_1 (_0, A0, B0);
  nor nor_2 (_1, A1, B1);
  nor nor_3 (_2, A2, B2);
  nor nor_4 (_3, A3, B3);
  nor nor_5 (_4, A4, B4);
  nor nor_6 (_5, A5, B5);
  nor nor_7 (_6, A6, B6);
  nor nor_8 (_7, A7, B7);
  nor nor_9 (_8, A8, B8);
  nor nor_10 (_9, A9, B9);
  nor nor_11 (_10, A10, B10);
  nor nor_12 (_11, A11, B11);
  nor nor_13 (_12, A12, B12);
  nor nor_14 (_13, A13, B13);
  nor nor_15 (_14, A14, B14);
  nor nor_16 (_15, A15, B15);

  assign _16 = A16;
  assign _17 = A17;
  assign _18 = A18;
  assign _19 = A19;
  assign _20 = A20;
  assign _21 = A21;
  assign _22 = A22;
  assign _23 = A23;
  assign _24 = A24;
  assign _25 = A25;
  assign _26 = A26;
  assign _27 = A27;
  assign _28 = A28;
  assign _29 = A29;
  assign _30 = A30;
  assign _31 = A31;
endmodule

module \xor  (
  input  A0,
  input  B0,
  input  A1,
  input  B1,
  input  A2,
  input  B2,
  input  A3,
  input  B3,
  input  A4,
  input  B4,
  input  A5,
  input  B5,
  input  A6,
  input  B6,
  input  A7,
  input  B7,
  input  A8,
  input  B8,
  input  A9,
  input  B9,
  input  A10,
  input  B10,
  input  A11,
  input  B11,
  input  A12,
  input  B12,
  input  A13,
  input  B13,
  input  A14,
  input  B14,
  input  A15,
  input  B15,
  input  A16,
  input  B16,
  input  A17,
  input  B17,
  input  A18,
  input  B18,
  input  A19,
  input  B19,
  input  A20,
  input  B20,
  input  A21,
  input  B21,
  input  A22,
  input  B22,
  input  A23,
  input  B23,
  input  A24,
  input  B24,
  input  A25,
  input  B25,
  input  A26,
  input  B26,
  input  A27,
  input  B27,
  input  A28,
  input  B28,
  input  A29,
  input  B29,
  input  A30,
  input  B30,
  input  A31,
  input  B31,
  output _0,
  output _1,
  output _2,
  output _3,
  output _4,
  output _5,
  output _6,
  output _7,
  output _8,
  output _9,
  output _10,
  output _11,
  output _12,
  output _13,
  output _14,
  output _15,
  output _16,
  output _17,
  output _18,
  output _19,
  output _20,
  output _21,
  output _22,
  output _23,
  output _24,
  output _25,
  output _26,
  output _27,
  output _28,
  output _29,
  output _30,
  output _31
);

  xor xor_1 (_0, A0, B0);
  xor xor_2 (_1, A1, B1);
  xor xor_3 (_2, A2, B2);
  xor xor_4 (_3, A3, B3);
  xor xor_5 (_4, A4, B4);
  xor xor_6 (_5, A5, B5);
  xor xor_7 (_6, A6, B6);
  xor xor_8 (_7, A7, B7);
  xor xor_9 (_8, A8, B8);
  xor xor_10 (_9, A9, B9);
  xor xor_11 (_10, A10, B10);
  xor xor_12 (_11, A11, B11);
  xor xor_13 (_12, A12, B12);
  xor xor_14 (_13, A13, B13);
  xor xor_15 (_14, A14, B14);
  xor xor_16 (_15, A15, B15);
  xor xor_17 (_16, A16, B16);
  xor xor_18 (_17, A17, B17);
  xor xor_19 (_18, A18, B18);
  xor xor_20 (_19, A19, B19);
  xor xor_21 (_20, A20, B20);
  xor xor_22 (_21, A21, B21);
  xor xor_23 (_22, A22, B22);
  xor xor_24 (_23, A23, B23);
  xor xor_25 (_24, A24, B24);
  xor xor_26 (_25, A25, B25);
  xor xor_27 (_26, A26, B26);
  xor xor_28 (_27, A27, B27);
  xor xor_29 (_28, A28, B28);
  xor xor_30 (_29, A29, B29);
  xor xor_31 (_30, A30, B30);
  xor xor_32 (_31, A31, B31);
endmodule

module xori (
  input  A0,
  input  B0,
  input  A1,
  input  B1,
  input  A2,
  input  B2,
  input  A3,
  input  B3,
  input  A4,
  input  B4,
  input  A5,
  input  B5,
  input  A6,
  input  B6,
  input  A7,
  input  B7,
  input  A8,
  input  B8,
  input  A9,
  input  B9,
  input  A10,
  input  B10,
  input  A11,
  input  B11,
  input  A12,
  input  B12,
  input  A13,
  input  B13,
  input  A14,
  input  B14,
  input  A15,
  input  B15,
  input  A16,
  input  A17,
  input  A18,
  input  A19,
  input  A20,
  input  A21,
  input  A22,
  input  A23,
  input  A24,
  input  A25,
  input  A26,
  input  A27,
  input  A28,
  input  A29,
  input  A30,
  input  A31,
  output _0,
  output _1,
  output _2,
  output _3,
  output _4,
  output _5,
  output _6,
  output _7,
  output _8,
  output _9,
  output _10,
  output _11,
  output _12,
  output _13,
  output _14,
  output _15,
  output _16,
  output _17,
  output _18,
  output _19,
  output _20,
  output _21,
  output _22,
  output _23,
  output _24,
  output _25,
  output _26,
  output _27,
  output _28,
  output _29,
  output _30,
  output _31
);

  xor xor_1 (_0, A0, B0);
  xor xor_2 (_1, A1, B1);
  xor xor_3 (_2, A2, B2);
  xor xor_4 (_3, A3, B3);
  xor xor_5 (_4, A4, B4);
  xor xor_6 (_5, A5, B5);
  xor xor_7 (_6, A6, B6);
  xor xor_8 (_7, A7, B7);
  xor xor_9 (_8, A8, B8);
  xor xor_10 (_9, A9, B9);
  xor xor_11 (_10, A10, B10);
  xor xor_12 (_11, A11, B11);
  xor xor_13 (_12, A12, B12);
  xor xor_14 (_13, A13, B13);
  xor xor_15 (_14, A14, B14);
  xor xor_16 (_15, A15, B15);

  assign _16 = A16;
  assign _17 = A17;
  assign _18 = A18;
  assign _19 = A19;
  assign _20 = A20;
  assign _21 = A21;
  assign _22 = A22;
  assign _23 = A23;
  assign _24 = A24;
  assign _25 = A25;
  assign _26 = A26;
  assign _27 = A27;
  assign _28 = A28;
  assign _29 = A29;
  assign _30 = A30;
  assign _31 = A31;
endmodule

module \xnor  (
  input  A0,
  input  B0,
  input  A1,
  input  B1,
  input  A2,
  input  B2,
  input  A3,
  input  B3,
  input  A4,
  input  B4,
  input  A5,
  input  B5,
  input  A6,
  input  B6,
  input  A7,
  input  B7,
  input  A8,
  input  B8,
  input  A9,
  input  B9,
  input  A10,
  input  B10,
  input  A11,
  input  B11,
  input  A12,
  input  B12,
  input  A13,
  input  B13,
  input  A14,
  input  B14,
  input  A15,
  input  B15,
  input  A16,
  input  B16,
  input  A17,
  input  B17,
  input  A18,
  input  B18,
  input  A19,
  input  B19,
  input  A20,
  input  B20,
  input  A21,
  input  B21,
  input  A22,
  input  B22,
  input  A23,
  input  B23,
  input  A24,
  input  B24,
  input  A25,
  input  B25,
  input  A26,
  input  B26,
  input  A27,
  input  B27,
  input  A28,
  input  B28,
  input  A29,
  input  B29,
  input  A30,
  input  B30,
  input  A31,
  input  B31,
  output _0,
  output _1,
  output _2,
  output _3,
  output _4,
  output _5,
  output _6,
  output _7,
  output _8,
  output _9,
  output _10,
  output _11,
  output _12,
  output _13,
  output _14,
  output _15,
  output _16,
  output _17,
  output _18,
  output _19,
  output _20,
  output _21,
  output _22,
  output _23,
  output _24,
  output _25,
  output _26,
  output _27,
  output _28,
  output _29,
  output _30,
  output _31
);

  xnor xnor_1 (_0, A0, B0);
  xnor xnor_2 (_1, A1, B1);
  xnor xnor_3 (_2, A2, B2);
  xnor xnor_4 (_3, A3, B3);
  xnor xnor_5 (_4, A4, B4);
  xnor xnor_6 (_5, A5, B5);
  xnor xnor_7 (_6, A6, B6);
  xnor xnor_8 (_7, A7, B7);
  xnor xnor_9 (_8, A8, B8);
  xnor xnor_10 (_9, A9, B9);
  xnor xnor_11 (_10, A10, B10);
  xnor xnor_12 (_11, A11, B11);
  xnor xnor_13 (_12, A12, B12);
  xnor xnor_14 (_13, A13, B13);
  xnor xnor_15 (_14, A14, B14);
  xnor xnor_16 (_15, A15, B15);
  xnor xnor_17 (_16, A16, B16);
  xnor xnor_18 (_17, A17, B17);
  xnor xnor_19 (_18, A18, B18);
  xnor xnor_20 (_19, A19, B19);
  xnor xnor_21 (_20, A20, B20);
  xnor xnor_22 (_21, A21, B21);
  xnor xnor_23 (_22, A22, B22);
  xnor xnor_24 (_23, A23, B23);
  xnor xnor_25 (_24, A24, B24);
  xnor xnor_26 (_25, A25, B25);
  xnor xnor_27 (_26, A26, B26);
  xnor xnor_28 (_27, A27, B27);
  xnor xnor_29 (_28, A28, B28);
  xnor xnor_30 (_29, A29, B29);
  xnor xnor_31 (_30, A30, B30);
  xnor xnor_32 (_31, A31, B31);
endmodule

module xnori (
  input  A0,
  input  B0,
  input  A1,
  input  B1,
  input  A2,
  input  B2,
  input  A3,
  input  B3,
  input  A4,
  input  B4,
  input  A5,
  input  B5,
  input  A6,
  input  B6,
  input  A7,
  input  B7,
  input  A8,
  input  B8,
  input  A9,
  input  B9,
  input  A10,
  input  B10,
  input  A11,
  input  B11,
  input  A12,
  input  B12,
  input  A13,
  input  B13,
  input  A14,
  input  B14,
  input  A15,
  input  B15,
  input  A16,
  input  A17,
  input  A18,
  input  A19,
  input  A20,
  input  A21,
  input  A22,
  input  A23,
  input  A24,
  input  A25,
  input  A26,
  input  A27,
  input  A28,
  input  A29,
  input  A30,
  input  A31,
  output _0,
  output _1,
  output _2,
  output _3,
  output _4,
  output _5,
  output _6,
  output _7,
  output _8,
  output _9,
  output _10,
  output _11,
  output _12,
  output _13,
  output _14,
  output _15,
  output _16,
  output _17,
  output _18,
  output _19,
  output _20,
  output _21,
  output _22,
  output _23,
  output _24,
  output _25,
  output _26,
  output _27,
  output _28,
  output _29,
  output _30,
  output _31
);

  xnor xnor_1 (_0, A0, B0);
  xnor xnor_2 (_1, A1, B1);
  xnor xnor_3 (_2, A2, B2);
  xnor xnor_4 (_3, A3, B3);
  xnor xnor_5 (_4, A4, B4);
  xnor xnor_6 (_5, A5, B5);
  xnor xnor_7 (_6, A6, B6);
  xnor xnor_8 (_7, A7, B7);
  xnor xnor_9 (_8, A8, B8);
  xnor xnor_10 (_9, A9, B9);
  xnor xnor_11 (_10, A10, B10);
  xnor xnor_12 (_11, A11, B11);
  xnor xnor_13 (_12, A12, B12);
  xnor xnor_14 (_13, A13, B13);
  xnor xnor_15 (_14, A14, B14);
  xnor xnor_16 (_15, A15, B15);
  not not_1 (_16, A16);
  not not_2 (_17, A17);
  not not_3 (_18, A18);
  not not_4 (_19, A19);
  not not_5 (_20, A20);
  not not_6 (_21, A21);
  not not_7 (_22, A22);
  not not_8 (_23, A23);
  not not_9 (_24, A24);
  not not_10 (_25, A25);
  not not_11 (_26, A26);
  not not_12 (_27, A27);
  not not_13 (_28, A28);
  not not_14 (_29, A29);
  not not_15 (_30, A30);
  not not_16 (_31, A31);
endmodule
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module sltu (
  input  B0,
  input  B1,
  input  B2,
  input  B3,
  input  B4,
  input  B5,
  input  B6,
  input  B7,
  input  B8,
  input  B9,
  input  B10,
  input  B11,
  input  B12,
  input  B13,
  input  B14,
  input  B15,
  input  B16,
  input  B17,
  input  B18,
  input  B19,
  input  B20,
  input  B21,
  input  B22,
  input  B23,
  input  B24,
  input  B25,
  input  B26,
  input  B27,
  input  B28,
  input  B29,
  input  B30,
  input  B31,
  input  A0,
  input  A1,
  input  A2,
  input  A3,
  input  A4,
  input  A5,
  input  A6,
  input  A7,
  input  A8,
  input  A9,
  input  A10,
  input  A11,
  input  A12,
  input  A13,
  input  A14,
  input  A15,
  input  A16,
  input  A17,
  input  A18,
  input  A19,
  input  A20,
  input  A21,
  input  A22,
  input  A23,
  input  A24,
  input  A25,
  input  A26,
  input  A27,
  input  A28,
  input  A29,
  input  A30,
  input  A31,
  output _0,
  output _1,
  output _2,
  output _3,
  output _4,
  output _5,
  output _6,
  output _7,
  output _8,
  output _9,
  output _10,
  output _11,
  output _12,
  output _13,
  output _14,
  output _15,
  output _16,
  output _17,
  output _18,
  output _19,
  output _20,
  output _21,
  output _22,
  output _23,
  output _24,
  output _25,
  output _26,
  output _27,
  output _28,
  output _29,
  output _30,
  output _31
);

  wire and_1_out, and_2_out, and_3_out, and_4_out, and_5_out, and_6_out, and_7_out, and_8_out, and_9_out,
       and_10_out, and_11_out, and_12_out, and_13_out, and_14_out, and_15_out, and_16_out, and_17_out,
       and_18_out, and_19_out, and_20_out, and_21_out, and_22_out, and_23_out, and_24_out, and_25_out,
       and_26_out, and_27_out, and_28_out, and_29_out, and_30_out, and_31_out, and_32_out, and_33_out,
       and_34_out, and_35_out, and_36_out, and_37_out, and_38_out, and_39_out, and_40_out, and_41_out,
       and_42_out, and_43_out, and_44_out, and_45_out, and_46_out, and_47_out, and_48_out, and_49_out,
       and_50_out, and_51_out, and_52_out, and_53_out, and_54_out, and_55_out, and_56_out, and_57_out,
       and_58_out, and_59_out, and_60_out, and_61_out, and_62_out, and_63_out, and_64_out, and_65_out,
       and_66_out, and_67_out, and_68_out, and_69_out, and_70_out, and_71_out, and_72_out, and_73_out,
       and_74_out, and_75_out, and_76_out, and_77_out, and_78_out, and_79_out, and_80_out, and_81_out,
       and_82_out, and_83_out, and_84_out, and_85_out, and_86_out, and_87_out, and_88_out, and_89_out,
       and_90_out, and_91_out, and_92_out, and_93_out, not_1_out, not_2_out, not_3_out, not_4_out, not_5_out,
       not_6_out, not_7_out, not_8_out, not_9_out, not_10_out, not_11_out, not_12_out, not_13_out,
       not_14_out, not_15_out, not_16_out, not_17_out, not_18_out, not_19_out, not_20_out, not_21_out,
       not_22_out, not_23_out, not_24_out, not_25_out, not_26_out, not_27_out, not_28_out, not_29_out,
       not_30_out, not_31_out, not_32_out, not_33_out, not_34_out, not_35_out, not_36_out, not_37_out,
       not_38_out, not_39_out, not_40_out, not_41_out, not_42_out, not_43_out, not_44_out, not_45_out,
       not_46_out, not_47_out, not_48_out, not_49_out, not_50_out, not_51_out, not_52_out, not_53_out,
       not_54_out, not_55_out, not_56_out, not_57_out, not_58_out, not_59_out, not_60_out, not_61_out,
       not_62_out, not_63_out, not_64_out, not_65_out, not_66_out, not_67_out, not_68_out, not_69_out,
       not_70_out, not_71_out, not_72_out, not_73_out, not_74_out, not_75_out, not_76_out, not_77_out,
       not_78_out, not_79_out, not_80_out, not_81_out, not_82_out, not_83_out, not_84_out, not_85_out,
       not_86_out, not_87_out, not_88_out, not_89_out, not_90_out, not_91_out, not_92_out, not_93_out,
       not_94_out, or_1_out, or_2_out, or_3_out, or_4_out, or_5_out, or_6_out, or_7_out, or_8_out, or_9_out,
       or_10_out, or_11_out, or_12_out, or_13_out, or_14_out, or_15_out, or_16_out, or_17_out, or_18_out,
       or_19_out, or_20_out, or_21_out, or_22_out, or_23_out, or_24_out, or_25_out, or_26_out, or_27_out,
       or_28_out, or_29_out, or_30_out;

  not not_1 (not_1_out, B31);
  not not_2 (not_2_out, A31);
  not not_3 (not_3_out, A31);
  not not_4 (not_4_out, B30);
  not not_5 (not_5_out, A30);
  not not_6 (not_6_out, A30);
  and and_1 (and_1_out, not_1_out, not_2_out);
  and and_2 (and_2_out, B31, not_3_out);
  or or_1 (or_1_out, and_2_out, and_5_out);
  or or_2 (or_2_out, or_1_out, and_8_out);
  or or_3 (or_3_out, or_2_out, and_10_out);
  or or_4 (or_4_out, or_3_out, and_13_out);
  or or_5 (or_5_out, or_4_out, and_16_out);
  or or_6 (or_6_out, or_5_out, and_19_out);
  and and_3 (and_3_out, not_4_out, not_5_out);
  and and_4 (and_4_out, and_3_out, and_1_out);
  and and_5 (and_5_out, B30, not_6_out, and_1_out);
  or or_7 (or_7_out, or_6_out, and_22_out);
  or or_8 (or_8_out, or_7_out, and_25_out);
  or or_9 (or_9_out, or_8_out, and_29_out);
  or or_10 (or_10_out, or_9_out, and_32_out);
  or or_11 (or_11_out, or_10_out, and_34_out);
  or or_12 (or_12_out, or_11_out, and_37_out);
  or or_13 (or_13_out, or_12_out, and_40_out);
  or or_14 (or_14_out, or_13_out, and_43_out);
  not not_7 (not_7_out, B29);
  not not_8 (not_8_out, A29);
  not not_9 (not_9_out, A29);
  or or_15 (or_15_out, or_14_out, and_46_out);
  or or_16 (or_16_out, or_15_out, and_49_out);
  or or_17 (or_17_out, or_16_out, and_53_out);
  or or_18 (or_18_out, or_17_out, and_56_out);
  or or_19 (or_19_out, or_18_out, and_58_out);
  or or_20 (or_20_out, or_19_out, and_61_out);
  or or_21 (or_21_out, or_20_out, and_64_out);
  or or_22 (or_22_out, or_21_out, and_67_out);
  and and_6 (and_6_out, not_7_out, not_8_out);
  and and_7 (and_7_out, and_6_out, and_4_out);
  and and_8 (and_8_out, B29, not_9_out, and_4_out);
  or or_23 (or_23_out, or_22_out, and_70_out);
  or or_24 (or_24_out, or_23_out, and_73_out);
  or or_25 (or_25_out, or_24_out, and_77_out);
  or or_26 (or_26_out, or_25_out, and_80_out);
  or or_27 (or_27_out, or_26_out, and_82_out);
  or or_28 (or_28_out, or_27_out, and_85_out);
  or or_29 (or_29_out, or_28_out, and_88_out);
  or or_30 (or_30_out, or_29_out, and_91_out);
  not not_10 (not_10_out, B28);
  and and_9 (and_9_out, not_10_out, not_11_out);
  not not_11 (not_11_out, A28);
  not not_12 (not_12_out, A28);
  and and_10 (and_10_out, B28, not_12_out, and_7_out);
  or or_31 (_0, or_30_out, and_93_out);
  and and_11 (and_11_out, and_9_out, and_7_out);
  not not_13 (not_13_out, B27);
  and and_12 (and_12_out, not_13_out, not_14_out);
  not not_14 (not_14_out, A27);
  and and_13 (and_13_out, B27, not_15_out, and_11_out);
  not not_15 (not_15_out, A27);
  and and_14 (and_14_out, and_12_out, and_11_out);
  not not_16 (not_16_out, B26);
  and and_15 (and_15_out, not_16_out, not_17_out);
  not not_17 (not_17_out, A26);
  and and_16 (and_16_out, B26, not_18_out, and_14_out);
  not not_18 (not_18_out, A26);
  not not_19 (not_19_out, A25);
  and and_17 (and_17_out, and_15_out, and_14_out);
  not not_20 (not_20_out, B25);
  and and_18 (and_18_out, not_20_out, not_21_out);
  not not_21 (not_21_out, A25);
  and and_19 (and_19_out, B25, not_19_out, and_17_out);
  not not_22 (not_22_out, A24);
  and and_20 (and_20_out, and_18_out, and_17_out);
  not not_23 (not_23_out, B24);
  and and_21 (and_21_out, not_23_out, not_24_out);
  not not_24 (not_24_out, A24);
  and and_22 (and_22_out, B24, not_22_out, and_20_out);
  not not_25 (not_25_out, B23);
  not not_26 (not_26_out, A23);
  not not_27 (not_27_out, A23);
  and and_23 (and_23_out, and_21_out, and_20_out);
  and and_24 (and_24_out, not_25_out, not_26_out);
  and and_25 (and_25_out, B23, not_27_out, and_23_out);
  not not_28 (not_28_out, B22);
  not not_29 (not_29_out, A22);
  not not_30 (not_30_out, A22);
  and and_26 (and_26_out, and_24_out, and_23_out);
  and and_27 (and_27_out, not_28_out, not_29_out);
  and and_28 (and_28_out, and_27_out, and_26_out);
  and and_29 (and_29_out, B22, not_30_out, and_26_out);
  not not_31 (not_31_out, B21);
  not not_32 (not_32_out, A21);
  not not_33 (not_33_out, A21);
  and and_30 (and_30_out, not_31_out, not_32_out);
  and and_31 (and_31_out, and_30_out, and_28_out);
  and and_32 (and_32_out, B21, not_33_out, and_28_out);
  not not_34 (not_34_out, B20);
  and and_33 (and_33_out, not_34_out, not_35_out);
  not not_35 (not_35_out, A20);
  and and_34 (and_34_out, B20, not_36_out, and_31_out);
  not not_36 (not_36_out, A20);
  and and_35 (and_35_out, and_33_out, and_31_out);
  not not_37 (not_37_out, B19);
  and and_36 (and_36_out, not_37_out, not_38_out);
  not not_38 (not_38_out, A19);
  not not_39 (not_39_out, A19);
  and and_37 (and_37_out, B19, not_39_out, and_35_out);
  and and_38 (and_38_out, and_36_out, and_35_out);
  not not_40 (not_40_out, B18);
  and and_39 (and_39_out, not_40_out, not_41_out);
  not not_41 (not_41_out, A18);
  not not_42 (not_42_out, A18);
  and and_40 (and_40_out, B18, not_42_out, and_38_out);
  not not_43 (not_43_out, A17);
  and and_41 (and_41_out, and_39_out, and_38_out);
  not not_44 (not_44_out, B17);
  and and_42 (and_42_out, not_44_out, not_45_out);
  not not_45 (not_45_out, A17);
  and and_43 (and_43_out, B17, not_43_out, and_41_out);
  not not_46 (not_46_out, A16);
  and and_44 (and_44_out, and_42_out, and_41_out);
  not not_47 (not_47_out, B16);
  and and_45 (and_45_out, not_47_out, not_48_out);
  not not_48 (not_48_out, A16);
  and and_46 (and_46_out, B16, not_46_out, and_44_out);
  not not_49 (not_49_out, B15);
  not not_50 (not_50_out, A15);
  not not_51 (not_51_out, A15);
  and and_47 (and_47_out, and_45_out, and_44_out);
  and and_48 (and_48_out, not_49_out, not_50_out);
  and and_49 (and_49_out, B15, not_51_out, and_47_out);
  not not_52 (not_52_out, B14);
  not not_53 (not_53_out, A14);
  not not_54 (not_54_out, A14);
  and and_50 (and_50_out, and_48_out, and_47_out);
  and and_51 (and_51_out, not_52_out, not_53_out);
  and and_52 (and_52_out, and_51_out, and_50_out);
  and and_53 (and_53_out, B14, not_54_out, and_50_out);
  not not_55 (not_55_out, B13);
  not not_56 (not_56_out, A13);
  not not_57 (not_57_out, A13);
  and and_54 (and_54_out, not_55_out, not_56_out);
  and and_55 (and_55_out, and_54_out, and_52_out);
  and and_56 (and_56_out, B13, not_57_out, and_52_out);
  not not_58 (not_58_out, B12);
  and and_57 (and_57_out, not_58_out, not_59_out);
  not not_59 (not_59_out, A12);
  and and_58 (and_58_out, B12, not_60_out, and_55_out);
  not not_60 (not_60_out, A12);
  and and_59 (and_59_out, and_57_out, and_55_out);
  not not_61 (not_61_out, B11);
  and and_60 (and_60_out, not_61_out, not_62_out);
  not not_62 (not_62_out, A11);
  and and_61 (and_61_out, B11, not_63_out, and_59_out);
  not not_63 (not_63_out, A11);
  and and_62 (and_62_out, and_60_out, and_59_out);
  not not_64 (not_64_out, B10);
  and and_63 (and_63_out, not_64_out, not_65_out);
  not not_65 (not_65_out, A10);
  not not_66 (not_66_out, A10);
  and and_64 (and_64_out, B10, not_66_out, and_62_out);
  not not_67 (not_67_out, A9);
  and and_65 (and_65_out, and_63_out, and_62_out);
  not not_68 (not_68_out, B9);
  and and_66 (and_66_out, not_68_out, not_69_out);
  not not_69 (not_69_out, A9);
  and and_67 (and_67_out, B9, not_67_out, and_65_out);
  not not_70 (not_70_out, A8);
  and and_68 (and_68_out, and_66_out, and_65_out);
  not not_71 (not_71_out, B8);
  and and_69 (and_69_out, not_71_out, not_72_out);
  not not_72 (not_72_out, A8);
  and and_70 (and_70_out, B8, not_70_out, and_68_out);
  not not_73 (not_73_out, B7);
  not not_74 (not_74_out, A7);
  not not_75 (not_75_out, A7);
  and and_71 (and_71_out, and_69_out, and_68_out);
  and and_72 (and_72_out, not_73_out, not_74_out);
  and and_73 (and_73_out, B7, not_75_out, and_71_out);
  not not_76 (not_76_out, B6);
  not not_77 (not_77_out, A6);
  not not_78 (not_78_out, A6);
  and and_74 (and_74_out, and_72_out, and_71_out);
  and and_75 (and_75_out, not_76_out, not_77_out);
  and and_76 (and_76_out, and_75_out, and_74_out);
  and and_77 (and_77_out, B6, not_78_out, and_74_out);
  not not_79 (not_79_out, B5);
  not not_80 (not_80_out, A5);
  not not_81 (not_81_out, A5);
  and and_78 (and_78_out, not_79_out, not_80_out);
  and and_79 (and_79_out, and_78_out, and_76_out);
  and and_80 (and_80_out, B5, not_81_out, and_76_out);
  not not_82 (not_82_out, B4);
  and and_81 (and_81_out, not_82_out, not_83_out);
  not not_83 (not_83_out, A4);
  not not_84 (not_84_out, A4);
  and and_82 (and_82_out, B4, not_84_out, and_79_out);
  and and_83 (and_83_out, and_81_out, and_79_out);
  not not_85 (not_85_out, B3);
  and and_84 (and_84_out, not_85_out, not_86_out);
  not not_86 (not_86_out, A3);
  not not_87 (not_87_out, A3);
  and and_85 (and_85_out, B3, not_87_out, and_83_out);
  and and_86 (and_86_out, and_84_out, and_83_out);
  not not_88 (not_88_out, B2);
  and and_87 (and_87_out, not_88_out, not_89_out);
  not not_89 (not_89_out, A2);
  and and_88 (and_88_out, B2, not_90_out, and_86_out);
  not not_90 (not_90_out, A2);
  not not_91 (not_91_out, A1);
  and and_89 (and_89_out, and_87_out, and_86_out);
  not not_92 (not_92_out, B1);
  and and_90 (and_90_out, not_92_out, not_93_out);
  not not_93 (not_93_out, A1);
  and and_91 (and_91_out, B1, not_91_out, and_89_out);
  not not_94 (not_94_out, A0);
  and and_92 (and_92_out, and_90_out, and_89_out);
  and and_93 (and_93_out, B0, not_94_out, and_92_out);

  assign _1 = _0;
  assign _2 = _0;
  assign _3 = _0;
  assign _4 = _0;
  assign _5 = _0;
  assign _6 = _0;
  assign _7 = _0;
  assign _8 = _0;
  assign _9 = _0;
  assign _10 = _0;
  assign _11 = _0;
  assign _12 = _0;
  assign _13 = _0;
  assign _14 = _0;
  assign _15 = _0;
  assign _16 = _0;
  assign _17 = _0;
  assign _18 = _0;
  assign _19 = _0;
  assign _20 = _0;
  assign _21 = _0;
  assign _22 = _0;
  assign _23 = _0;
  assign _24 = _0;
  assign _25 = _0;
  assign _26 = _0;
  assign _27 = _0;
  assign _28 = _0;
  assign _29 = _0;
  assign _30 = _0;
  assign _31 = _0;

  // Notes on the sheet:
  //   b
  //   a
  //   b
  //   a
  //   b
  //   a
  //   b
  //   a
  //   b
  //   a
  //   b
  //   a
  //   b
  //   a
  //   b
  //   a
  //   b
  //   a
  //   b
  //   a
  //   b
  //   a
  //   b
  //   a
  //   b
  //   a
  //   b
  //   a
  //   b
  //   a
  //   b
  //   a
  //   b
  //   a
  //   b
  //   a
  //   b
  //   a
  //   b
  //   a
  //   b
  //   a
  //   b
  //   a
  //   b
  //   a
  //   b
  //   a
  //   b
  //   a
  //   b
  //   a
  //   b
  //   a
  //   b
  //   a
  //   b
  //   a
  //   b
  //   a
endmodule

module sltui (
  input  B0,
  input  B1,
  input  B2,
  input  B3,
  input  B4,
  input  B5,
  input  B6,
  input  B7,
  input  B8,
  input  B9,
  input  B10,
  input  B11,
  input  B12,
  input  B13,
  input  B14,
  input  B15,
  input  A0,
  input  A1,
  input  A2,
  input  A3,
  input  A4,
  input  A5,
  input  A6,
  input  A7,
  input  A8,
  input  A9,
  input  A10,
  input  A11,
  input  A12,
  input  A13,
  input  A14,
  input  A15,
  input  A16,
  input  A17,
  input  A18,
  input  A19,
  input  A20,
  input  A21,
  input  A22,
  input  A23,
  input  A24,
  input  A25,
  input  A26,
  input  A27,
  input  A28,
  input  A29,
  input  A30,
  input  A31,
  output _0,
  output _1,
  output _2,
  output _3,
  output _4,
  output _5,
  output _6,
  output _7,
  output _8,
  output _9,
  output _10,
  output _11,
  output _12,
  output _13,
  output _14,
  output _15,
  output _16,
  output _17,
  output _18,
  output _19,
  output _20,
  output _21,
  output _22,
  output _23,
  output _24,
  output _25,
  output _26,
  output _27,
  output _28,
  output _29,
  output _30,
  output _31
);

  wire and_1_out, and_2_out, and_3_out, and_4_out, and_5_out, and_6_out, and_7_out, and_8_out, and_9_out,
       and_10_out, and_11_out, and_12_out, and_13_out, and_14_out, and_15_out, and_16_out, and_17_out,
       and_18_out, and_19_out, and_20_out, and_21_out, and_22_out, and_23_out, and_24_out, and_25_out,
       and_26_out, and_27_out, and_28_out, and_29_out, and_30_out, and_31_out, and_32_out, and_33_out,
       and_34_out, and_35_out, and_36_out, and_37_out, and_38_out, and_39_out, and_40_out, and_41_out,
       and_42_out, and_43_out, and_44_out, and_45_out, and_46_out, and_47_out, and_48_out, and_49_out,
       and_50_out, and_51_out, and_52_out, and_53_out, and_54_out, and_55_out, and_56_out, and_57_out,
       and_58_out, and_59_out, and_60_out, and_61_out, and_62_out, and_63_out, and_64_out, and_65_out,
       and_66_out, and_67_out, and_68_out, and_69_out, and_70_out, and_71_out, and_72_out, and_73_out,
       and_74_out, and_75_out, and_76_out, and_77_out, and_78_out, and_79_out, and_80_out, and_81_out,
       and_82_out, and_83_out, and_84_out, and_85_out, and_86_out, and_87_out, and_88_out, and_89_out,
       and_90_out, and_91_out, and_92_out, and_93_out, not_1_out, not_2_out, not_3_out, not_4_out, not_5_out,
       not_6_out, not_7_out, not_8_out, not_9_out, not_10_out, not_11_out, not_12_out, not_13_out,
       not_14_out, not_15_out, not_16_out, not_17_out, not_18_out, not_19_out, not_20_out, not_21_out,
       not_22_out, not_23_out, not_24_out, not_25_out, not_26_out, not_27_out, not_28_out, not_29_out,
       not_30_out, not_31_out, not_32_out, not_33_out, not_34_out, not_35_out, not_36_out, not_37_out,
       not_38_out, not_39_out, not_40_out, not_41_out, not_42_out, not_43_out, not_44_out, not_45_out,
       not_46_out, not_47_out, not_48_out, not_49_out, not_50_out, not_51_out, not_52_out, not_53_out,
       not_54_out, not_55_out, not_56_out, not_57_out, not_58_out, not_59_out, not_60_out, not_61_out,
       not_62_out, not_63_out, not_64_out, not_65_out, not_66_out, not_67_out, not_68_out, not_69_out,
       not_70_out, not_71_out, not_72_out, not_73_out, not_74_out, not_75_out, not_76_out, not_77_out,
       not_78_out, not_79_out, not_80_out, not_81_out, not_82_out, not_83_out, not_84_out, not_85_out,
       not_86_out, not_87_out, not_88_out, not_89_out, not_90_out, not_91_out, not_92_out, not_93_out,
       not_94_out, or_1_out, or_2_out, or_3_out, or_4_out, or_5_out, or_6_out, or_7_out, or_8_out, or_9_out,
       or_10_out, or_11_out, or_12_out, or_13_out, or_14_out, or_15_out, or_16_out, or_17_out, or_18_out,
       or_19_out, or_20_out, or_21_out, or_22_out, or_23_out, or_24_out, or_25_out, or_26_out, or_27_out,
       or_28_out, or_29_out, or_30_out;

  not not_1 (not_1_out, 1'b0);
  not not_2 (not_2_out, A31);
  not not_3 (not_3_out, A31);
  not not_4 (not_4_out, 1'b0);
  not not_5 (not_5_out, A30);
  not not_6 (not_6_out, A30);
  and and_1 (and_1_out, not_1_out, not_2_out);
  and and_2 (and_2_out, 1'b0, not_3_out);
  or or_1 (or_1_out, and_2_out, and_5_out);
  or or_2 (or_2_out, or_1_out, and_8_out);
  or or_3 (or_3_out, or_2_out, and_10_out);
  or or_4 (or_4_out, or_3_out, and_13_out);
  or or_5 (or_5_out, or_4_out, and_16_out);
  or or_6 (or_6_out, or_5_out, and_19_out);
  and and_3 (and_3_out, not_4_out, not_5_out);
  and and_4 (and_4_out, and_3_out, and_1_out);
  and and_5 (and_5_out, 1'b0, not_6_out, and_1_out);
  or or_7 (or_7_out, or_6_out, and_22_out);
  or or_8 (or_8_out, or_7_out, and_25_out);
  or or_9 (or_9_out, or_8_out, and_29_out);
  or or_10 (or_10_out, or_9_out, and_32_out);
  or or_11 (or_11_out, or_10_out, and_34_out);
  or or_12 (or_12_out, or_11_out, and_37_out);
  or or_13 (or_13_out, or_12_out, and_40_out);
  or or_14 (or_14_out, or_13_out, and_43_out);
  not not_7 (not_7_out, 1'b0);
  not not_8 (not_8_out, A29);
  not not_9 (not_9_out, A29);
  or or_15 (or_15_out, or_14_out, and_46_out);
  or or_16 (or_16_out, or_15_out, and_49_out);
  or or_17 (or_17_out, or_16_out, and_53_out);
  or or_18 (or_18_out, or_17_out, and_56_out);
  or or_19 (or_19_out, or_18_out, and_58_out);
  or or_20 (or_20_out, or_19_out, and_61_out);
  or or_21 (or_21_out, or_20_out, and_64_out);
  or or_22 (or_22_out, or_21_out, and_67_out);
  and and_6 (and_6_out, not_7_out, not_8_out);
  and and_7 (and_7_out, and_6_out, and_4_out);
  and and_8 (and_8_out, 1'b0, not_9_out, and_4_out);
  or or_23 (or_23_out, or_22_out, and_70_out);
  or or_24 (or_24_out, or_23_out, and_73_out);
  or or_25 (or_25_out, or_24_out, and_77_out);
  or or_26 (or_26_out, or_25_out, and_80_out);
  or or_27 (or_27_out, or_26_out, and_82_out);
  or or_28 (or_28_out, or_27_out, and_85_out);
  or or_29 (or_29_out, or_28_out, and_88_out);
  or or_30 (or_30_out, or_29_out, and_91_out);
  not not_10 (not_10_out, 1'b0);
  and and_9 (and_9_out, not_10_out, not_11_out);
  not not_11 (not_11_out, A28);
  not not_12 (not_12_out, A28);
  and and_10 (and_10_out, 1'b0, not_12_out, and_7_out);
  or or_31 (_0, or_30_out, and_93_out);
  and and_11 (and_11_out, and_9_out, and_7_out);
  not not_13 (not_13_out, 1'b0);
  and and_12 (and_12_out, not_13_out, not_14_out);
  not not_14 (not_14_out, A27);
  not not_15 (not_15_out, A27);
  and and_13 (and_13_out, 1'b0, not_15_out, and_11_out);
  and and_14 (and_14_out, and_12_out, and_11_out);
  not not_16 (not_16_out, 1'b0);
  and and_15 (and_15_out, not_16_out, not_17_out);
  not not_17 (not_17_out, A26);
  and and_16 (and_16_out, 1'b0, not_18_out, and_14_out);
  not not_18 (not_18_out, A26);
  not not_19 (not_19_out, A25);
  and and_17 (and_17_out, and_15_out, and_14_out);
  not not_20 (not_20_out, 1'b0);
  and and_18 (and_18_out, not_20_out, not_21_out);
  not not_21 (not_21_out, A25);
  and and_19 (and_19_out, 1'b0, not_19_out, and_17_out);
  not not_22 (not_22_out, A24);
  and and_20 (and_20_out, and_18_out, and_17_out);
  not not_23 (not_23_out, 1'b0);
  and and_21 (and_21_out, not_23_out, not_24_out);
  not not_24 (not_24_out, A24);
  and and_22 (and_22_out, 1'b0, not_22_out, and_20_out);
  not not_25 (not_25_out, 1'b0);
  not not_26 (not_26_out, A23);
  not not_27 (not_27_out, A23);
  and and_23 (and_23_out, and_21_out, and_20_out);
  and and_24 (and_24_out, not_25_out, not_26_out);
  and and_25 (and_25_out, 1'b0, not_27_out, and_23_out);
  not not_28 (not_28_out, 1'b0);
  not not_29 (not_29_out, A22);
  not not_30 (not_30_out, A22);
  and and_26 (and_26_out, and_24_out, and_23_out);
  and and_27 (and_27_out, not_28_out, not_29_out);
  and and_28 (and_28_out, and_27_out, and_26_out);
  and and_29 (and_29_out, 1'b0, not_30_out, and_26_out);
  not not_31 (not_31_out, 1'b0);
  not not_32 (not_32_out, A21);
  not not_33 (not_33_out, A21);
  and and_30 (and_30_out, not_31_out, not_32_out);
  and and_31 (and_31_out, and_30_out, and_28_out);
  and and_32 (and_32_out, 1'b0, not_33_out, and_28_out);
  not not_34 (not_34_out, 1'b0);
  and and_33 (and_33_out, not_34_out, not_35_out);
  not not_35 (not_35_out, A20);
  not not_36 (not_36_out, A20);
  and and_34 (and_34_out, 1'b0, not_36_out, and_31_out);
  and and_35 (and_35_out, and_33_out, and_31_out);
  not not_37 (not_37_out, 1'b0);
  and and_36 (and_36_out, not_37_out, not_38_out);
  not not_38 (not_38_out, A19);
  and and_37 (and_37_out, 1'b0, not_39_out, and_35_out);
  not not_39 (not_39_out, A19);
  and and_38 (and_38_out, and_36_out, and_35_out);
  not not_40 (not_40_out, 1'b0);
  and and_39 (and_39_out, not_40_out, not_41_out);
  not not_41 (not_41_out, A18);
  not not_42 (not_42_out, A18);
  and and_40 (and_40_out, 1'b0, not_42_out, and_38_out);
  not not_43 (not_43_out, A17);
  and and_41 (and_41_out, and_39_out, and_38_out);
  not not_44 (not_44_out, 1'b0);
  and and_42 (and_42_out, not_44_out, not_45_out);
  not not_45 (not_45_out, A17);
  and and_43 (and_43_out, 1'b0, not_43_out, and_41_out);
  not not_46 (not_46_out, A16);
  and and_44 (and_44_out, and_42_out, and_41_out);
  not not_47 (not_47_out, 1'b0);
  and and_45 (and_45_out, not_47_out, not_48_out);
  not not_48 (not_48_out, A16);
  and and_46 (and_46_out, 1'b0, not_46_out, and_44_out);
  not not_49 (not_49_out, B15);
  not not_50 (not_50_out, A15);
  not not_51 (not_51_out, A15);
  and and_47 (and_47_out, and_45_out, and_44_out);
  and and_48 (and_48_out, not_49_out, not_50_out);
  and and_49 (and_49_out, B15, not_51_out, and_47_out);
  not not_52 (not_52_out, B14);
  not not_53 (not_53_out, A14);
  not not_54 (not_54_out, A14);
  and and_50 (and_50_out, and_48_out, and_47_out);
  and and_51 (and_51_out, not_52_out, not_53_out);
  and and_52 (and_52_out, and_51_out, and_50_out);
  and and_53 (and_53_out, B14, not_54_out, and_50_out);
  not not_55 (not_55_out, B13);
  not not_56 (not_56_out, A13);
  not not_57 (not_57_out, A13);
  and and_54 (and_54_out, not_55_out, not_56_out);
  and and_55 (and_55_out, and_54_out, and_52_out);
  and and_56 (and_56_out, B13, not_57_out, and_52_out);
  not not_58 (not_58_out, B12);
  and and_57 (and_57_out, not_58_out, not_59_out);
  not not_59 (not_59_out, A12);
  not not_60 (not_60_out, A12);
  and and_58 (and_58_out, B12, not_60_out, and_55_out);
  and and_59 (and_59_out, and_57_out, and_55_out);
  not not_61 (not_61_out, B11);
  and and_60 (and_60_out, not_61_out, not_62_out);
  not not_62 (not_62_out, A11);
  not not_63 (not_63_out, A11);
  and and_61 (and_61_out, B11, not_63_out, and_59_out);
  and and_62 (and_62_out, and_60_out, and_59_out);
  not not_64 (not_64_out, B10);
  and and_63 (and_63_out, not_64_out, not_65_out);
  not not_65 (not_65_out, A10);
  and and_64 (and_64_out, B10, not_66_out, and_62_out);
  not not_66 (not_66_out, A10);
  not not_67 (not_67_out, A9);
  and and_65 (and_65_out, and_63_out, and_62_out);
  not not_68 (not_68_out, B9);
  and and_66 (and_66_out, not_68_out, not_69_out);
  not not_69 (not_69_out, A9);
  and and_67 (and_67_out, B9, not_67_out, and_65_out);
  not not_70 (not_70_out, A8);
  and and_68 (and_68_out, and_66_out, and_65_out);
  not not_71 (not_71_out, B8);
  and and_69 (and_69_out, not_71_out, not_72_out);
  not not_72 (not_72_out, A8);
  and and_70 (and_70_out, B8, not_70_out, and_68_out);
  not not_73 (not_73_out, B7);
  not not_74 (not_74_out, A7);
  not not_75 (not_75_out, A7);
  and and_71 (and_71_out, and_69_out, and_68_out);
  and and_72 (and_72_out, not_73_out, not_74_out);
  and and_73 (and_73_out, B7, not_75_out, and_71_out);
  not not_76 (not_76_out, B6);
  not not_77 (not_77_out, A6);
  not not_78 (not_78_out, A6);
  and and_74 (and_74_out, and_72_out, and_71_out);
  and and_75 (and_75_out, not_76_out, not_77_out);
  and and_76 (and_76_out, and_75_out, and_74_out);
  and and_77 (and_77_out, B6, not_78_out, and_74_out);
  not not_79 (not_79_out, B5);
  not not_80 (not_80_out, A5);
  not not_81 (not_81_out, A5);
  and and_78 (and_78_out, not_79_out, not_80_out);
  and and_79 (and_79_out, and_78_out, and_76_out);
  and and_80 (and_80_out, B5, not_81_out, and_76_out);
  not not_82 (not_82_out, B4);
  and and_81 (and_81_out, not_82_out, not_83_out);
  not not_83 (not_83_out, A4);
  not not_84 (not_84_out, A4);
  and and_82 (and_82_out, B4, not_84_out, and_79_out);
  and and_83 (and_83_out, and_81_out, and_79_out);
  not not_85 (not_85_out, B3);
  and and_84 (and_84_out, not_85_out, not_86_out);
  not not_86 (not_86_out, A3);
  and and_85 (and_85_out, B3, not_87_out, and_83_out);
  not not_87 (not_87_out, A3);
  and and_86 (and_86_out, and_84_out, and_83_out);
  not not_88 (not_88_out, B2);
  and and_87 (and_87_out, not_88_out, not_89_out);
  not not_89 (not_89_out, A2);
  and and_88 (and_88_out, B2, not_90_out, and_86_out);
  not not_90 (not_90_out, A2);
  not not_91 (not_91_out, A1);
  and and_89 (and_89_out, and_87_out, and_86_out);
  not not_92 (not_92_out, B1);
  and and_90 (and_90_out, not_92_out, not_93_out);
  not not_93 (not_93_out, A1);
  and and_91 (and_91_out, B1, not_91_out, and_89_out);
  not not_94 (not_94_out, A0);
  and and_92 (and_92_out, and_90_out, and_89_out);
  and and_93 (and_93_out, B0, not_94_out, and_92_out);

  assign _1 = _0;
  assign _2 = _0;
  assign _3 = _0;
  assign _4 = _0;
  assign _5 = _0;
  assign _6 = _0;
  assign _7 = _0;
  assign _8 = _0;
  assign _9 = _0;
  assign _10 = _0;
  assign _11 = _0;
  assign _12 = _0;
  assign _13 = _0;
  assign _14 = _0;
  assign _15 = _0;
  assign _16 = _0;
  assign _17 = _0;
  assign _18 = _0;
  assign _19 = _0;
  assign _20 = _0;
  assign _21 = _0;
  assign _22 = _0;
  assign _23 = _0;
  assign _24 = _0;
  assign _25 = _0;
  assign _26 = _0;
  assign _27 = _0;
  assign _28 = _0;
  assign _29 = _0;
  assign _30 = _0;
  assign _31 = _0;

  // Notes on the sheet:
  //   b
  //   a
  //   b
  //   a
  //   b
  //   a
  //   b
  //   a
  //   b
  //   a
  //   b
  //   a
  //   b
  //   a
  //   b
  //   a
  //   b
  //   a
  //   b
  //   a
  //   b
  //   a
  //   b
  //   a
  //   b
  //   a
  //   b
  //   a
  //   b
  //   a
  //   b
  //   a
  //   b
  //   a
  //   b
  //   a
  //   b
  //   a
  //   b
  //   a
  //   b
  //   a
  //   b
  //   a
  //   b
  //   a
  //   b
  //   a
  //   b
  //   a
  //   b
  //   a
  //   b
  //   a
  //   b
  //   a
  //   b
  //   a
  //   b
  //   a
endmodule
