// Logisim project MIPS.circ as structural Verilog: 5 circuits, main circuit Init Check
module Init_Check (
  input  A0,
  input  A1,
  input  A2,
  input  A3,
  input  A4,
  input  A5,
  input  A6,
  input  A7,
  input  A8,
  input  A9,
  input  A10,
  input  A11,
  input  A12,
  input  A13,
  input  A14,
  input  A15,
  input  A16,
  input  A17,
  input  A18,
  input  A19,
  input  A20,
  input  A21,
  input  A22,
  input  A23,
  input  A24,
  input  A25,
  input  A26,
  input  A27,
  input  A28,
  input  A29,
  input  A30,
  input  A31,
  output out_33
);

  wire and_1_out, and_2_out, and_3_out, and_4_out, and_5_out, and_6_out, and_7_out, and_8_out, and_9_out,
       and_10_out, and_11_out, and_12_out, and_13_out, and_14_out, and_15_out, and_16_out, and_17_out,
       and_18_out, and_19_out, and_20_out, and_21_out, and_22_out, and_23_out, and_24_out, and_25_out,
       and_26_out, and_27_out, and_28_out, and_29_out, and_30_out;

  and and_1 (and_1_out, A0, A1);
  and and_2 (and_2_out, A2, A3);
  and and_3 (and_3_out, A4, A5);
  and and_4 (and_4_out, A6, A7);
  and and_5 (and_5_out, A8, A9);
  and and_6 (and_6_out, A10, A11);
  and and_7 (and_7_out, A12, A13);
  and and_8 (and_8_out, A14, A15);
  and and_9 (and_9_out, A16, A17);
  and and_10 (and_10_out, A18, A19);
  and and_11 (and_11_out, A20, A21);
  and and_12 (and_12_out, A22, A23);
  and and_13 (and_13_out, A24, A25);
  and and_14 (and_14_out, A26, A27);
  and and_15 (and_15_out, A28, A29);
  and and_16 (and_16_out, A30, A31);
  and and_17 (and_17_out, and_1_out, and_2_out);
  and and_18 (and_18_out, and_3_out, and_4_out);
  and and_19 (and_19_out, and_5_out, and_6_out);
  and and_20 (and_20_out, and_7_out, and_8_out);
  and and_21 (and_21_out, and_9_out, and_10_out);
  and and_22 (and_22_out, and_11_out, and_12_out);
  and and_23 (and_23_out, and_13_out, and_14_out);
  and and_24 (and_24_out, and_15_out, and_16_out);
  and and_25 (and_25_out, and_17_out, and_18_out);
  and and_26 (and_26_out, and_25_out, and_27_out);
  and and_27 (and_27_out, and_19_out, and_20_out);
  and and_28 (and_28_out, and_21_out, and_22_out);
  and and_29 (and_29_out, and_28_out, and_30_out);
  and and_30 (and_30_out, and_23_out, and_24_out);
  and and_31 (out_33, and_26_out, and_29_out);
endmodule

module syscall_noop (
  input  A0,
  input  A1,
  input  A2,
  input  A3,
  input  A4,
  input  A5,
  input  A6,
  input  A7,
  input  A8,
  input  A9,
  input  A10,
  input  A11,
  input  A12,
  input  A13,
  input  A14,
  input  A15,
  input  A16,
  input  A17,
  input  A18,
  input  A19,
  input  A20,
  input  A21,
  input  A22,
  input  A23,
  input  A24,
  input  A25,
  input  A26,
  input  A27,
  input  A28,
  input  A29,
  input  A30,
  input  A31,
  output out_33
);

  wire and_1_out, and_2_out, and_3_out, and_4_out, and_5_out, and_6_out, and_7_out, and_8_out, and_9_out,
       and_10_out, and_11_out, and_12_out, and_13_out, and_14_out, and_15_out, and_16_out, and_17_out,
       and_18_out, and_19_out, and_20_out, and_21_out, and_22_out, and_23_out, and_24_out, and_25_out,
       and_26_out, and_27_out, and_28_out, and_29_out, and_30_out, not_1_out, not_2_out, not_3_out,
       not_4_out, not_5_out, not_6_out, not_7_out, not_8_out, not_9_out, not_10_out, not_11_out, not_12_out,
       not_13_out, not_14_out, not_15_out, not_16_out, not_17_out, not_18_out, not_19_out, not_20_out,
       not_21_out, not_22_out, not_23_out, not_24_out, not_25_out, not_26_out, not_27_out, not_28_out,
       not_29_out, not_30_out, not_31_out, not_32_out;

  not not_1 (not_1_out, A0);
  not not_2 (not_2_out, A1);
  not not_3 (not_3_out, A2);
  not not_4 (not_4_out, A3);
  not not_5 (not_5_out, A4);
  not not_6 (not_6_out, A5);
  not not_7 (not_7_out, A6);
  not not_8 (not_8_out, A7);
  not not_9 (not_9_out, A8);
  not not_10 (not_10_out, A9);
  not not_11 (not_11_out, A10);
  not not_12 (not_12_out, A11);
  not not_13 (not_13_out, A12);
  not not_14 (not_14_out, A13);
  not not_15 (not_15_out, A14);
  not not_16 (not_16_out, A15);
  not not_17 (not_17_out, A16);
  not not_18 (not_18_out, A17);
  not not_19 (not_19_out, A18);
  not not_20 (not_20_out, A19);
  not not_21 (not_21_out, A20);
  not not_22 (not_22_out, A21);
  not not_23 (not_23_out, A22);
  not not_24 (not_24_out, A23);
  not not_25 (not_25_out, A24);
  not not_26 (not_26_out, A25);
  not not_27 (not_27_out, A26);
  not not_28 (not_28_out, A27);
  not not_29 (not_29_out, A28);
  not not_30 (not_30_out, A29);
  not not_31 (not_31_out, A30);
  not not_32 (not_32_out, A31);
  and and_1 (and_1_out, not_1_out, not_2_out);
  and and_2 (and_2_out, not_3_out, not_4_out);
  and and_3 (and_3_out, and_2_out, and_4_out);
  and and_4 (and_4_out, not_5_out, not_6_out);
  and and_5 (and_5_out, not_7_out, not_8_out);
  and and_6 (and_6_out, and_5_out, and_7_out);
  and and_7 (and_7_out, not_9_out, not_10_out);
  and and_8 (and_8_out, not_11_out, not_12_out);
  and and_9 (and_9_out, and_8_out, and_10_out);
  and and_10 (and_10_out, not_13_out, not_14_out);
  and and_11 (and_11_out, not_15_out, not_16_out);
  and and_12 (and_12_out, and_11_out, and_13_out);
  and and_13 (and_13_out, not_17_out, not_18_out);
  and and_14 (and_14_out, not_19_out, not_20_out);
  and and_15 (and_15_out, and_14_out, and_16_out);
  and and_16 (and_16_out, not_21_out, not_22_out);
  and and_17 (and_17_out, not_23_out, not_24_out);
  and and_18 (and_18_out, and_17_out, and_19_out);
  and and_19 (and_19_out, not_25_out, not_26_out);
  and and_20 (and_20_out, not_27_out, not_28_out);
  and and_21 (and_21_out, and_20_out, and_22_out);
  and and_22 (and_22_out, not_29_out, not_30_out);
  and and_23 (and_23_out, not_31_out, not_32_out);
  and and_24 (and_24_out, and_1_out, and_3_out);
  and and_25 (and_25_out, and_9_out, and_12_out);
  and and_26 (and_26_out, and_15_out, and_18_out);
  and and_27 (and_27_out, and_21_out, and_23_out);
  and and_28 (and_28_out, and_6_out, and_25_out);
  and and_29 (and_29_out, and_28_out, and_30_out);
  and and_30 (and_30_out, and_26_out, and_27_out);
  or or_1 (out_33, and_24_out, and_29_out);
endmodule

module Program_Counter (
  input  On_reset,
  input  CLK,
  input  offset____2,
  input  target___2,
  input  s,
  input  [31:0] in_6,
  output [31:0] out_7
);

  wire add_1__0, add_1__1, add_1__2, add_1__3, add_1__4, add_1__5, add_1__6, add_1__7, add_1__8, add_1__9,
       add_1__10, add_1__11, add_1__12, add_1__13, add_1__14, add_1__15, add_1__16, add_1__17, add_1__18,
       add_1__19, add_1__20, add_1__21, add_1__22, add_1__23, add_1__24, add_1__25, add_1__26, add_1__27,
       add_1__28, add_1__29, add_1__30, add_1__31, and_1_out, and_2_out, and_3_out, and_4_out, and_5_out,
       and_6_out, and_7_out, and_8_out, and_9_out, and_10_out, and_11_out, and_12_out, and_13_out,
       and_14_out, and_15_out, and_16_out, and_17_out, and_18_out, and_19_out, and_20_out, and_21_out,
       and_22_out, and_23_out, and_24_out, and_25_out, and_26_out, and_27_out, and_28_out, and_29_out,
       and_30_out, and_31_out, and_32_out, and_33_out, and_34_out, and_35_out, and_36_out, and_37_out,
       and_38_out, and_39_out, and_40_out, and_41_out, and_42_out, and_43_out, and_44_out, and_45_out,
       and_46_out, and_47_out, and_48_out, and_49_out, and_50_out, and_51_out, and_52_out, and_53_out,
       and_54_out, and_55_out, and_56_out, and_57_out, and_58_out, and_59_out, and_60_out, and_61_out,
       and_62_out, and_63_out, and_64_out, and_65_out, and_66_out, and_67_out, and_68_out, and_69_out,
       and_70_out, and_71_out, and_72_out, and_73_out, and_74_out, and_75_out, and_76_out, and_77_out,
       and_78_out, and_79_out, and_80_out, and_81_out, and_82_out, and_83_out, and_84_out, and_85_out,
       and_86_out, and_87_out, and_88_out, and_89_out, and_90_out, and_91_out, and_92_out, and_93_out,
       and_94_out, and_95_out, and_96_out, and_97_out, and_98_out, and_99_out, and_100_out, and_101_out,
       and_102_out, and_103_out, and_104_out, and_105_out, and_106_out, and_107_out, and_108_out,
       and_109_out, and_110_out, and_111_out, and_112_out, and_113_out, and_114_out, and_115_out,
       and_116_out, and_117_out, and_118_out, and_119_out, and_120_out, and_121_out, and_122_out,
       and_123_out, and_124_out, and_125_out, and_126_out, and_127_out, and_128_out, and_129_out,
       and_130_out, and_131_out, and_132_out, and_133_out, and_134_out, and_135_out, and_136_out,
       and_137_out, and_138_out, and_139_out, and_140_out, and_141_out, and_142_out, and_143_out,
       and_144_out, and_145_out, and_146_out, and_147_out, and_148_out, and_149_out, and_150_out,
       and_151_out, and_152_out, and_153_out, and_154_out, and_155_out, and_156_out, and_157_out,
       and_158_out, and_159_out, and_160_out, and_161_out, and_162_out, and_163_out, and_164_out,
       and_165_out, and_166_out, and_167_out, and_168_out, and_169_out, and_170_out, and_171_out,
       and_172_out, and_173_out, and_174_out, and_175_out, and_176_out, and_177_out, and_178_out,
       and_179_out, and_180_out, and_181_out, and_182_out, and_183_out, and_184_out, and_185_out,
       and_186_out, and_187_out, and_188_out, and_189_out, and_190_out, and_191_out, and_192_out,
       and_193_out, and_194_out, and_195_out, and_196_out, and_197_out, and_198_out, and_199_out,
       and_200_out, and_201_out, and_202_out, and_203_out, and_204_out, and_205_out, and_206_out,
       and_207_out, and_208_out, and_209_out, and_210_out, and_211_out, and_212_out, and_213_out,
       and_214_out, and_215_out, and_216_out, and_217_out, and_218_out, and_219_out, and_220_out,
       and_221_out, and_222_out, and_223_out, and_224_out, and_225_out, and_226_out, and_227__0, and_227__1,
       and_227__2, and_227__3, and_227__4, and_227__5, and_227__6, and_227__7, and_227__8, and_227__9,
       and_227__10, and_227__11, and_227__12, and_227__13, and_227__14, and_227__15, and_227__16,
       and_227__17, and_227__18, and_227__19, and_227__20, and_227__21, and_227__22, and_227__23,
       and_227__24, and_227__25, and_227__26, and_227__27, and_227__28, and_227__29, and_227__30,
       and_227__31, n32_bit_general_register_2_d19_2, n32_bit_general_register_2_d20_2,
       n32_bit_general_register_2_d21_2, n32_bit_general_register_2_d22_2, n32_bit_general_register_2_d23_2,
       n32_bit_general_register_2_d24_2, n32_bit_general_register_2_d25_2, n32_bit_general_register_2_d26_2,
       n32_bit_general_register_2_d27_2, n32_bit_general_register_2_d28_2, n32_bit_general_register_2_d29_2,
       n32_bit_general_register_2_d30_2, n32_bit_general_register_2_d31_2, n32_bit_general_register_2_q0,
       n32_bit_general_register_2_q1, n32_bit_general_register_2_q2, n32_bit_general_register_2_q3,
       n32_bit_general_register_2_q4, n32_bit_general_register_2_q5, n32_bit_general_register_2_q6,
       n32_bit_general_register_2_q7, n32_bit_general_register_2_q8, n32_bit_general_register_2_q9,
       n32_bit_general_register_2_q10, n32_bit_general_register_2_q11, n32_bit_general_register_2_q12,
       n32_bit_general_register_2_q13, n32_bit_general_register_2_q14, n32_bit_general_register_2_q15,
       n32_bit_general_register_2_q16, n32_bit_general_register_2_q17, n32_bit_general_register_2_q18,
       not_1_out, not_2_out, not_3_out, not_4_out, not_5_out, or_1_out, or_2_out, or_3_out, or_4_out,
       or_5_out, or_6_out, or_7_out, or_8_out, or_9_out, or_10_out, or_11_out, or_12_out, or_13_out,
       or_14_out, or_15_out, or_16_out, or_17_out, or_18_out, or_19_out, or_20_out, or_21_out, or_22_out,
       or_23_out, or_24_out, or_25_out, or_26_out, or_27_out, or_28_out, or_29_out, or_30_out, or_31_out,
       or_32_out, or_33_out, or_34_out, or_35__0, or_35__1, or_35__2, or_35__3, or_35__4, or_35__5, or_35__6,
       or_35__7, or_35__8, or_35__9, or_35__10, or_35__11, or_35__12, or_35__13, or_35__14, or_35__15,
       or_35__16, or_35__17, or_35__18, or_35__19, or_35__20, or_35__21, or_35__22, or_35__23, or_35__24,
       or_35__25, or_35__26, or_35__27, or_35__28, or_35__29, or_35__30, or_35__31, or_36_out, or_37_out,
       or_38_out, or_39_out, or_40_out, or_41_out, or_42_out, or_43_out, or_44_out, or_45_out, or_46_out,
       or_47_out, or_48_out, or_49_out, or_50_out, or_51_out, or_52_out, or_53_out, or_54_out, or_55_out,
       or_56_out, or_57_out, or_58_out, or_59_out, or_60_out, or_61_out, or_62_out, or_63_out, or_64_out,
       or_65_out, or_66_out, or_67_out, or_68_out, sll_1__0, sll_1__1, sll_1__2, sll_1__3, sll_1__4,
       sll_1__5, sll_1__6, sll_1__7, sll_1__8, sll_1__9, sll_1__10, sll_1__11, sll_1__12, sll_1__13,
       sll_1__14, sll_1__15, sll_1__16, sll_1__17, sll_1__18, sll_1__19, sll_1__20, sll_1__21, sll_1__22,
       sll_1__23, sll_1__24, sll_1__25, sll_1__26, sll_1__27, sll_1__28, sll_1__29, sll_1__30, sll_1__31;

  not not_1 (not_1_out, On_reset);
  or or_1 (or_1_out, On_reset, CLK);
  _32_Bit_General_Register u_32_bit_general_register_1 (
    .E(or_1_out), .D0(and_1_out), .Q0(out_7[0]), .D1(and_2_out), .Q1(out_7[1]), .D2(and_3_out),
    .Q2(out_7[2]), .D3(and_4_out), .Q3(out_7[3]), .D4(and_5_out), .Q4(out_7[4]), .D5(and_6_out),
    .Q5(out_7[5]), .D6(and_7_out), .Q6(out_7[6]), .D7(and_8_out), .Q7(out_7[7]), .D8(and_9_out),
    .Q8(out_7[8]), .D9(and_10_out), .Q9(out_7[9]), .D10(and_11_out), .Q10(out_7[10]), .D11(and_12_out),
    .Q11(out_7[11]), .D12(and_13_out), .Q12(out_7[12]), .D13(and_14_out), .Q13(out_7[13]), .D14(and_15_out),
    .Q14(out_7[14]), .D15(and_16_out), .Q15(out_7[15]), .D16(and_17_out), .Q16(out_7[16]), .D17(and_18_out),
    .Q17(out_7[17]), .D18(and_19_out), .Q18(out_7[18]), .D19(and_20_out), .D19_2(out_7[19]),
    .D20(and_21_out), .D20_2(out_7[20]), .D21(and_22_out), .D21_2(out_7[21]), .D22(and_23_out),
    .D22_2(out_7[22]), .D23(and_24_out), .D23_2(out_7[23]), .D24(and_25_out), .D24_2(out_7[24]),
    .D25(and_26_out), .D25_2(out_7[25]), .D26(and_27_out), .D26_2(out_7[26]), .D27(and_28_out),
    .D27_2(out_7[27]), .D28(and_29_out), .D28_2(out_7[28]), .D29(and_30_out), .D29_2(out_7[29]),
    .D30(and_31_out), .D30_2(out_7[30]), .D31(and_32_out), .D31_2(out_7[31]));
  and and_1 (and_1_out, not_1_out, n32_bit_general_register_2_q0);
  and and_2 (and_2_out, not_1_out, n32_bit_general_register_2_q1);
  and and_3 (and_3_out, not_1_out, n32_bit_general_register_2_q2);
  and and_4 (and_4_out, not_1_out, n32_bit_general_register_2_q3);
  and and_5 (and_5_out, not_1_out, n32_bit_general_register_2_q4);
  and and_6 (and_6_out, not_1_out, n32_bit_general_register_2_q5);
  and and_7 (and_7_out, not_1_out, n32_bit_general_register_2_q6);
  and and_8 (and_8_out, not_1_out, n32_bit_general_register_2_q7);
  and and_9 (and_9_out, not_1_out, n32_bit_general_register_2_q8);
  and and_10 (and_10_out, not_1_out, n32_bit_general_register_2_q9);
  and and_11 (and_11_out, not_1_out, n32_bit_general_register_2_q10);
  and and_12 (and_12_out, not_1_out, n32_bit_general_register_2_q11);
  and and_13 (and_13_out, not_1_out, n32_bit_general_register_2_q12);
  and and_14 (and_14_out, not_1_out, n32_bit_general_register_2_q13);
  and and_15 (and_15_out, not_1_out, n32_bit_general_register_2_q14);
  and and_16 (and_16_out, not_1_out, n32_bit_general_register_2_q15);
  and and_17 (and_17_out, not_1_out, n32_bit_general_register_2_q16);
  and and_18 (and_18_out, not_1_out, n32_bit_general_register_2_q17);
  and and_19 (and_19_out, not_1_out, n32_bit_general_register_2_q18);
  and and_20 (and_20_out, not_1_out, n32_bit_general_register_2_d19_2);
  and and_21 (and_21_out, not_1_out, n32_bit_general_register_2_d20_2);
  and and_22 (and_22_out, not_1_out, n32_bit_general_register_2_d21_2);
  and and_23 (and_23_out, not_1_out, n32_bit_general_register_2_d22_2);
  and and_24 (and_24_out, not_1_out, n32_bit_general_register_2_d23_2);
  and and_25 (and_25_out, not_1_out, n32_bit_general_register_2_d24_2);
  and and_26 (and_26_out, not_1_out, n32_bit_general_register_2_d25_2);
  and and_27 (and_27_out, not_1_out, n32_bit_general_register_2_d26_2);
  and and_28 (and_28_out, not_1_out, n32_bit_general_register_2_d27_2);
  and and_29 (and_29_out, not_1_out, n32_bit_general_register_2_d28_2);
  and and_30 (and_30_out, not_1_out, n32_bit_general_register_2_d29_2);
  and and_31 (and_31_out, not_1_out, n32_bit_general_register_2_d30_2);
  and and_32 (and_32_out, not_1_out, n32_bit_general_register_2_d31_2);
  not not_2 (not_2_out, CLK);
  _32_Bit_General_Register u_32_bit_general_register_2 (
    .E(not_2_out), .D0(or_2_out), .Q0(n32_bit_general_register_2_q0), .D1(or_3_out),
    .Q1(n32_bit_general_register_2_q1), .D2(or_5_out), .Q2(n32_bit_general_register_2_q2), .D3(or_4_out),
    .Q3(n32_bit_general_register_2_q3), .D4(or_6_out), .Q4(n32_bit_general_register_2_q4), .D5(or_7_out),
    .Q5(n32_bit_general_register_2_q5), .D6(or_8_out), .Q6(n32_bit_general_register_2_q6), .D7(or_11_out),
    .Q7(n32_bit_general_register_2_q7), .D8(or_9_out), .Q8(n32_bit_general_register_2_q8), .D9(or_10_out),
    .Q9(n32_bit_general_register_2_q9), .D10(or_13_out), .Q10(n32_bit_general_register_2_q10),
    .D11(or_14_out), .Q11(n32_bit_general_register_2_q11), .D12(or_15_out),
    .Q12(n32_bit_general_register_2_q12), .D13(or_16_out), .Q13(n32_bit_general_register_2_q13),
    .D14(or_17_out), .Q14(n32_bit_general_register_2_q14), .D15(or_20_out),
    .Q15(n32_bit_general_register_2_q15), .D16(or_18_out), .Q16(n32_bit_general_register_2_q16),
    .D17(or_19_out), .Q17(n32_bit_general_register_2_q17), .D18(or_21_out),
    .Q18(n32_bit_general_register_2_q18), .D19(or_23_out), .D19_2(n32_bit_general_register_2_d19_2),
    .D20(or_22_out), .D20_2(n32_bit_general_register_2_d20_2), .D21(or_25_out),
    .D21_2(n32_bit_general_register_2_d21_2), .D22(or_24_out), .D22_2(n32_bit_general_register_2_d22_2),
    .D23(or_26_out), .D23_2(n32_bit_general_register_2_d23_2), .D24(or_28_out),
    .D24_2(n32_bit_general_register_2_d24_2), .D25(or_27_out), .D25_2(n32_bit_general_register_2_d25_2),
    .D26(or_30_out), .D26_2(n32_bit_general_register_2_d26_2), .D27(or_29_out),
    .D27_2(n32_bit_general_register_2_d27_2), .D28(or_31_out), .D28_2(n32_bit_general_register_2_d28_2),
    .D29(or_32_out), .D29_2(n32_bit_general_register_2_d29_2), .D30(or_33_out),
    .D30_2(n32_bit_general_register_2_d30_2), .D31(or_34_out), .D31_2(n32_bit_general_register_2_d31_2));
  or or_2 (or_2_out, and_33_out, or_37_out);
  or or_3 (or_3_out, and_34_out, or_38_out);
  and and_33 (and_33_out, s, in_6[0]);
  and and_34 (and_34_out, s, in_6[1]);
  and and_35 (and_35_out, s, in_6[2]);
  and and_36 (and_36_out, s, in_6[3]);
  and and_37 (and_37_out, s, in_6[4]);
  and and_38 (and_38_out, s, in_6[5]);
  and and_39 (and_39_out, s, in_6[6]);
  and and_40 (and_40_out, s, in_6[7]);
  and and_41 (and_41_out, s, in_6[8]);
  and and_42 (and_42_out, s, in_6[9]);
  and and_43 (and_43_out, s, in_6[10]);
  and and_44 (and_44_out, s, in_6[11]);
  and and_45 (and_45_out, s, in_6[12]);
  and and_46 (and_46_out, s, in_6[13]);
  and and_47 (and_47_out, s, in_6[14]);
  and and_48 (and_48_out, s, in_6[15]);
  and and_49 (and_49_out, s, in_6[16]);
  and and_50 (and_50_out, s, in_6[17]);
  and and_51 (and_51_out, s, in_6[18]);
  and and_52 (and_52_out, s, in_6[19]);
  and and_53 (and_53_out, s, in_6[20]);
  and and_54 (and_54_out, s, in_6[21]);
  and and_55 (and_55_out, s, in_6[22]);
  and and_56 (and_56_out, s, in_6[23]);
  and and_57 (and_57_out, s, in_6[24]);
  and and_58 (and_58_out, s, in_6[25]);
  and and_59 (and_59_out, s, in_6[26]);
  and and_60 (and_60_out, s, in_6[27]);
  and and_61 (and_61_out, s, in_6[28]);
  and and_62 (and_62_out, s, in_6[29]);
  and and_63 (and_63_out, s, in_6[30]);
  and and_64 (and_64_out, s, in_6[31]);
  and and_65 (and_65_out, offset____2, in_6[0]);
  and and_66 (and_66_out, offset____2, in_6[1]);
  and and_67 (and_67_out, offset____2, in_6[2]);
  and and_68 (and_68_out, offset____2, in_6[3]);
  and and_69 (and_69_out, offset____2, in_6[4]);
  and and_70 (and_70_out, offset____2, in_6[5]);
  and and_71 (and_71_out, offset____2, in_6[6]);
  and and_72 (and_72_out, offset____2, in_6[7]);
  and and_73 (and_73_out, offset____2, in_6[8]);
  and and_74 (and_74_out, offset____2, in_6[9]);
  and and_75 (and_75_out, offset____2, in_6[10]);
  and and_76 (and_76_out, offset____2, in_6[11]);
  and and_77 (and_77_out, offset____2, in_6[12]);
  and and_78 (and_78_out, offset____2, in_6[13]);
  and and_79 (and_79_out, offset____2, in_6[14]);
  and and_80 (and_80_out, offset____2, in_6[15]);
  and and_81 (and_81_out, offset____2, in_6[16]);
  and and_82 (and_82_out, offset____2, in_6[17]);
  and and_83 (and_83_out, offset____2, in_6[18]);
  and and_84 (and_84_out, offset____2, in_6[19]);
  and and_85 (and_85_out, offset____2, in_6[20]);
  and and_86 (and_86_out, offset____2, in_6[21]);
  and and_87 (and_87_out, offset____2, in_6[22]);
  and and_88 (and_88_out, offset____2, in_6[23]);
  and and_89 (and_89_out, offset____2, in_6[24]);
  and and_90 (and_90_out, offset____2, in_6[25]);
  and and_91 (and_91_out, offset____2, in_6[26]);
  and and_92 (and_92_out, offset____2, in_6[27]);
  and and_93 (and_93_out, offset____2, in_6[28]);
  and and_94 (and_94_out, offset____2, in_6[29]);
  and and_95 (and_95_out, offset____2, in_6[30]);
  and and_96 (and_96_out, offset____2, in_6[31]);
  and and_97 (and_97_out, target___2, in_6[0]);
  and and_98 (and_98_out, target___2, in_6[1]);
  and and_99 (and_99_out, target___2, in_6[2]);
  and and_100 (and_100_out, target___2, in_6[3]);
  and and_101 (and_101_out, target___2, in_6[4]);
  and and_102 (and_102_out, target___2, in_6[5]);
  and and_103 (and_103_out, target___2, in_6[6]);
  and and_104 (and_104_out, target___2, in_6[7]);
  and and_105 (and_105_out, target___2, in_6[8]);
  and and_106 (and_106_out, target___2, in_6[9]);
  and and_107 (and_107_out, target___2, in_6[10]);
  and and_108 (and_108_out, target___2, in_6[11]);
  and and_109 (and_109_out, target___2, in_6[12]);
  and and_110 (and_110_out, target___2, in_6[13]);
  and and_111 (and_111_out, target___2, in_6[14]);
  and and_112 (and_112_out, target___2, in_6[15]);
  and and_113 (and_113_out, target___2, in_6[16]);
  and and_114 (and_114_out, target___2, in_6[17]);
  and and_115 (and_115_out, target___2, in_6[18]);
  and and_116 (and_116_out, target___2, in_6[19]);
  and and_117 (and_117_out, target___2, in_6[20]);
  and and_118 (and_118_out, target___2, in_6[21]);
  and and_119 (and_119_out, target___2, in_6[22]);
  and and_120 (and_120_out, target___2, in_6[23]);
  and and_121 (and_121_out, target___2, in_6[24]);
  and and_122 (and_122_out, target___2, in_6[25]);
  and and_123 (and_123_out, target___2, in_6[26]);
  and and_124 (and_124_out, target___2, in_6[27]);
  and and_125 (and_125_out, target___2, in_6[28]);
  and and_126 (and_126_out, target___2, in_6[29]);
  and and_127 (and_127_out, target___2, in_6[30]);
  and and_128 (and_128_out, target___2, in_6[31]);
  or or_4 (or_4_out, and_36_out, or_40_out);
  or or_5 (or_5_out, and_35_out, or_39_out);
  or or_6 (or_6_out, and_37_out, or_41_out);
  or or_7 (or_7_out, and_38_out, or_42_out);
  or or_8 (or_8_out, and_39_out, or_43_out);
  not not_3 (not_3_out, offset____2);
  not not_4 (not_4_out, target___2);
  and and_129 (and_129_out, not_3_out, not_4_out);
  not not_5 (not_5_out, s);
  and and_130 (and_130_out, and_129_out, not_5_out);
  add add_1 (
    .A0(out_7[0]), .B0(and_65_out), .A1(out_7[1]), .B1(and_66_out), .A2(out_7[2]), .B2(or_12_out),
    .A3(out_7[3]), .B3(and_68_out), .A4(out_7[4]), .B4(and_69_out), .A5(out_7[5]), .B5(and_70_out),
    .A6(out_7[6]), .B6(and_71_out), .A7(out_7[7]), .B7(and_72_out), .A8(out_7[8]), .B8(and_73_out),
    .A9(out_7[9]), .B9(and_74_out), .A10(out_7[10]), .B10(and_75_out), .A11(out_7[11]), .B11(and_76_out),
    .A12(out_7[12]), .B12(and_77_out), .A13(out_7[13]), .B13(and_78_out), .A14(out_7[14]), .B14(and_79_out),
    .A15(out_7[15]), .B15(and_80_out), .A16(out_7[16]), .B16(and_81_out), .A17(out_7[17]), .B17(and_82_out),
    .A18(out_7[18]), .B18(and_83_out), .A19(out_7[19]), .B19(and_84_out), .A20(out_7[20]), .B20(and_85_out),
    .A21(out_7[21]), .B21(and_86_out), .A22(out_7[22]), .B22(and_87_out), .A23(out_7[23]), .B23(and_88_out),
    .A24(out_7[24]), .B24(and_89_out), .A25(out_7[25]), .B25(and_90_out), .A26(out_7[26]), .B26(and_91_out),
    .A27(out_7[27]), .B27(and_92_out), .A28(out_7[28]), .B28(and_93_out), .A29(out_7[29]), .B29(and_94_out),
    .A30(out_7[30]), .B30(and_95_out), .A31(out_7[31]), ._0(add_1__0), ._1(add_1__1), ._2(add_1__2),
    ._3(add_1__3), ._4(add_1__4), ._5(add_1__5), ._6(add_1__6), ._7(add_1__7), ._8(add_1__8), ._9(add_1__9),
    ._10(add_1__10), ._11(add_1__11), ._12(add_1__12), ._13(add_1__13), ._14(add_1__14), ._15(add_1__15),
    ._16(add_1__16), ._17(add_1__17), ._18(add_1__18), ._19(add_1__19), ._20(add_1__20), ._21(add_1__21),
    ._22(add_1__22), ._23(add_1__23), ._24(add_1__24), ._25(add_1__25), ._26(add_1__26), ._27(add_1__27),
    ._28(add_1__28), ._29(add_1__29), ._30(add_1__30), ._31(add_1__31), .B31(and_96_out));  // open: Carry, Overflow
  or or_9 (or_9_out, and_41_out, or_45_out);
  or or_10 (or_10_out, and_42_out, or_46_out);
  or or_11 (or_11_out, and_40_out, or_44_out);
  or or_12 (or_12_out, and_130_out, and_67_out);
  or or_13 (or_13_out, and_43_out, or_47_out);
  or or_14 (or_14_out, and_44_out, or_48_out);
  or or_15 (or_15_out, and_45_out, or_49_out);
  sll sll_1 (
    .B0(1'b0), .B1(target___2), .B2(1'b0), .B3(1'b0), .B4(1'b0), .A0(and_97_out), .A1(and_98_out),
    .A2(and_99_out), .A3(and_100_out), .A4(and_101_out), .A5(and_102_out), .A6(and_103_out),
    .A7(and_104_out), .A8(and_105_out), .A9(and_106_out), .A10(and_107_out), .A11(and_108_out),
    .A12(and_109_out), .A13(and_110_out), .A14(and_111_out), .A15(and_112_out), .A16(and_113_out),
    .A17(and_114_out), .A18(and_115_out), .A19(and_116_out), .A20(and_117_out), .A21(and_118_out),
    .A22(and_119_out), .A23(and_120_out), .A24(and_121_out), .A25(and_122_out), .A26(and_123_out),
    .A27(and_124_out), .A28(and_125_out), .A29(and_126_out), .A30(and_127_out), .A31(and_128_out),
    ._0(sll_1__0), ._1(sll_1__1), ._2(sll_1__2), ._3(sll_1__3), ._4(sll_1__4), ._5(sll_1__5), ._6(sll_1__6),
    ._7(sll_1__7), ._8(sll_1__8), ._9(sll_1__9), ._10(sll_1__10), ._11(sll_1__11), ._12(sll_1__12),
    ._13(sll_1__13), ._14(sll_1__14), ._15(sll_1__15), ._16(sll_1__16), ._17(sll_1__17), ._18(sll_1__18),
    ._19(sll_1__19), ._20(sll_1__20), ._21(sll_1__21), ._22(sll_1__22), ._23(sll_1__23), ._24(sll_1__24),
    ._25(sll_1__25), ._26(sll_1__26), ._27(sll_1__27), ._28(sll_1__28), ._29(sll_1__29), ._30(sll_1__30),
    ._31(sll_1__31));
  or or_16 (or_16_out, and_46_out, or_50_out);
  or or_17 (or_17_out, and_47_out, or_51_out);
  or or_18 (or_18_out, and_49_out, or_53_out);
  or or_19 (or_19_out, and_50_out, or_54_out);
  or or_20 (or_20_out, and_48_out, or_52_out);
  or or_21 (or_21_out, and_51_out, or_55_out);
  or or_22 (or_22_out, and_53_out, or_57_out);
  or or_23 (or_23_out, and_52_out, or_56_out);
  or or_24 (or_24_out, and_55_out, or_59_out);
  or or_25 (or_25_out, and_54_out, or_58_out);
  or or_26 (or_26_out, and_56_out, or_60_out);
  or or_27 (or_27_out, and_58_out, or_62_out);
  or or_28 (or_28_out, and_57_out, or_61_out);
  or or_29 (or_29_out, and_60_out, or_64_out);
  or or_30 (or_30_out, and_59_out, or_63_out);
  or or_31 (or_31_out, and_61_out, or_65_out);
  or or_32 (or_32_out, and_62_out, or_66_out);
  or or_33 (or_33_out, and_63_out, or_67_out);
  or or_34 (or_34_out, and_64_out, or_68_out);
  \or  or_35 (
    .A0(sll_1__0), .B0(and_227__0), .A1(sll_1__1), .B1(and_227__1), .A2(sll_1__2), .B2(and_227__2),
    .A3(sll_1__3), .B3(and_227__3), .A4(sll_1__4), .B4(and_227__4), .A5(sll_1__5), .B5(and_227__5),
    .A6(sll_1__6), .B6(and_227__6), .A7(sll_1__7), .B7(and_227__7), .A8(sll_1__8), .B8(and_227__8),
    .A9(sll_1__9), .B9(and_227__9), .A10(sll_1__10), .B10(and_227__10), .A11(sll_1__11), .B11(and_227__11),
    .A12(sll_1__12), .B12(and_227__12), .A13(sll_1__13), .B13(and_227__13), .A14(sll_1__14),
    .B14(and_227__14), .A15(sll_1__15), .B15(and_227__15), .A16(sll_1__16), .B16(and_227__16),
    .A17(sll_1__17), .B17(and_227__17), .A18(sll_1__18), .B18(and_227__18), .A19(sll_1__19),
    .B19(and_227__19), .A20(sll_1__20), .B20(and_227__20), .A21(sll_1__21), .B21(and_227__21),
    .A22(sll_1__22), .B22(and_227__22), .A23(sll_1__23), .B23(and_227__23), .A24(sll_1__24),
    .B24(and_227__24), .A25(sll_1__25), .B25(and_227__25), .A26(sll_1__26), .B26(and_227__26),
    .A27(sll_1__27), .B27(and_227__27), .A28(sll_1__28), .B28(and_227__28), .A29(sll_1__29),
    .B29(and_227__29), .A30(sll_1__30), .B30(and_227__30), .A31(sll_1__31), .B31(and_227__31), ._0(or_35__0),
    ._1(or_35__1), ._2(or_35__2), ._3(or_35__3), ._4(or_35__4), ._5(or_35__5), ._6(or_35__6), ._7(or_35__7),
    ._8(or_35__8), ._9(or_35__9), ._10(or_35__10), ._11(or_35__11), ._12(or_35__12), ._13(or_35__13),
    ._14(or_35__14), ._15(or_35__15), ._16(or_35__16), ._17(or_35__17), ._18(or_35__18), ._19(or_35__19),
    ._20(or_35__20), ._21(or_35__21), ._22(or_35__22), ._23(or_35__23), ._24(or_35__24), ._25(or_35__25),
    ._26(or_35__26), ._27(or_35__27), ._28(or_35__28), ._29(or_35__29), ._30(or_35__30), ._31(or_35__31));
  or or_36 (or_36_out, offset____2, and_130_out);
  and and_131 (and_131_out, or_36_out, add_1__0);
  and and_132 (and_132_out, or_36_out, add_1__1);
  and and_133 (and_133_out, or_36_out, add_1__2);
  and and_134 (and_134_out, or_36_out, add_1__3);
  and and_135 (and_135_out, or_36_out, add_1__4);
  and and_136 (and_136_out, or_36_out, add_1__5);
  and and_137 (and_137_out, or_36_out, add_1__6);
  and and_138 (and_138_out, or_36_out, add_1__7);
  and and_139 (and_139_out, or_36_out, add_1__8);
  and and_140 (and_140_out, or_36_out, add_1__9);
  and and_141 (and_141_out, or_36_out, add_1__10);
  and and_142 (and_142_out, or_36_out, add_1__11);
  and and_143 (and_143_out, or_36_out, add_1__12);
  and and_144 (and_144_out, or_36_out, add_1__13);
  and and_145 (and_145_out, or_36_out, add_1__14);
  and and_146 (and_146_out, or_36_out, add_1__15);
  and and_147 (and_147_out, or_36_out, add_1__16);
  and and_148 (and_148_out, or_36_out, add_1__17);
  and and_149 (and_149_out, or_36_out, add_1__18);
  and and_150 (and_150_out, or_36_out, add_1__19);
  and and_151 (and_151_out, or_36_out, add_1__20);
  and and_152 (and_152_out, or_36_out, add_1__21);
  and and_153 (and_153_out, or_36_out, add_1__22);
  and and_154 (and_154_out, or_36_out, add_1__23);
  and and_155 (and_155_out, or_36_out, add_1__24);
  and and_156 (and_156_out, or_36_out, add_1__25);
  and and_157 (and_157_out, or_36_out, add_1__26);
  and and_158 (and_158_out, or_36_out, add_1__27);
  and and_159 (and_159_out, or_36_out, add_1__28);
  and and_160 (and_160_out, or_36_out, add_1__29);
  and and_161 (and_161_out, or_36_out, add_1__30);
  and and_162 (and_162_out, or_36_out, add_1__31);
  and and_163 (and_163_out, target___2, add_1__0);
  and and_164 (and_164_out, target___2, add_1__1);
  and and_165 (and_165_out, target___2, add_1__2);
  and and_166 (and_166_out, target___2, add_1__3);
  and and_167 (and_167_out, target___2, add_1__4);
  and and_168 (and_168_out, target___2, add_1__5);
  and and_169 (and_169_out, target___2, add_1__6);
  and and_170 (and_170_out, target___2, add_1__7);
  and and_171 (and_171_out, target___2, add_1__8);
  and and_172 (and_172_out, target___2, add_1__9);
  and and_173 (and_173_out, target___2, add_1__10);
  and and_174 (and_174_out, target___2, add_1__11);
  and and_175 (and_175_out, target___2, add_1__12);
  and and_176 (and_176_out, target___2, add_1__13);
  and and_177 (and_177_out, target___2, add_1__14);
  and and_178 (and_178_out, target___2, add_1__15);
  and and_179 (and_179_out, target___2, add_1__16);
  and and_180 (and_180_out, target___2, add_1__17);
  and and_181 (and_181_out, target___2, add_1__18);
  and and_182 (and_182_out, target___2, add_1__19);
  and and_183 (and_183_out, target___2, add_1__20);
  and and_184 (and_184_out, target___2, add_1__21);
  and and_185 (and_185_out, target___2, add_1__22);
  and and_186 (and_186_out, target___2, add_1__23);
  and and_187 (and_187_out, target___2, add_1__24);
  and and_188 (and_188_out, target___2, add_1__25);
  and and_189 (and_189_out, target___2, add_1__26);
  and and_190 (and_190_out, target___2, add_1__27);
  and and_191 (and_191_out, target___2, add_1__28);
  and and_192 (and_192_out, target___2, add_1__29);
  and and_193 (and_193_out, target___2, add_1__30);
  and and_194 (and_194_out, target___2, add_1__31);
  or or_37 (or_37_out, and_195_out, and_131_out);
  or or_38 (or_38_out, and_196_out, and_132_out);
  or or_39 (or_39_out, and_197_out, and_133_out);
  or or_40 (or_40_out, and_198_out, and_134_out);
  or or_41 (or_41_out, and_199_out, and_135_out);
  or or_42 (or_42_out, and_200_out, and_136_out);
  or or_43 (or_43_out, and_201_out, and_137_out);
  or or_44 (or_44_out, and_202_out, and_138_out);
  or or_45 (or_45_out, and_203_out, and_139_out);
  or or_46 (or_46_out, and_204_out, and_140_out);
  or or_47 (or_47_out, and_205_out, and_141_out);
  or or_48 (or_48_out, and_206_out, and_142_out);
  or or_49 (or_49_out, and_207_out, and_143_out);
  or or_50 (or_50_out, and_208_out, and_144_out);
  or or_51 (or_51_out, and_209_out, and_145_out);
  or or_52 (or_52_out, and_210_out, and_146_out);
  or or_53 (or_53_out, and_211_out, and_147_out);
  or or_54 (or_54_out, and_212_out, and_148_out);
  or or_55 (or_55_out, and_213_out, and_149_out);
  or or_56 (or_56_out, and_214_out, and_150_out);
  or or_57 (or_57_out, and_215_out, and_151_out);
  or or_58 (or_58_out, and_216_out, and_152_out);
  or or_59 (or_59_out, and_217_out, and_153_out);
  or or_60 (or_60_out, and_218_out, and_154_out);
  or or_61 (or_61_out, and_219_out, and_155_out);
  or or_62 (or_62_out, and_220_out, and_156_out);
  or or_63 (or_63_out, and_221_out, and_157_out);
  or or_64 (or_64_out, and_222_out, and_158_out);
  or or_65 (or_65_out, and_223_out, and_159_out);
  or or_66 (or_66_out, and_224_out, and_160_out);
  or or_67 (or_67_out, and_225_out, and_161_out);
  or or_68 (or_68_out, and_226_out, and_162_out);
  and and_195 (and_195_out, target___2, or_35__0);
  and and_196 (and_196_out, target___2, or_35__1);
  and and_197 (and_197_out, target___2, or_35__2);
  and and_198 (and_198_out, target___2, or_35__3);
  and and_199 (and_199_out, target___2, or_35__4);
  and and_200 (and_200_out, target___2, or_35__5);
  and and_201 (and_201_out, target___2, or_35__6);
  and and_202 (and_202_out, target___2, or_35__7);
  and and_203 (and_203_out, target___2, or_35__8);
  and and_204 (and_204_out, target___2, or_35__9);
  and and_205 (and_205_out, target___2, or_35__10);
  and and_206 (and_206_out, target___2, or_35__11);
  and and_207 (and_207_out, target___2, or_35__12);
  and and_208 (and_208_out, target___2, or_35__13);
  and and_209 (and_209_out, target___2, or_35__14);
  and and_210 (and_210_out, target___2, or_35__15);
  and and_211 (and_211_out, target___2, or_35__16);
  and and_212 (and_212_out, target___2, or_35__17);
  and and_213 (and_213_out, target___2, or_35__18);
  and and_214 (and_214_out, target___2, or_35__19);
  and and_215 (and_215_out, target___2, or_35__20);
  and and_216 (and_216_out, target___2, or_35__21);
  and and_217 (and_217_out, target___2, or_35__22);
  and and_218 (and_218_out, target___2, or_35__23);
  and and_219 (and_219_out, target___2, or_35__24);
  and and_220 (and_220_out, target___2, or_35__25);
  and and_221 (and_221_out, target___2, or_35__26);
  and and_222 (and_222_out, target___2, or_35__27);
  and and_223 (and_223_out, target___2, or_35__28);
  and and_224 (and_224_out, target___2, or_35__29);
  and and_225 (and_225_out, target___2, or_35__30);
  and and_226 (and_226_out, target___2, or_35__31);
  \and  and_227 (
    .A0(and_163_out), .B0(1'b0), .A1(and_164_out), .B1(1'b0), .A2(and_165_out), .B2(1'b0), .A3(and_166_out),
    .B3(1'b0), .A4(and_167_out), .B4(1'b0), .A5(and_168_out), .B5(1'b0), .A6(and_169_out), .B6(1'b0),
    .A7(and_170_out), .B7(1'b0), .A8(and_171_out), .B8(1'b0), .A9(and_172_out), .B9(1'b0), .A10(and_173_out),
    .B10(1'b0), .A11(and_174_out), .B11(1'b0), .A12(and_175_out), .B12(1'b0), .A13(and_176_out), .B13(1'b0),
    .A14(and_177_out), .B14(1'b0), .A15(and_178_out), .B15(1'b0), .A16(and_179_out), .B16(1'b0),
    .A17(and_180_out), .B17(1'b0), .A18(and_181_out), .B18(1'b0), .A19(and_182_out), .B19(1'b0),
    .A20(and_183_out), .B20(1'b0), .A21(and_184_out), .B21(1'b0), .A22(and_185_out), .B22(1'b0),
    .A23(and_186_out), .B23(1'b0), .A24(and_187_out), .B24(1'b0), .A25(and_188_out), .B25(1'b0),
    .A26(and_189_out), .B26(1'b0), .A27(and_190_out), .B27(1'b0), .A28(and_191_out), .B28(1'b1),
    .A29(and_192_out), .B29(1'b1), .A30(and_193_out), .B30(1'b1), .A31(and_194_out), .B31(1'b1),
    ._0(and_227__0), ._1(and_227__1), ._2(and_227__2), ._3(and_227__3), ._4(and_227__4), ._5(and_227__5),
    ._6(and_227__6), ._7(and_227__7), ._8(and_227__8), ._9(and_227__9), ._10(and_227__10), ._11(and_227__11),
    ._12(and_227__12), ._13(and_227__13), ._14(and_227__14), ._15(and_227__15), ._16(and_227__16),
    ._17(and_227__17), ._18(and_227__18), ._19(and_227__19), ._20(and_227__20), ._21(and_227__21),
    ._22(and_227__22), ._23(and_227__23), ._24(and_227__24), ._25(and_227__25), ._26(and_227__26),
    ._27(and_227__27), ._28(and_227__28), ._29(and_227__29), ._30(and_227__30), ._31(and_227__31));

  // Notes on the sheet:
  //   $s
  //   offset
  //   target
  //   PC
  //   nPC
  //   ADV_PC(4)
  //   target
endmodule

module Main (
  input  in_1,
  input  Load
);

  wire and_7_out, and_9_out, and_16_out, clock_1_out, not_1_out, not_2_out, not_3_out, not_5_out,
       operations_conditional_6_bit_register_1_out_8, operations_conditional_6_bit_register_1_out_9,
       operations_conditional_6_bit_register_1_out_10, operations_conditional_6_bit_register_1_out_11,
       operations_conditional_6_bit_register_1_out_12, operations_conditional_6_bit_register_1_out_13,
       operations_conditional_6_bit_register_1_out_14, operations_conditional_6_bit_register_1_out_15,
       operations_conditional_6_bit_register_1_out_16, operations_conditional_6_bit_register_1_out_17,
       operations_conditional_6_bit_register_1_out_18, operations_conditional_6_bit_register_1_out_19,
       operations_conditional_6_bit_register_1_out_20, operations_conditional_6_bit_register_1_out_21,
       operations_conditional_6_bit_register_1_out_22, operations_conditional_6_bit_register_1_out_23,
       operations_conditional_6_bit_register_1_out_24, operations_conditional_6_bit_register_1_out_25,
       operations_conditional_6_bit_register_1_out_26, operations_conditional_6_bit_register_1_out_27,
       operations_conditional_6_bit_register_1_out_28, operations_conditional_6_bit_register_1_out_29,
       operations_conditional_6_bit_register_1_out_30, operations_conditional_6_bit_register_1_out_31,
       operations_conditional_6_bit_register_1_out_33, operations_conditional_6_bit_register_1_out_34,
       operations_conditional_6_bit_register_1_out_35, operations_conditional_6_bit_register_1_out_36,
       operations_conditional_6_bit_register_1_out_37, operations_conditional_6_bit_register_1_out_38,
       operations_conditional_6_bit_register_1_out_39, operations_conditional_6_bit_register_1_out_40,
       operations_conditional_6_bit_register_1_out_41, operations_conditional_6_bit_register_1_out_42,
       operations_conditional_6_bit_register_1_out_43, operations_conditional_6_bit_register_1_out_44,
       operations_conditional_6_bit_register_1_out_45, operations_conditional_6_bit_register_1_out_46,
       operations_conditional_6_bit_register_1_out_48, operations_conditional_6_bit_register_1_out_49,
       operations_conditional_6_bit_register_1_out_50, operations_conditional_6_bit_register_1_out_51,
       operations_conditional_6_bit_register_1_out_52, operations_conditional_6_bit_register_1_out_53,
       or_4_out, or_6_out, or_10_out, or_12_out, or_13_out, or_14_out, or_15_out, or_16_out, or_17_out,
       or_18_out, or_19_out, or_21_out, or_22_out, or_23_out, or_24_out, or_25_out, or_26_out, or_28_out,
       or_29_out, or_30_out, or_33_out, or_34_out, or_35_out, or_36_out, or_37_out, or_39_out, or_41_out,
       or_42_out, or_43_out, or_44_out, or_45_out, or_46_out, or_48_out, or_51_out, or_52_out, or_53_out,
       or_54_out, or_55_out, or_56_out, or_57_out, or_59_out, or_60_out, or_61_out, or_62_out, or_63_out,
       or_64_out, rom_1_addr_err__reset;
  wire [4:0] blu_1_p4, d_2_out, d_3_out, d_out, or_5_out, or_7_out, or_8_out, s_out, t_out;
  wire [4:4] nor_1_out, nor_2_out, nor_3_out, or_9_out, or_11_out, or_20_out, or_27_out, or_38_out,
       or_47_out, or_50_out;
  wire [15:0] and_12_out;
  wire [15:15] operations_conditional_6_bit_register_1_out_32;
  wire [25:0] and_11_out;
  wire [31:0] add_1__0, alu_1_out_14, alu_1_out_15, alu_1_out_16, and_1_out, and_2_out, and_3_out, and_4_out,
       and_5_out, and_8_out, and_10_out, and_13_out, and_14_out, and_15_out, and_17_out, and_18_out,
       n32_bit_general_register_1_out_3, n32_bit_general_register_2_out_3, n32_bit_general_register_3_out_3,
       n32_bit_general_register_4_out_3, n32_bit_general_register_5_out_3, n32_bit_general_register_6_out_3,
       n32_bit_general_register_7_out_3, n32_bit_general_register_8_out_3, not_4_out, not_6_out, or_1_out,
       or_2_out, or_3_out, or_31_out, or_32_out, or_40_out, or_65_out, or_66_out, or_67_out,
       program_counter_1_out_7, register_arrayregister_array_1_out_7, register_arrayregister_array_1_out_8,
       rom_1_out_7, undriven;
  wire [31:11] and_11_out_2;
  wire [31:31] and_6_out, operations_conditional_6_bit_register_1_out_47,
       operations_conditional_6_bit_register_1_out_54, operations_conditional_6_bit_register_1_out_55,
       operations_conditional_6_bit_register_1_out_56, operations_conditional_6_bit_register_1_out_57,
       or_49_out, or_58_out;

  assign and_1_out = {32{or_50_out[4]}} & program_counter_1_out_7;  // AND_Gate and_1, 32 bits wide
  add add_1 (
    .A0(and_1_out[0]), .B0(1'b0), .A1(and_1_out[1]), .B1(1'b0), .A2(and_1_out[2]), .B2(1'b0),
    .A3(and_1_out[3]), .B3(1'b1), .A4(and_1_out[4]), .B4(1'b0), .A5(and_1_out[5]), .B5(1'b0),
    .A6(and_1_out[6]), .B6(1'b0), .A7(and_1_out[7]), .B7(1'b0), .A8(and_1_out[8]), .B8(1'b0),
    .A9(and_1_out[9]), .B9(1'b0), .A10(and_1_out[10]), .B10(1'b0), .A11(and_1_out[11]), .B11(1'b0),
    .A12(and_1_out[12]), .B12(1'b0), .A13(and_1_out[13]), .B13(1'b0), .A14(and_1_out[14]), .B14(1'b0),
    .A15(and_1_out[15]), .B15(1'b0), .A16(and_1_out[16]), .B16(1'b0), .A17(and_1_out[17]), .B17(1'b0),
    .A18(and_1_out[18]), .B18(1'b0), .A19(and_1_out[19]), .B19(1'b0), .A20(and_1_out[20]), .B20(1'b0),
    .A21(and_1_out[21]), .B21(1'b0), .A22(and_1_out[22]), .B22(1'b0), .A23(and_1_out[23]), .B23(1'b0),
    .A24(and_1_out[24]), .B24(1'b0), .A25(and_1_out[25]), .B25(1'b0), .A26(and_1_out[26]), .B26(1'b0),
    .A27(and_1_out[27]), .B27(1'b0), .A28(and_1_out[28]), .B28(1'b0), .A29(and_1_out[29]), .B29(1'b0),
    .A30(and_1_out[30]), .B30(1'b0), .A31(and_1_out[31]), ._0(add_1__0[0]), ._1(add_1__0[1]),
    ._2(add_1__0[2]), ._3(add_1__0[3]), ._4(add_1__0[4]), ._5(add_1__0[5]), ._6(add_1__0[6]),
    ._7(add_1__0[7]), ._8(add_1__0[8]), ._9(add_1__0[9]), ._10(add_1__0[10]), ._11(add_1__0[11]),
    ._12(add_1__0[12]), ._13(add_1__0[13]), ._14(add_1__0[14]), ._15(add_1__0[15]), ._16(add_1__0[16]),
    ._17(add_1__0[17]), ._18(add_1__0[18]), ._19(add_1__0[19]), ._20(add_1__0[20]), ._21(add_1__0[21]),
    ._22(add_1__0[22]), ._23(add_1__0[23]), ._24(add_1__0[24]), ._25(add_1__0[25]), ._26(add_1__0[26]),
    ._27(add_1__0[27]), ._28(add_1__0[28]), ._29(add_1__0[29]), ._30(add_1__0[30]), ._31(add_1__0[31]),
    .B31(1'b0));  // open: Carry, Overflow
  assign and_2_out = n32_bit_general_register_1_out_3 & {32{operations_conditional_6_bit_register_1_out_47[31]}};  // AND_Gate and_2, 32 bits wide
  assign and_3_out = n32_bit_general_register_2_out_3 & {32{or_58_out[31]}};  // AND_Gate and_3, 32 bits wide
  assign and_4_out = n32_bit_general_register_3_out_3 & {32{or_49_out[31]}};  // AND_Gate and_4, 32 bits wide
  _32_Bit_General_Register u_32_bit_general_register_1 (
    .in_2(n32_bit_general_register_5_out_3), .out_3(n32_bit_general_register_1_out_3), .CLK(clock_1_out));
  _32_Bit_General_Register u_32_bit_general_register_2 (
    .in_2({{6{1'b0}}, and_11_out}), .out_3(n32_bit_general_register_2_out_3), .CLK(clock_1_out));
  _32_Bit_General_Register u_32_bit_general_register_3 (
    .in_2({{16{1'b0}}, and_11_out[15:0]}), .out_3(n32_bit_general_register_3_out_3), .CLK(clock_1_out));
  _32_Bit_General_Register u_32_bit_general_register_4 (
    .in_2(or_2_out), .out_3(n32_bit_general_register_4_out_3), .CLK(not_1_out));
  assign or_1_out = and_2_out | and_3_out;  // OR_Gate or_1, 32 bits wide
  assign or_2_out = or_1_out | and_4_out;  // OR_Gate or_2, 32 bits wide
  not not_1 (not_1_out, clock_1_out);
  assign and_5_out = add_1__0 & {32{or_50_out[4]}};  // AND_Gate and_5, 32 bits wide
  and and_6 (and_6_out[31], not_3_out, not_2_out);
  not not_2 (not_2_out, or_4_out);
  not not_3 (not_3_out, Load);
  Program_Counter program_counter_1 (
    .On_reset(and_9_out), .offset____2(or_49_out[31]), .target___2(or_58_out[31]),
    .s(operations_conditional_6_bit_register_1_out_47[31]), .out_7(program_counter_1_out_7),
    .in_6(n32_bit_general_register_4_out_3), .CLK(and_7_out));
  and and_7 (and_7_out, clock_1_out, and_6_out[31]);
  assign or_3_out = and_8_out | and_5_out;  // OR_Gate or_3, 32 bits wide
  assign and_8_out = or_32_out & not_4_out;  // AND_Gate and_8, 32 bits wide
  assign not_4_out = ~{32{or_50_out[4]}};  // NOT_Gate not_4, 32 bits wide
  and and_9 (and_9_out, clock_1_out, or_4_out);
  or or_4 (or_4_out, rom_1_addr_err__reset, in_1);
  Clock clock_1 (.out(clock_1_out));
  Register_ArrayRegister_Array register_arrayregister_array_1 (
    .in_6(or_3_out), .out_7(register_arrayregister_array_1_out_7),
    .out_8(register_arrayregister_array_1_out_8), .in_2(in_1), .s(s_out), .t(t_out), .d(or_5_out),
    .init(not_5_out));
  not not_5 (not_5_out, clock_1_out);
  assign not_6_out = ~{32{Load}};  // NOT_Gate not_6, 32 bits wide
  ROM rom_1 (
    .Start_clear(and_9_out), .in_3(Load), .CLK(clock_1_out), .Store(1'b0), .in_4({32{1'b0}}),
    .in_5(and_10_out), .Addr_Err__RESET(rom_1_addr_err__reset), .out_7(rom_1_out_7));
  assign and_10_out = program_counter_1_out_7 & not_6_out;  // AND_Gate and_10, 32 bits wide
  assign or_5_out = {5{or_50_out[4]}} | or_8_out;  // OR_Gate or_5, 5 bits wide
  _32_Bit_General_Register u_32_bit_general_register_5 (
    .in_2(register_arrayregister_array_1_out_7), .out_3(n32_bit_general_register_5_out_3), .CLK(clock_1_out));
  _32_Bit_General_Register u_32_bit_general_register_6 (
    .in_2(register_arrayregister_array_1_out_8), .out_3(n32_bit_general_register_6_out_3), .CLK(clock_1_out));
  assign {and_11_out_2, and_11_out[10:0]} = rom_1_out_7 & {32{and_6_out[31]}};  // AND_Gate and_11, 32 bits wide
  or or_6 (or_6_out, clock_1_out, in_1);
  assign or_7_out = d_out | d_2_out;  // OR_Gate or_7, 5 bits wide
  assign or_8_out = or_7_out | d_3_out;  // OR_Gate or_8, 5 bits wide
  Operations_Conditional_6_Bit_Register operations_conditional_6_bit_register_1 (
    ._2_0(and_11_out_2[26]), ._2_1(and_11_out_2[27]), ._2_2(and_11_out_2[28]), ._2_3(and_11_out_2[29]),
    ._2_4(and_11_out_2[30]), ._2_5(and_11_out_2[31]), .out_8(operations_conditional_6_bit_register_1_out_8),
    .out_9(operations_conditional_6_bit_register_1_out_9),
    .out_10(operations_conditional_6_bit_register_1_out_10),
    .out_11(operations_conditional_6_bit_register_1_out_11),
    .out_12(operations_conditional_6_bit_register_1_out_12),
    .out_13(operations_conditional_6_bit_register_1_out_13),
    .out_14(operations_conditional_6_bit_register_1_out_14),
    .out_15(operations_conditional_6_bit_register_1_out_15),
    .out_16(operations_conditional_6_bit_register_1_out_16),
    .out_17(operations_conditional_6_bit_register_1_out_17),
    .out_18(operations_conditional_6_bit_register_1_out_18),
    .out_19(operations_conditional_6_bit_register_1_out_19),
    .out_20(operations_conditional_6_bit_register_1_out_20),
    .out_21(operations_conditional_6_bit_register_1_out_21),
    .out_22(operations_conditional_6_bit_register_1_out_22),
    .out_23(operations_conditional_6_bit_register_1_out_23),
    .out_24(operations_conditional_6_bit_register_1_out_24),
    .out_25(operations_conditional_6_bit_register_1_out_25),
    .out_26(operations_conditional_6_bit_register_1_out_26),
    .out_27(operations_conditional_6_bit_register_1_out_27),
    .out_28(operations_conditional_6_bit_register_1_out_28),
    .out_29(operations_conditional_6_bit_register_1_out_29),
    .out_30(operations_conditional_6_bit_register_1_out_30),
    .out_31(operations_conditional_6_bit_register_1_out_31),
    .out_32(operations_conditional_6_bit_register_1_out_32[15]),
    .out_33(operations_conditional_6_bit_register_1_out_33),
    .out_34(operations_conditional_6_bit_register_1_out_34),
    .out_35(operations_conditional_6_bit_register_1_out_35),
    .out_36(operations_conditional_6_bit_register_1_out_36),
    .out_37(operations_conditional_6_bit_register_1_out_37),
    .out_38(operations_conditional_6_bit_register_1_out_38),
    .out_39(operations_conditional_6_bit_register_1_out_39),
    .out_40(operations_conditional_6_bit_register_1_out_40),
    .out_41(operations_conditional_6_bit_register_1_out_41),
    .out_42(operations_conditional_6_bit_register_1_out_42),
    .out_43(operations_conditional_6_bit_register_1_out_43),
    .out_44(operations_conditional_6_bit_register_1_out_44),
    .out_45(operations_conditional_6_bit_register_1_out_45),
    .out_46(operations_conditional_6_bit_register_1_out_46),
    .out_47(operations_conditional_6_bit_register_1_out_47[31]),
    .out_48(operations_conditional_6_bit_register_1_out_48),
    .out_49(operations_conditional_6_bit_register_1_out_49),
    .out_50(operations_conditional_6_bit_register_1_out_50),
    .out_51(operations_conditional_6_bit_register_1_out_51),
    .out_52(operations_conditional_6_bit_register_1_out_52),
    .out_53(operations_conditional_6_bit_register_1_out_53),
    .out_54(operations_conditional_6_bit_register_1_out_54[31]),
    .out_55(operations_conditional_6_bit_register_1_out_55[31]),
    .out_56(operations_conditional_6_bit_register_1_out_56[31]),
    .out_57(operations_conditional_6_bit_register_1_out_57[31]), .E(or_6_out));
  // BLU blu_1: pin names not known; wires that end beside it: n32_bit_general_register_5_out_3, n32_bit_general_register_6_out_3, and_11_out[15:0], blu_1_p4, operations_conditional_6_bit_register_1_out_18, operations_conditional_6_bit_register_1_out_19, operations_conditional_6_bit_register_1_out_20, operations_conditional_6_bit_register_1_out_21, operations_conditional_6_bit_register_1_out_22, operations_conditional_6_bit_register_1_out_23, operations_conditional_6_bit_register_1_out_24, operations_conditional_6_bit_register_1_out_25, operations_conditional_6_bit_register_1_out_26, operations_conditional_6_bit_register_1_out_27, operations_conditional_6_bit_register_1_out_28
  or or_9 (or_9_out[4], operations_conditional_6_bit_register_1_out_45, operations_conditional_6_bit_register_1_out_46);
  or or_10 (or_10_out, operations_conditional_6_bit_register_1_out_32[15], operations_conditional_6_bit_register_1_out_54[31]);
  or or_11 (or_11_out[4], or_10_out, operations_conditional_6_bit_register_1_out_55[31]);
  assign and_11_out[25:21] = and_11_out_2[25:21] & {5{or_9_out[4]}};  // AND_Gate C, 5 bits wide
  assign d_out = and_11_out_2[25:21] & {5{or_11_out[4]}};  // AND_Gate d, 5 bits wide
  or or_12 (or_12_out, operations_conditional_6_bit_register_1_out_9, operations_conditional_6_bit_register_1_out_11);
  or or_13 (or_13_out, operations_conditional_6_bit_register_1_out_50, operations_conditional_6_bit_register_1_out_49);
  or or_14 (or_14_out, or_12_out, or_13_out);
  or or_15 (or_15_out, or_14_out, or_19_out);
  nor nor_1 (nor_1_out[4], or_9_out[4], or_11_out[4]);
  assign s_out = and_11_out_2[25:21] & {5{nor_1_out[4]}};  // AND_Gate s, 5 bits wide
  or or_16 (or_16_out, operations_conditional_6_bit_register_1_out_48, operations_conditional_6_bit_register_1_out_19);
  or or_17 (or_17_out, operations_conditional_6_bit_register_1_out_25, operations_conditional_6_bit_register_1_out_27);
  or or_18 (or_18_out, operations_conditional_6_bit_register_1_out_21, operations_conditional_6_bit_register_1_out_23);
  or or_19 (or_19_out, or_16_out, or_18_out);
  or or_20 (or_20_out[4], or_15_out, or_26_out);
  assign d_2_out = and_11_out_2[20:16] & {5{or_20_out[4]}};  // AND_Gate d_2, 5 bits wide
  or or_21 (or_21_out, operations_conditional_6_bit_register_1_out_36, operations_conditional_6_bit_register_1_out_30);
  or or_22 (or_22_out, operations_conditional_6_bit_register_1_out_31, 1'b0);
  or or_23 (or_23_out, operations_conditional_6_bit_register_1_out_29, operations_conditional_6_bit_register_1_out_34);
  or or_24 (or_24_out, or_21_out, or_22_out);
  or or_25 (or_25_out, or_17_out, or_23_out);
  or or_26 (or_26_out, or_25_out, or_24_out);
  or or_27 (or_27_out[4], operations_conditional_6_bit_register_1_out_46, operations_conditional_6_bit_register_1_out_45);
  assign and_11_out[20:16] = and_11_out_2[20:16] & {5{or_27_out[4]}};  // AND_Gate C_2, 5 bits wide
  or or_28 (or_28_out, operations_conditional_6_bit_register_1_out_8, operations_conditional_6_bit_register_1_out_10);
  or or_29 (or_29_out, or_28_out, or_35_out);
  nor nor_2 (nor_2_out[4], or_20_out[4], or_27_out[4]);
  assign t_out = and_11_out_2[20:16] & {5{nor_2_out[4]}};  // AND_Gate t, 5 bits wide
  or or_30 (or_30_out, operations_conditional_6_bit_register_1_out_38, operations_conditional_6_bit_register_1_out_39);
  assign or_31_out = or_40_out | or_67_out;  // OR_Gate or_31, 32 bits wide
  assign or_32_out = or_31_out | and_13_out;  // OR_Gate or_32, 32 bits wide
  or or_33 (or_33_out, operations_conditional_6_bit_register_1_out_18, operations_conditional_6_bit_register_1_out_20);
  or or_34 (or_34_out, operations_conditional_6_bit_register_1_out_22, operations_conditional_6_bit_register_1_out_24);
  or or_35 (or_35_out, operations_conditional_6_bit_register_1_out_16, operations_conditional_6_bit_register_1_out_17);
  or or_36 (or_36_out, or_33_out, or_34_out);
  or or_37 (or_37_out, or_29_out, or_36_out);
  or or_38 (or_38_out[4], or_37_out, or_45_out);
  assign d_3_out = and_11_out_2[15:11] & {5{or_38_out[4]}};  // AND_Gate d_3, 5 bits wide
  assign and_11_out[15:11] = and_11_out_2[15:11] & {5{nor_3_out[4]}};  // AND_Gate C_3, 5 bits wide
  or or_39 (or_39_out, operations_conditional_6_bit_register_1_out_42, operations_conditional_6_bit_register_1_out_43);
  assign or_40_out = undriven | alu_1_out_14;  // OR_Gate or_40, 32 bits wide
  or or_41 (or_41_out, operations_conditional_6_bit_register_1_out_26, operations_conditional_6_bit_register_1_out_28);
  or or_42 (or_42_out, operations_conditional_6_bit_register_1_out_33, operations_conditional_6_bit_register_1_out_35);
  or or_43 (or_43_out, 1'b0, 1'b0);
  or or_44 (or_44_out, or_41_out, or_42_out);
  or or_45 (or_45_out, or_44_out, or_48_out);
  nor nor_3 (nor_3_out[4], or_38_out[4], or_47_out[4]);
  assign blu_1_p4 = and_11_out_2[15:11] & {5{or_47_out[4]}};  // AND_Gate H, 5 bits wide
  ALU alu_1 (
    .in_11(n32_bit_general_register_5_out_3), .in_12(n32_bit_general_register_6_out_3),
    .in_13(and_11_out[15:0]), .out_14(alu_1_out_14), .out_15(alu_1_out_15), .out_16(alu_1_out_16),
    .in_1(operations_conditional_6_bit_register_1_out_8),
    .in_2(operations_conditional_6_bit_register_1_out_9),
    .in_3(operations_conditional_6_bit_register_1_out_10),
    .in_4(operations_conditional_6_bit_register_1_out_11),
    .in_5(operations_conditional_6_bit_register_1_out_16),
    .in_6(operations_conditional_6_bit_register_1_out_17),
    .in_7(operations_conditional_6_bit_register_1_out_14),
    .in_8(operations_conditional_6_bit_register_1_out_15),
    .in_9(operations_conditional_6_bit_register_1_out_12),
    .in_10(operations_conditional_6_bit_register_1_out_13));  // open: out_17, out_18
  or or_46 (or_46_out, operations_conditional_6_bit_register_1_out_30, operations_conditional_6_bit_register_1_out_31);
  or or_47 (or_47_out[4], or_46_out, 1'b0);
  or or_48 (or_48_out, or_43_out, 1'b0);
  or or_49 (or_49_out[31], or_51_out, or_52_out);
  or or_50 (or_50_out[4], operations_conditional_6_bit_register_1_out_46, or_53_out);
  or or_51 (or_51_out, or_54_out, or_55_out);
  or or_52 (or_52_out, or_56_out, or_57_out);
  or or_53 (or_53_out, operations_conditional_6_bit_register_1_out_42, operations_conditional_6_bit_register_1_out_39);
  or or_54 (or_54_out, operations_conditional_6_bit_register_1_out_44, operations_conditional_6_bit_register_1_out_43);
  or or_55 (or_55_out, operations_conditional_6_bit_register_1_out_42, operations_conditional_6_bit_register_1_out_41);
  or or_56 (or_56_out, operations_conditional_6_bit_register_1_out_40, operations_conditional_6_bit_register_1_out_39);
  or or_57 (or_57_out, operations_conditional_6_bit_register_1_out_38, operations_conditional_6_bit_register_1_out_37);
  or or_58 (or_58_out[31], operations_conditional_6_bit_register_1_out_46, operations_conditional_6_bit_register_1_out_45);
  or or_59 (or_59_out, operations_conditional_6_bit_register_1_out_14, operations_conditional_6_bit_register_1_out_15);
  or or_60 (or_60_out, or_59_out, or_61_out);
  or or_61 (or_61_out, operations_conditional_6_bit_register_1_out_12, operations_conditional_6_bit_register_1_out_13);
  assign and_12_out = {16{operations_conditional_6_bit_register_1_out_32[15]}} & and_11_out[15:0];  // AND_Gate and_12, 16 bits wide
  assign and_13_out = {and_12_out, {16{1'b0}}} & {32{operations_conditional_6_bit_register_1_out_32[15]}};  // AND_Gate and_13, 32 bits wide
  assign and_14_out = n32_bit_general_register_5_out_3 & {32{operations_conditional_6_bit_register_1_out_56[31]}};  // AND_Gate and_14, 32 bits wide
  assign and_15_out = n32_bit_general_register_5_out_3 & {32{operations_conditional_6_bit_register_1_out_57[31]}};  // AND_Gate and_15, 32 bits wide
  or or_62 (or_62_out, operations_conditional_6_bit_register_1_out_56[31], operations_conditional_6_bit_register_1_out_57[31]);
  or or_63 (or_63_out, or_60_out, or_62_out);
  and and_16 (and_16_out, clock_1_out, or_63_out);
  or or_64 (or_64_out, and_16_out, or_6_out);
  _32_Bit_General_Register u_32_bit_general_register_7 (
    .in_2(or_65_out), .out_3(n32_bit_general_register_7_out_3), .CLK(or_64_out));
  assign or_65_out = alu_1_out_15 | and_14_out;  // OR_Gate or_65, 32 bits wide
  _32_Bit_General_Register u_32_bit_general_register_8 (
    .in_2(or_66_out), .out_3(n32_bit_general_register_8_out_3), .CLK(or_64_out));
  assign or_66_out = alu_1_out_16 | and_15_out;  // OR_Gate or_66, 32 bits wide
  assign and_17_out = n32_bit_general_register_7_out_3 & {32{operations_conditional_6_bit_register_1_out_54[31]}};  // AND_Gate and_17, 32 bits wide
  assign and_18_out = n32_bit_general_register_8_out_3 & {32{operations_conditional_6_bit_register_1_out_55[31]}};  // AND_Gate and_18, 32 bits wide
  assign or_67_out = and_17_out | and_18_out;  // OR_Gate or_67, 32 bits wide

  // Notes on the sheet:
  //   $s
  //   target
  //   offset
  //   Jump Instructions
  //   $s
  //   target
  //   offset
  //   on/reset
  //   CLK
  //   Data Bus (To Registers)
  //   $d
  //   $s
  //   24-20
  //   $t
  //   H
  //   19-15
  //   sra
  //   14-10
  //   sllv,srlv,srav
  //   Branch Instruction
  //   sra
  //   10-0
  //   C
  //   Register 31 Link
  //   LUI
  //   Move To/From Hi/Lo
endmodule

module ROM (
  input  Start_clear,
  input  CLK,
  input  in_3,
  input  [31:0] in_4,
  input  [31:0] in_5,
  input  Store,
  output [31:0] out_7,
  output Addr_Err__RESET
);

  wire add_1__0, add_1__1, add_1__2, add_1__3, add_1__4, add_1__5, add_1__6, add_1__7, add_1__8, add_1__9,
       add_1__10, add_1__11, add_1__12, add_1__13, add_1__14, add_1__15, add_1__16, add_1__17, add_1__18,
       add_1__19, add_1__20, add_1__21, add_1__22, add_1__23, add_1__24, add_1__25, add_1__26, add_1__27,
       add_1__28, add_1__29, add_1__30, add_1__31, and_1_out, and_2_out, and_3_out, and_4_out, and_5_out,
       and_6_out, and_7_out, and_8_out, and_9_out, and_10_out, and_11_out, and_12_out, and_13_out,
       and_14_out, and_15_out, and_16_out, and_17_out, and_18_out, and_19_out, and_20_out, and_21_out,
       and_22_out, and_23_out, and_24_out, and_25_out, and_26_out, and_27_out, and_28_out, and_29_out,
       and_30_out, and_31_out, and_32_out, and_33_out, and_34_out, and_38_out,
       n32_bit_general_register_1_d19_2, n32_bit_general_register_1_d20_2, n32_bit_general_register_1_d21_2,
       n32_bit_general_register_1_d22_2, n32_bit_general_register_1_d23_2, n32_bit_general_register_1_d24_2,
       n32_bit_general_register_1_d25_2, n32_bit_general_register_1_d26_2, n32_bit_general_register_1_d27_2,
       n32_bit_general_register_1_d28_2, n32_bit_general_register_1_d29_2, n32_bit_general_register_1_d30_2,
       n32_bit_general_register_1_d31_2, n32_bit_general_register_1_q0, n32_bit_general_register_1_q1,
       n32_bit_general_register_1_q2, n32_bit_general_register_1_q3, n32_bit_general_register_1_q4,
       n32_bit_general_register_1_q5, n32_bit_general_register_1_q6, n32_bit_general_register_1_q7,
       n32_bit_general_register_1_q8, n32_bit_general_register_1_q9, n32_bit_general_register_1_q10,
       n32_bit_general_register_1_q11, n32_bit_general_register_1_q12, n32_bit_general_register_1_q13,
       n32_bit_general_register_1_q14, n32_bit_general_register_1_q15, n32_bit_general_register_1_q16,
       n32_bit_general_register_1_q17, n32_bit_general_register_1_q18, n32_bit_general_register_2_d24_2,
       n32_bit_general_register_2_d25_2, n32_bit_general_register_2_d26_2, n32_bit_general_register_2_d27_2,
       n32_bit_general_register_2_d28_2, n32_bit_general_register_2_d29_2, n32_bit_general_register_2_d30_2,
       n32_bit_general_register_2_d31_2, not_1_out, not_2_out, not_3_out, not_4_out, or_1_out, or_2_out,
       or_3_out, or_4_out, or_5_out, or_6_out, or_8_out, or_9_out, or_12_out;
  wire [23:0] and_36_out, and_39_out, n32_bit_general_register_2_q0, not_5_out, or_10_out;
  wire [23:23] and_35_out;
  wire [31:0] and_37_out, or_11_out, rom_1_data;

  or or_1 (or_1_out, in_5[29], in_5[28]);
  or or_2 (or_2_out, in_5[31], in_5[30]);
  or or_3 (or_3_out, or_2_out, or_1_out);
  or or_4 (or_4_out, in_5[27], in_5[26]);
  or or_5 (or_5_out, in_5[25], in_5[24]);
  or or_6 (or_6_out, or_4_out, or_5_out);
  or or_7 (Addr_Err__RESET, or_3_out, or_6_out);
  not not_1 (not_1_out, Start_clear);
  or or_8 (or_8_out, Start_clear, not_3_out);
  _32_Bit_General_Register u_32_bit_general_register_1 (
    .E(or_8_out), .D0(add_1__0), .Q0(n32_bit_general_register_1_q0), .D1(add_1__1),
    .Q1(n32_bit_general_register_1_q1), .D2(add_1__2), .Q2(n32_bit_general_register_1_q2), .D3(add_1__3),
    .Q3(n32_bit_general_register_1_q3), .D4(add_1__4), .Q4(n32_bit_general_register_1_q4), .D5(add_1__5),
    .Q5(n32_bit_general_register_1_q5), .D6(add_1__6), .Q6(n32_bit_general_register_1_q6), .D7(add_1__7),
    .Q7(n32_bit_general_register_1_q7), .D8(add_1__8), .Q8(n32_bit_general_register_1_q8), .D9(add_1__9),
    .Q9(n32_bit_general_register_1_q9), .D10(add_1__10), .Q10(n32_bit_general_register_1_q10),
    .D11(add_1__11), .Q11(n32_bit_general_register_1_q11), .D12(add_1__12),
    .Q12(n32_bit_general_register_1_q12), .D13(add_1__13), .Q13(n32_bit_general_register_1_q13),
    .D14(add_1__14), .Q14(n32_bit_general_register_1_q14), .D15(add_1__15),
    .Q15(n32_bit_general_register_1_q15), .D16(add_1__16), .Q16(n32_bit_general_register_1_q16),
    .D17(add_1__17), .Q17(n32_bit_general_register_1_q17), .D18(add_1__18),
    .Q18(n32_bit_general_register_1_q18), .D19(add_1__19), .D19_2(n32_bit_general_register_1_d19_2),
    .D20(add_1__20), .D20_2(n32_bit_general_register_1_d20_2), .D21(add_1__21),
    .D21_2(n32_bit_general_register_1_d21_2), .D22(add_1__22), .D22_2(n32_bit_general_register_1_d22_2),
    .D23(add_1__23), .D23_2(n32_bit_general_register_1_d23_2), .D24(add_1__24),
    .D24_2(n32_bit_general_register_1_d24_2), .D25(add_1__25), .D25_2(n32_bit_general_register_1_d25_2),
    .D26(add_1__26), .D26_2(n32_bit_general_register_1_d26_2), .D27(add_1__27),
    .D27_2(n32_bit_general_register_1_d27_2), .D28(add_1__28), .D28_2(n32_bit_general_register_1_d28_2),
    .D29(add_1__29), .D29_2(n32_bit_general_register_1_d29_2), .D30(add_1__30),
    .D30_2(n32_bit_general_register_1_d30_2), .D31(add_1__31), .D31_2(n32_bit_general_register_1_d31_2));
  not not_2 (not_2_out, add_1__24);
  and and_1 (and_1_out, not_2_out, and_34_out);
  not not_3 (not_3_out, and_1_out);
  or or_9 (or_9_out, Start_clear, and_1_out);
  _32_Bit_General_Register u_32_bit_general_register_2 (
    .E(or_9_out), .D0(and_2_out), .Q0(n32_bit_general_register_2_q0[0]), .D1(and_3_out),
    .Q1(n32_bit_general_register_2_q0[1]), .D2(and_4_out), .Q2(n32_bit_general_register_2_q0[2]),
    .D3(and_5_out), .Q3(n32_bit_general_register_2_q0[3]), .D4(and_6_out),
    .Q4(n32_bit_general_register_2_q0[4]), .D5(and_7_out), .Q5(n32_bit_general_register_2_q0[5]),
    .D6(and_8_out), .Q6(n32_bit_general_register_2_q0[6]), .D7(and_9_out),
    .Q7(n32_bit_general_register_2_q0[7]), .D8(and_10_out), .Q8(n32_bit_general_register_2_q0[8]),
    .D9(and_11_out), .Q9(n32_bit_general_register_2_q0[9]), .D10(and_12_out),
    .Q10(n32_bit_general_register_2_q0[10]), .D11(and_13_out), .Q11(n32_bit_general_register_2_q0[11]),
    .D12(and_14_out), .Q12(n32_bit_general_register_2_q0[12]), .D13(and_15_out),
    .Q13(n32_bit_general_register_2_q0[13]), .D14(and_16_out), .Q14(n32_bit_general_register_2_q0[14]),
    .D15(and_17_out), .Q15(n32_bit_general_register_2_q0[15]), .D16(and_18_out),
    .Q16(n32_bit_general_register_2_q0[16]), .D17(and_19_out), .Q17(n32_bit_general_register_2_q0[17]),
    .D18(and_20_out), .Q18(n32_bit_general_register_2_q0[18]), .D19(and_21_out),
    .D19_2(n32_bit_general_register_2_q0[19]), .D20(and_22_out), .D20_2(n32_bit_general_register_2_q0[20]),
    .D21(and_23_out), .D21_2(n32_bit_general_register_2_q0[21]), .D22(and_24_out),
    .D22_2(n32_bit_general_register_2_q0[22]), .D23(and_25_out), .D23_2(n32_bit_general_register_2_q0[23]),
    .D24(and_26_out), .D24_2(n32_bit_general_register_2_d24_2), .D25(and_27_out),
    .D25_2(n32_bit_general_register_2_d25_2), .D26(and_28_out), .D26_2(n32_bit_general_register_2_d26_2),
    .D27(and_29_out), .D27_2(n32_bit_general_register_2_d27_2), .D28(and_30_out),
    .D28_2(n32_bit_general_register_2_d28_2), .D29(and_31_out), .D29_2(n32_bit_general_register_2_d29_2),
    .D30(and_32_out), .D30_2(n32_bit_general_register_2_d30_2), .D31(and_33_out),
    .D31_2(n32_bit_general_register_2_d31_2));
  and and_2 (and_2_out, n32_bit_general_register_1_q0, not_1_out);
  and and_3 (and_3_out, n32_bit_general_register_1_q1, not_1_out);
  and and_4 (and_4_out, n32_bit_general_register_1_q2, not_1_out);
  and and_5 (and_5_out, n32_bit_general_register_1_q3, not_1_out);
  and and_6 (and_6_out, n32_bit_general_register_1_q4, not_1_out);
  and and_7 (and_7_out, n32_bit_general_register_1_q5, not_1_out);
  and and_8 (and_8_out, n32_bit_general_register_1_q6, not_1_out);
  and and_9 (and_9_out, n32_bit_general_register_1_q7, not_1_out);
  and and_10 (and_10_out, n32_bit_general_register_1_q8, not_1_out);
  and and_11 (and_11_out, n32_bit_general_register_1_q9, not_1_out);
  and and_12 (and_12_out, n32_bit_general_register_1_q10, not_1_out);
  and and_13 (and_13_out, n32_bit_general_register_1_q11, not_1_out);
  and and_14 (and_14_out, n32_bit_general_register_1_q12, not_1_out);
  and and_15 (and_15_out, n32_bit_general_register_1_q13, not_1_out);
  and and_16 (and_16_out, n32_bit_general_register_1_q14, not_1_out);
  and and_17 (and_17_out, n32_bit_general_register_1_q15, not_1_out);
  and and_18 (and_18_out, n32_bit_general_register_1_q16, not_1_out);
  and and_19 (and_19_out, n32_bit_general_register_1_q17, not_1_out);
  and and_20 (and_20_out, n32_bit_general_register_1_q18, not_1_out);
  and and_21 (and_21_out, n32_bit_general_register_1_d19_2, not_1_out);
  and and_22 (and_22_out, n32_bit_general_register_1_d20_2, not_1_out);
  and and_23 (and_23_out, n32_bit_general_register_1_d21_2, not_1_out);
  and and_24 (and_24_out, n32_bit_general_register_1_d22_2, not_1_out);
  and and_25 (and_25_out, n32_bit_general_register_1_d23_2, not_1_out);
  and and_26 (and_26_out, n32_bit_general_register_1_d24_2, not_1_out);
  and and_27 (and_27_out, n32_bit_general_register_1_d25_2, not_1_out);
  and and_28 (and_28_out, n32_bit_general_register_1_d26_2, not_1_out);
  and and_29 (and_29_out, n32_bit_general_register_1_d27_2, not_1_out);
  and and_30 (and_30_out, n32_bit_general_register_1_d28_2, not_1_out);
  and and_31 (and_31_out, n32_bit_general_register_1_d29_2, not_1_out);
  and and_32 (and_32_out, n32_bit_general_register_1_d30_2, not_1_out);
  and and_33 (and_33_out, n32_bit_general_register_1_d31_2, not_1_out);
  and and_34 (and_34_out, CLK, in_3);
  and and_35 (and_35_out[23], in_3, not_2_out);
  add add_1 (
    .A0(n32_bit_general_register_2_q0[0]), .B0(not_4_out), .A1(n32_bit_general_register_2_q0[1]), .B1(1'b0),
    .A2(n32_bit_general_register_2_q0[2]), .B2(1'b0), .A3(n32_bit_general_register_2_q0[3]), .B3(1'b0),
    .A4(n32_bit_general_register_2_q0[4]), .B4(1'b0), .A5(n32_bit_general_register_2_q0[5]), .B5(1'b0),
    .A6(n32_bit_general_register_2_q0[6]), .B6(1'b0), .A7(n32_bit_general_register_2_q0[7]), .B7(1'b0),
    .A8(n32_bit_general_register_2_q0[8]), .B8(1'b0), .A9(n32_bit_general_register_2_q0[9]), .B9(1'b0),
    .A10(n32_bit_general_register_2_q0[10]), .B10(1'b0), .A11(n32_bit_general_register_2_q0[11]), .B11(1'b0),
    .A12(n32_bit_general_register_2_q0[12]), .B12(1'b0), .A13(n32_bit_general_register_2_q0[13]), .B13(1'b0),
    .A14(n32_bit_general_register_2_q0[14]), .B14(1'b0), .A15(n32_bit_general_register_2_q0[15]), .B15(1'b0),
    .A16(n32_bit_general_register_2_q0[16]), .B16(1'b0), .A17(n32_bit_general_register_2_q0[17]), .B17(1'b0),
    .A18(n32_bit_general_register_2_q0[18]), .B18(1'b0), .A19(n32_bit_general_register_2_q0[19]), .B19(1'b0),
    .A20(n32_bit_general_register_2_q0[20]), .B20(1'b0), .A21(n32_bit_general_register_2_q0[21]), .B21(1'b0),
    .A22(n32_bit_general_register_2_q0[22]), .B22(1'b0), .A23(n32_bit_general_register_2_q0[23]), .B23(1'b0),
    .A24(n32_bit_general_register_2_d24_2), .B24(1'b0), .A25(n32_bit_general_register_2_d25_2), .B25(1'b0),
    .A26(n32_bit_general_register_2_d26_2), .B26(1'b0), .A27(n32_bit_general_register_2_d27_2), .B27(1'b0),
    .A28(n32_bit_general_register_2_d28_2), .B28(1'b0), .A29(n32_bit_general_register_2_d29_2), .B29(1'b0),
    .A30(n32_bit_general_register_2_d30_2), .B30(1'b0), .A31(n32_bit_general_register_2_d31_2),
    ._0(add_1__0), ._1(add_1__1), ._2(add_1__2), ._3(add_1__3), ._4(add_1__4), ._5(add_1__5), ._6(add_1__6),
    ._7(add_1__7), ._8(add_1__8), ._9(add_1__9), ._10(add_1__10), ._11(add_1__11), ._12(add_1__12),
    ._13(add_1__13), ._14(add_1__14), ._15(add_1__15), ._16(add_1__16), ._17(add_1__17), ._18(add_1__18),
    ._19(add_1__19), ._20(add_1__20), ._21(add_1__21), ._22(add_1__22), ._23(add_1__23), ._24(add_1__24),
    ._25(add_1__25), ._26(add_1__26), ._27(add_1__27), ._28(add_1__28), ._29(add_1__29), ._30(add_1__30),
    ._31(add_1__31), .B31(1'b0));  // open: Carry, Overflow
  not not_4 (not_4_out, 1'b0);
  assign and_36_out = {24{and_35_out[23]}} & n32_bit_general_register_2_q0;  // AND_Gate and_36, 24 bits wide
  ROM_part #(.addrWidth(24), .dataWidth(32)) rom_1 (
    .addr(n32_bit_general_register_2_q0), .data(rom_1_data));  // open: sel
  assign and_37_out = {32{and_35_out[23]}} & rom_1_data;  // AND_Gate and_37, 32 bits wide
  assign not_5_out = ~and_36_out;  // NOT_Gate not_5, 24 bits wide
  and and_38 (and_38_out, in_3, and_35_out[23]);
  assign and_39_out = in_5[23:0] & not_5_out;  // AND_Gate and_39, 24 bits wide
  assign or_10_out = and_36_out | and_39_out;  // OR_Gate or_10, 24 bits wide
  assign or_11_out = and_37_out | in_4;  // OR_Gate or_11, 32 bits wide
  or or_12 (or_12_out, and_38_out, Store);
  RAM #(.addrWidth(24), .dataWidth(32), .bus("separate")) ram_1 (
    .addr(or_10_out), .din(or_11_out), .data(out_7), .str(or_12_out), .clk(CLK), .ld(1'b1), .clr(Start_clear));  // open: sel

  // Notes on the sheet:
  //   Data In
  //   Addr
  //   Load  ROM into RAM
  //   Load Your
  //   Own Program
  //   Here!
  //   contents of rom_1 (hex, n*v repeats v):
  //   4*0 8010064 0 0 0 8020064 0 0 0 4221800 0 0 0 a0000000
  //   Data Out
endmodule
